// Logisim project Questao_1102.circ as structural Verilog: 1 circuit, main circuit main
module main (
  input  X,
  output Y
);

  wire and_1_out, and_2_out, and_3_out, clock_1_out, d_ff_1_q, d_ff_2_q, d_ff_3_q, not_1_out, not_2_out;

  Clock clock_1 (.out(clock_1_out));
  and and_1 (and_1_out, d_ff_1_q, d_ff_2_q);
  not not_1 (not_1_out, X);
  and and_2 (and_2_out, not_2_out, d_ff_2_q, clock_1_out, d_ff_3_q);
  and and_3 (and_3_out, not_1_out, d_ff_1_q);
  D_Flip_Flop d_ff_1 (.clk(clock_1_out), .D(and_1_out), .Q(d_ff_1_q), .preset(d_ff_1_q));  // open: Qn, reset
  // AND_Gate and_4 has open pins: in0=d_ff_1_q, in1=X, in2=d_ff_2_q, in3=d_ff_3_q, out=open
  D_Flip_Flop d_ff_2 (.clk(d_ff_1_q), .D(and_2_out), .Q(d_ff_2_q));  // open: Qn, preset, reset
  D_Flip_Flop d_ff_3 (.clk(clock_1_out), .D(and_3_out), .Q(d_ff_3_q));  // open: Qn, preset, reset
  not not_2 (not_2_out, d_ff_1_q);
  and and_5 (Y, d_ff_1_q, d_ff_2_q);
endmodule
