// Logisim project Questao_1104.circ as structural Verilog: 1 circuit, main circuit main
module main (
  input  X,
  output Y
);

  wire and_1_out, and_2_out, and_3_out, clock_1_out, d_ff_1_q, d_ff_2_q, d_ff_3_q, not_1_out, not_2_out;

  Clock clock_1 (.out(clock_1_out));
  not not_1 (not_1_out, d_ff_3_q);
  not not_2 (not_2_out, X);
  and and_1 (and_1_out, d_ff_1_q, X, d_ff_2_q);
  and and_2 (and_2_out, not_1_out, d_ff_2_q, X);
  and and_3 (and_3_out, d_ff_2_q, d_ff_3_q, not_2_out);
  D_Flip_Flop d_ff_1 (.clk(clock_1_out), .D(and_1_out), .Q(d_ff_1_q));  // open: Qn, preset, reset
  D_Flip_Flop d_ff_2 (.clk(clock_1_out), .D(and_2_out), .Q(d_ff_2_q));  // open: Qn, preset, reset
  D_Flip_Flop d_ff_3 (.clk(clock_1_out), .D(and_3_out), .Q(d_ff_3_q));  // open: Qn, preset, reset
  and and_4 (Y, d_ff_2_q, d_ff_3_q);
endmodule
