// Logisim project Questao01.circ as structural Verilog: 1 circuit, main circuit main
module main (
  input  x,
  output y
);

  wire and_1_out, and_2_out, and_3_out, and_4_out, clock_1_out, d_ff_1_q, d_ff_2_q, not_1_out, not_2_out,
       not_3_out, or_1_out, or_2_out;

  not not_1 (not_1_out, d_ff_2_q);
  and and_1 (and_1_out, x, d_ff_1_q);
  or or_1 (or_1_out, and_1_out, and_2_out);
  and and_2 (and_2_out, d_ff_1_q, x, not_1_out);
  Clock clock_1 (.out(clock_1_out));
  not not_2 (not_2_out, d_ff_1_q);
  and and_3 (and_3_out, not_2_out, not_1_out, x);
  and and_4 (and_4_out, d_ff_1_q, d_ff_2_q);
  D_Flip_Flop d_ff_1 (.clk(clock_1_out), .D(or_1_out), .Q(d_ff_1_q), .reset(x));  // open: Qn, preset
  and and_5 (y, d_ff_1_q, x, not_3_out);
  not not_3 (not_3_out, d_ff_2_q);
  or or_2 (or_2_out, and_3_out, and_4_out);
  D_Flip_Flop d_ff_2 (.clk(clock_1_out), .D(or_2_out), .Q(d_ff_2_q));  // open: Qn, preset, reset
endmodule
