// Logisim project Questao02.circ as structural Verilog: 1 circuit, main circuit main
module main (
  input  x,
  output y
);

  wire and_1_out, and_3_out, and_4_out, clock_1_out, d_ff_2_q, d_ff_3_q, not_1_out, not_2_out, not_3_out;

  Clock clock_1 (.out(clock_1_out));
  and and_1 (and_1_out, clock_1_out, x, d_ff_2_q);
  not not_1 (not_1_out, x);
  D_Flip_Flop d_ff_1 (.clk(clock_1_out), .D(and_1_out), .Q(clock_1_out), .preset(clock_1_out));  // open: Qn, reset
  // AND_Gate and_2 has open pins: in0=clock_1_out, in1=d_ff_2_q, in2=x, in3=d_ff_3_q, out=open
  not not_2 (not_2_out, d_ff_3_q);
  and and_3 (and_3_out, d_ff_2_q, not_1_out, clock_1_out);
  not not_3 (not_3_out, clock_1_out);
  D_Flip_Flop d_ff_2 (.clk(clock_1_out), .D(and_4_out), .Q(d_ff_2_q));  // open: Qn, preset, reset
  and and_4 (and_4_out, not_3_out, d_ff_2_q, clock_1_out, not_2_out);
  D_Flip_Flop d_ff_3 (.clk(clock_1_out), .D(and_3_out), .Q(d_ff_3_q));  // open: Qn, preset, reset
  and and_5 (y, clock_1_out, d_ff_2_q);
endmodule
