// Logisim project Questao06.circ as structural Verilog: 1 circuit, main circuit main
module main (
  input  x,
  output out_2
);

  wire and_1_out, and_2_out, d_ff_1_q, d_ff_2_q, d_ff_3_q, not_1_out, or_1_out, or_2_out;

  and and_1 (and_1_out, d_ff_3_q, x, d_ff_2_q);
  not not_1 (not_1_out, d_ff_1_q);
  D_Flip_Flop d_ff_1 (.D(and_1_out), .Q(d_ff_1_q));  // open: clk, Qn, preset, reset
  or or_1 (or_1_out, not_1_out, d_ff_3_q);
  D_Flip_Flop d_ff_2 (.D(d_ff_2_q), .Q(d_ff_2_q));  // open: clk, Qn, preset, reset
  D_Flip_Flop d_ff_3 (.D(or_1_out), .Q(d_ff_3_q));  // open: clk, Qn, preset, reset
  and and_2 (and_2_out, d_ff_1_q, d_ff_1_q);
  or or_2 (or_2_out, d_ff_3_q, d_ff_3_q);
  and and_3 (out_2, and_2_out, or_2_out, d_ff_2_q);
endmodule
