// Logisim project Guia12.circ as structural Verilog: 9 circuits, main circuit 1x1 memory
module _1x1_memory (
  input  ADDR,
  input  R_W,
  input  CLK,
  input  IN,
  input  CLR,
  output out_6
);

  wire and_1_out, d_ff_1_q;

  and and_1 (and_1_out, ADDR, R_W, CLK);
  D_Flip_Flop d_ff_1 (.clk(and_1_out), .D(IN), .Q(d_ff_1_q), .reset(CLR));  // open: Qn, preset
  and and_2 (out_6, ADDR, d_ff_1_q);

  // Notes on the sheet:
  //   806937 - GUIA 12 - Felipe Pereira Da Silva
endmodule

module _1x2_memory (
  input  ADDR,
  input  R_W,
  input  CLK,
  input  IN,
  input  in_5,
  output out_6
);

  wire demultiplexer_1_out0, demultiplexer_1_out1, n1x1_memory_1_out_6, n1x1_memory_2_out_6;

  Demultiplexer #(.enable("false")) demultiplexer_1 (
    .out0(demultiplexer_1_out0), .out1(demultiplexer_1_out1), .in(1'b1), .sel(ADDR));
  _1x1_memory u_1x1_memory_1 (
    .ADDR(demultiplexer_1_out0), .R_W(R_W), .CLK(CLK), .IN(IN), .CLR(in_5), .out_6(n1x1_memory_1_out_6));
  _1x1_memory u_1x1_memory_2 (
    .ADDR(demultiplexer_1_out1), .R_W(R_W), .CLK(CLK), .IN(IN), .CLR(in_5), .out_6(n1x1_memory_2_out_6));
  Multiplexer #(.enable("false")) multiplexer_1 (
    .in0(n1x1_memory_1_out_6), .in1(n1x1_memory_2_out_6), .out(out_6), .sel(ADDR));
endmodule

module _1x1_ram (
  input  ADDR,
  input  R_W,
  input  CLK,
  input  IN_0,
  input  IN_1,
  output OUT_0,
  output OUT_1
);

  _1x1_memory u_1x1_memory_1 (.ADDR(ADDR), .R_W(R_W), .CLK(CLK), .IN(IN_0), .out_6(OUT_0));  // open: CLR
  _1x1_memory u_1x1_memory_2 (.ADDR(ADDR), .R_W(R_W), .CLK(CLK), .IN(IN_1), .out_6(OUT_1));  // open: CLR
endmodule

module _1x2_ram (
  input  ADDR,
  input  R_W,
  input  CLK,
  input  IN,
  input  in_5,
  output out_6
);

  wire demultiplexer_1_out0, demultiplexer_1_out1, n1x2_memory_1_out_6, n1x2_memory_2_out_6;

  Demultiplexer #(.enable("false")) demultiplexer_1 (
    .out0(demultiplexer_1_out0), .out1(demultiplexer_1_out1), .in(1'b1), .sel(ADDR));
  _1x2_memory u_1x2_memory_1 (
    .ADDR(demultiplexer_1_out0), .R_W(R_W), .CLK(CLK), .IN(IN), .out_6(n1x2_memory_1_out_6), .in_5(in_5));
  _1x2_memory u_1x2_memory_2 (
    .ADDR(demultiplexer_1_out1), .R_W(R_W), .CLK(CLK), .IN(IN), .out_6(n1x2_memory_2_out_6), .in_5(in_5));
  Multiplexer #(.enable("false")) multiplexer_1 (
    .in0(n1x2_memory_1_out_6), .in1(n1x2_memory_2_out_6), .out(out_6), .sel(ADDR));
endmodule

module _1x4_ram__ex_1 (
  input  [1:0] ADDR,
  input  R_W,
  input  CLK,
  input  IN,
  input  in_5,
  output out_6
);

  wire demultiplexer_1_out0, demultiplexer_1_out1, demultiplexer_1_out2, demultiplexer_1_out3,
       n1x1_memory_1_out_6, n1x1_memory_2_out_6, n1x1_memory_3_out_6, n1x1_memory_4_out_6;

  Demultiplexer #(.select(2), .enable("false")) demultiplexer_1 (
    .out0(demultiplexer_1_out0), .out1(demultiplexer_1_out1), .out2(demultiplexer_1_out2),
    .out3(demultiplexer_1_out3), .in(1'b1), .sel(ADDR));
  _1x1_memory u_1x1_memory_1 (
    .ADDR(demultiplexer_1_out0), .R_W(R_W), .CLK(CLK), .IN(IN), .CLR(in_5), .out_6(n1x1_memory_1_out_6));
  _1x1_memory u_1x1_memory_2 (
    .ADDR(demultiplexer_1_out1), .R_W(R_W), .CLK(CLK), .IN(IN), .CLR(in_5), .out_6(n1x1_memory_2_out_6));
  _1x1_memory u_1x1_memory_3 (
    .ADDR(demultiplexer_1_out2), .R_W(R_W), .CLK(CLK), .IN(IN), .CLR(in_5), .out_6(n1x1_memory_3_out_6));
  _1x1_memory u_1x1_memory_4 (
    .ADDR(demultiplexer_1_out3), .R_W(R_W), .CLK(CLK), .IN(IN), .CLR(in_5), .out_6(n1x1_memory_4_out_6));
  Multiplexer #(.select(2), .enable("false")) multiplexer_1 (
    .in0(n1x1_memory_1_out_6), .in1(n1x1_memory_2_out_6), .in2(n1x1_memory_3_out_6),
    .in3(n1x1_memory_4_out_6), .out(out_6), .sel(ADDR));
endmodule

module _1x8_ram__ex_2 (
  input  [1:0] ADDR,
  input  R_W,
  input  CLK,
  input  IN,
  input  in_5,
  output out_6
);

  wire n1x4_ram_ex_1_1_out_6, n1x4_ram_ex_1_2_out_6;
  wire [1:0] demultiplexer_1_out0, demultiplexer_1_out1;

  Demultiplexer #(.select(2), .width(2), .enable("false")) demultiplexer_1 (
    .out0(demultiplexer_1_out0), .out1(demultiplexer_1_out1), .in(2'b11), .sel(ADDR));  // open: out2, out3
  _1x4_ram__ex_1 u_1x4_ram_ex_1_1 (
    .ADDR(demultiplexer_1_out0), .R_W(R_W), .out_6(n1x4_ram_ex_1_1_out_6), .CLK(CLK), .IN(IN), .in_5(in_5));
  _1x4_ram__ex_1 u_1x4_ram_ex_1_2 (
    .ADDR(demultiplexer_1_out1), .R_W(R_W), .out_6(n1x4_ram_ex_1_2_out_6), .CLK(CLK), .in_5(in_5));  // open: IN
  Multiplexer #(.select(2), .enable("false")) multiplexer_1 (
    .in0(n1x4_ram_ex_1_1_out_6), .in3(n1x4_ram_ex_1_2_out_6), .out(out_6), .sel(ADDR));  // open: in1, in2
endmodule

module ram_2x8__ex_3 (
  input  [1:0] ADDR,
  input  R_W,
  input  CLK,
  input  IN_0,
  input  IN_1,
  input  in_6,
  output OUT_0,
  output OUT_1
);

  _1x8_ram__ex_2 u_1x8_ram_ex_2_1 (.ADDR(ADDR), .R_W(R_W), .CLK(CLK), .IN(IN_0), .out_6(OUT_0), .in_5(in_6));
  _1x8_ram__ex_2 u_1x8_ram_ex_2_2 (.ADDR(ADDR), .R_W(R_W), .CLK(CLK), .IN(IN_1), .out_6(OUT_1), .in_5(in_6));
endmodule

module ram_4x8__ex_4 (
  input  [1:0] ADDR,
  input  R_W,
  input  CLK,
  input  IN_0,
  input  IN_1,
  input  in_6,
  output OUT_0,
  output OUT_1,
  output OUT_2,
  output OUT_3
);

  ram_2x8__ex_3 ram_2x8_ex_3_1 (
    .ADDR(ADDR), .R_W(R_W), .CLK(CLK), .IN_0(IN_0), .IN_1(IN_1), .OUT_0(OUT_0), .OUT_1(OUT_1), .in_6(in_6));
  ram_2x8__ex_3 ram_2x8_ex_3_2 (
    .ADDR(ADDR), .R_W(R_W), .CLK(CLK), .IN_0(IN_0), .IN_1(IN_1), .OUT_0(OUT_2), .OUT_1(OUT_3), .in_6(in_6));
endmodule

module ram_8x8__ex_5 (
  input  [1:0] ADDR,
  input  R_W,
  input  CLK,
  input  IN_0,
  input  IN_1,
  input  in_6,
  output OUT_0,
  output OUT_1,
  output OUT_2,
  output OUT_3,
  output OUT_4,
  output OUT_5,
  output OUT_6,
  output OUT_7
);

  ram_4x8__ex_4 ram_4x8_ex_4_1 (
    .ADDR(ADDR), .R_W(R_W), .CLK(CLK), .IN_0(IN_0), .IN_1(IN_1), .OUT_0(OUT_0), .OUT_1(OUT_1), .OUT_2(OUT_2),
    .OUT_3(OUT_3), .in_6(in_6));
  ram_4x8__ex_4 ram_4x8_ex_4_2 (
    .ADDR(ADDR), .R_W(R_W), .CLK(CLK), .IN_0(IN_0), .IN_1(IN_1), .OUT_0(OUT_4), .OUT_1(OUT_5), .OUT_2(OUT_6),
    .OUT_3(OUT_7), .in_6(in_6));
endmodule
