// Logisim project g12q2.circ as structural Verilog: 1 circuit, main circuit main
module main (
  input  R_W,
  input  CLR,
  input  R_W_2,
  input  in_4
);

  wire and_1_out, clock_1_out, clock_2_out, j_k_ff_1_q, j_k_ff_1_qn, j_k_ff_2_q, j_k_ff_2_qn, j_k_ff_3_q,
       j_k_ff_3_qn, j_k_ff_4_q, j_k_ff_4_qn, j_k_ff_5_q, j_k_ff_5_qn, j_k_ff_6_q, j_k_ff_6_qn, j_k_ff_7_qn,
       j_k_ff_8_qn;

  Clock clock_1 (.out(clock_1_out));
  Clock clock_2 (.out(clock_2_out));
  J_K_Flip_Flop j_k_ff_1 (
    .J(R_W), .clk(clock_1_out), .K(CLR), .Q(j_k_ff_1_q), .Qn(j_k_ff_1_qn), .preset(clock_1_out), .reset(CLR));
  J_K_Flip_Flop j_k_ff_2 (
    .J(R_W_2), .clk(clock_2_out), .K(in_4), .Q(j_k_ff_2_q), .Qn(j_k_ff_2_qn), .preset(clock_2_out),
    .reset(in_4));
  J_K_Flip_Flop j_k_ff_3 (
    .J(j_k_ff_1_q), .clk(clock_1_out), .K(j_k_ff_1_qn), .Q(j_k_ff_3_q), .Qn(j_k_ff_3_qn),
    .preset(clock_1_out), .reset(CLR));
  J_K_Flip_Flop j_k_ff_4 (
    .J(j_k_ff_2_q), .clk(clock_2_out), .K(j_k_ff_2_qn), .Q(j_k_ff_4_q), .Qn(j_k_ff_4_qn),
    .preset(clock_2_out), .reset(in_4));
  J_K_Flip_Flop j_k_ff_5 (
    .J(j_k_ff_3_q), .clk(clock_1_out), .K(j_k_ff_3_qn), .Q(j_k_ff_5_q), .Qn(j_k_ff_5_qn),
    .preset(clock_1_out), .reset(CLR));
  J_K_Flip_Flop j_k_ff_6 (
    .J(j_k_ff_4_q), .clk(clock_2_out), .K(j_k_ff_4_qn), .Q(j_k_ff_6_q), .Qn(j_k_ff_6_qn),
    .preset(clock_2_out), .reset(in_4));
  J_K_Flip_Flop j_k_ff_7 (
    .J(j_k_ff_6_q), .clk(clock_2_out), .K(j_k_ff_6_qn), .Qn(j_k_ff_7_qn), .preset(clock_2_out), .reset(in_4));  // open: Q
  J_K_Flip_Flop j_k_ff_8 (
    .J(j_k_ff_5_q), .clk(clock_1_out), .K(j_k_ff_5_qn), .Qn(j_k_ff_8_qn), .preset(clock_1_out), .reset(CLR));  // open: Q
  and and_1 (and_1_out, j_k_ff_8_qn, j_k_ff_7_qn);
  // Probe on and_1_out
endmodule
