// Logisim project g12q3.circ as structural Verilog: 1 circuit, main circuit main
module main (
  input  R_W,
  input  CLR,
  input  R_W_2,
  input  CLR_2,
  input  in_5,
  input  R_W_3,
  input  CLR_3,
  input  R_W_4,
  input  CLR_4
);

  wire and_1_out, and_2_out, and_3_out, and_4_out, and_5_out, and_6_out, clock_1_out, clock_2_out,
       clock_3_out, clock_4_out, j_k_ff_1_q, j_k_ff_1_qn, j_k_ff_2_q, j_k_ff_3_q, j_k_ff_3_qn, j_k_ff_4_q,
       j_k_ff_4_qn, j_k_ff_5_q, j_k_ff_5_qn, j_k_ff_6_q, j_k_ff_7_q, j_k_ff_7_qn, j_k_ff_8_q, j_k_ff_8_qn,
       j_k_ff_9_q, j_k_ff_9_qn, j_k_ff_10_q, j_k_ff_10_qn, j_k_ff_11_q, j_k_ff_11_qn, j_k_ff_12_q,
       j_k_ff_12_qn, j_k_ff_13_q, j_k_ff_13_qn, j_k_ff_14_q, j_k_ff_14_qn, j_k_ff_15_q, j_k_ff_15_qn,
       j_k_ff_16_q, j_k_ff_16_qn, multiplexer_1_out;

  Clock clock_1 (.out(clock_1_out));
  Clock clock_2 (.out(clock_2_out));
  Clock clock_3 (.out(clock_3_out));
  Clock clock_4 (.out(clock_4_out));
  J_K_Flip_Flop j_k_ff_1 (
    .J(R_W), .clk(clock_1_out), .K(CLR), .Q(j_k_ff_1_q), .Qn(j_k_ff_1_qn));  // open: preset, reset
  J_K_Flip_Flop j_k_ff_2 (.J(R_W_2), .clk(clock_2_out), .K(CLR_2), .Q(j_k_ff_2_q));  // open: Qn, preset, reset
  J_K_Flip_Flop j_k_ff_3 (
    .J(R_W_3), .clk(clock_3_out), .K(CLR_3), .Q(j_k_ff_3_q), .Qn(j_k_ff_3_qn));  // open: preset, reset
  J_K_Flip_Flop j_k_ff_4 (
    .J(R_W_4), .clk(clock_4_out), .K(CLR_4), .Q(j_k_ff_4_q), .Qn(j_k_ff_4_qn));  // open: preset, reset
  J_K_Flip_Flop j_k_ff_5 (
    .J(j_k_ff_1_q), .clk(clock_1_out), .K(j_k_ff_1_qn), .Q(j_k_ff_5_q), .Qn(j_k_ff_5_qn));  // open: preset, reset
  J_K_Flip_Flop j_k_ff_6 (.J(j_k_ff_2_q), .clk(clock_2_out), .K(CLR_2), .Q(j_k_ff_6_q));  // open: Qn, preset, reset
  J_K_Flip_Flop j_k_ff_7 (
    .J(j_k_ff_3_q), .clk(clock_3_out), .K(j_k_ff_3_qn), .Q(j_k_ff_7_q), .Qn(j_k_ff_7_qn));  // open: preset, reset
  J_K_Flip_Flop j_k_ff_8 (
    .J(j_k_ff_4_q), .clk(clock_4_out), .K(j_k_ff_4_qn), .Q(j_k_ff_8_q), .Qn(j_k_ff_8_qn));  // open: preset, reset
  J_K_Flip_Flop j_k_ff_9 (
    .J(j_k_ff_5_q), .clk(clock_1_out), .K(j_k_ff_5_qn), .Q(j_k_ff_9_q), .Qn(j_k_ff_9_qn));  // open: preset, reset
  J_K_Flip_Flop j_k_ff_10 (
    .J(j_k_ff_6_q), .clk(clock_2_out), .K(CLR_2), .Q(j_k_ff_10_q), .Qn(j_k_ff_10_qn));  // open: preset, reset
  J_K_Flip_Flop j_k_ff_11 (
    .J(j_k_ff_7_q), .clk(clock_3_out), .K(j_k_ff_7_qn), .Q(j_k_ff_11_q), .Qn(j_k_ff_11_qn));  // open: preset, reset
  J_K_Flip_Flop j_k_ff_12 (
    .J(j_k_ff_8_q), .clk(clock_4_out), .K(j_k_ff_8_qn), .Q(j_k_ff_12_q), .Qn(j_k_ff_12_qn));  // open: preset, reset
  J_K_Flip_Flop j_k_ff_13 (
    .J(j_k_ff_9_q), .clk(clock_1_out), .K(j_k_ff_9_qn), .Q(j_k_ff_13_q), .Qn(j_k_ff_13_qn));  // open: preset, reset
  J_K_Flip_Flop j_k_ff_14 (
    .J(j_k_ff_10_q), .clk(clock_2_out), .K(j_k_ff_10_qn), .Q(j_k_ff_14_q), .Qn(j_k_ff_14_qn));  // open: preset, reset
  J_K_Flip_Flop j_k_ff_15 (
    .J(j_k_ff_11_q), .clk(clock_3_out), .K(j_k_ff_11_qn), .Q(j_k_ff_15_q), .Qn(j_k_ff_15_qn));  // open: preset, reset
  J_K_Flip_Flop j_k_ff_16 (
    .J(j_k_ff_12_q), .clk(clock_4_out), .K(j_k_ff_12_qn), .Q(j_k_ff_16_q), .Qn(j_k_ff_16_qn));  // open: preset, reset
  and and_1 (and_1_out, j_k_ff_13_q, j_k_ff_13_qn);
  and and_2 (and_2_out, j_k_ff_14_q, j_k_ff_14_qn);
  and and_3 (and_3_out, j_k_ff_15_q, j_k_ff_15_qn);
  and and_4 (and_4_out, j_k_ff_16_q, j_k_ff_16_qn);
  and and_5 (and_5_out, and_1_out, and_2_out);
  and and_6 (and_6_out, and_3_out, and_4_out);
  Multiplexer #(.enable("false")) multiplexer_1 (.in0(and_5_out), .in1(and_6_out), .out(multiplexer_1_out), .sel(in_5));
  // Probe on multiplexer_1_out
endmodule
