// Logisim project guia12.circ as structural Verilog: 1 circuit, main circuit main
module main (
  input  in_1,
  input  in_2
);

  wire demultiplexer_1_out0, demultiplexer_1_out1, j_k_ff_1_q, multiplexer_1_out;

  Clock clock_1 (.out(in_2));
  Demultiplexer #(.enable("false")) demultiplexer_1 (
    .out0(demultiplexer_1_out0), .out1(demultiplexer_1_out1), .in(in_1), .sel(in_2));
  J_K_Flip_Flop j_k_ff_1 (
    .J(demultiplexer_1_out0), .K(demultiplexer_1_out1), .Q(j_k_ff_1_q));  // open: clk, Qn, preset, reset
  Multiplexer #(.enable("false")) multiplexer_1 (.in1(j_k_ff_1_q), .out(multiplexer_1_out));  // open: in0, sel
  // Probe on multiplexer_1_out
endmodule
