// Logisim project guia12q1.circ as structural Verilog: 1 circuit, main circuit main
// CLR
module main (
  input  R_W,
  input  CLR
);

  wire and_1_out, clock_1_out, j_k_ff_1_q, j_k_ff_1_qn, j_k_ff_2_q, j_k_ff_2_qn, j_k_ff_3_q, j_k_ff_3_qn,
       j_k_ff_4_q, j_k_ff_4_qn, or_1_out;

  Clock clock_1 (.out(clock_1_out));
  and and_1 (and_1_out, R_W, R_W);
  J_K_Flip_Flop j_k_ff_1 (
    .J(R_W), .clk(clock_1_out), .K(and_1_out), .Q(j_k_ff_1_q), .Qn(j_k_ff_1_qn), .preset(clock_1_out),
    .reset(CLR));
  J_K_Flip_Flop j_k_ff_2 (
    .J(j_k_ff_1_q), .clk(clock_1_out), .K(j_k_ff_1_qn), .Q(j_k_ff_2_q), .Qn(j_k_ff_2_qn),
    .preset(clock_1_out), .reset(CLR));
  J_K_Flip_Flop j_k_ff_3 (
    .J(j_k_ff_2_q), .clk(clock_1_out), .K(j_k_ff_2_qn), .Q(j_k_ff_3_q), .Qn(j_k_ff_3_qn),
    .preset(clock_1_out), .reset(CLR));
  J_K_Flip_Flop j_k_ff_4 (
    .J(j_k_ff_3_q), .clk(clock_1_out), .K(j_k_ff_3_qn), .Q(j_k_ff_4_q), .Qn(j_k_ff_4_qn),
    .preset(clock_1_out), .reset(CLR));
  or or_1 (or_1_out, j_k_ff_4_q, j_k_ff_4_qn);
  // Probe on or_1_out
endmodule
