// Logisim project guia12q4.circ as structural Verilog: 1 circuit, main circuit main
module main (
  input  R_W,
  input  CLR,
  input  R_W_2,
  input  CLR_2,
  input  R_W_3,
  input  CLR_3,
  input  R_W_4,
  input  CLR_4,
  input  in_9,
  input  R_W_5,
  input  CLR_5,
  input  R_W_6,
  input  CLR_6,
  input  R_W_7,
  input  CLR_7,
  input  R_W_8,
  input  CLR_8
);

  wire and_1_out, and_2_out, and_3_out, and_4_out, and_5_out, and_6_out, and_7_out, and_8_out, and_9_out,
       and_10_out, and_11_out, and_12_out, and_13_out, and_14_out, clock_1_out, clock_2_out, clock_3_out,
       clock_4_out, clock_5_out, clock_6_out, clock_7_out, clock_8_out, j_k_ff_1_q, j_k_ff_1_qn, j_k_ff_2_q,
       j_k_ff_3_q, j_k_ff_3_qn, j_k_ff_4_q, j_k_ff_4_qn, j_k_ff_5_q, j_k_ff_5_qn, j_k_ff_6_q, j_k_ff_7_q,
       j_k_ff_7_qn, j_k_ff_8_q, j_k_ff_8_qn, j_k_ff_9_q, j_k_ff_9_qn, j_k_ff_10_q, j_k_ff_10_qn, j_k_ff_11_q,
       j_k_ff_12_q, j_k_ff_13_q, j_k_ff_13_qn, j_k_ff_14_q, j_k_ff_14_qn, j_k_ff_15_q, j_k_ff_15_qn,
       j_k_ff_16_q, j_k_ff_16_qn, j_k_ff_17_q, j_k_ff_17_qn, j_k_ff_18_q, j_k_ff_18_qn, j_k_ff_19_q,
       j_k_ff_19_qn, j_k_ff_20_q, j_k_ff_20_qn, j_k_ff_21_q, j_k_ff_21_qn, j_k_ff_22_q, j_k_ff_22_qn,
       j_k_ff_23_q, j_k_ff_23_qn, j_k_ff_24_q, j_k_ff_24_qn, j_k_ff_25_q, j_k_ff_25_qn, j_k_ff_26_q,
       j_k_ff_26_qn, j_k_ff_27_q, j_k_ff_27_qn, j_k_ff_28_q, j_k_ff_28_qn, j_k_ff_29_q, j_k_ff_29_qn,
       j_k_ff_30_q, j_k_ff_30_qn, j_k_ff_31_q, j_k_ff_31_qn, j_k_ff_32_q, j_k_ff_32_qn, multiplexer_1_out;

  Clock clock_1 (.out(clock_1_out));
  Clock clock_2 (.out(clock_2_out));
  Clock clock_3 (.out(clock_3_out));
  Clock clock_4 (.out(clock_4_out));
  Clock clock_5 (.out(clock_5_out));
  Clock clock_6 (.out(clock_6_out));
  Clock clock_7 (.out(clock_7_out));
  Clock clock_8 (.out(clock_8_out));
  J_K_Flip_Flop j_k_ff_1 (
    .J(R_W), .clk(clock_1_out), .K(CLR), .Q(j_k_ff_1_q), .Qn(j_k_ff_1_qn));  // open: preset, reset
  J_K_Flip_Flop j_k_ff_2 (.J(R_W_2), .clk(clock_2_out), .K(CLR_2), .Q(j_k_ff_2_q));  // open: Qn, preset, reset
  J_K_Flip_Flop j_k_ff_3 (
    .J(R_W_3), .clk(clock_3_out), .K(CLR_3), .Q(j_k_ff_3_q), .Qn(j_k_ff_3_qn));  // open: preset, reset
  J_K_Flip_Flop j_k_ff_4 (
    .J(R_W_4), .clk(clock_4_out), .K(CLR_4), .Q(j_k_ff_4_q), .Qn(j_k_ff_4_qn));  // open: preset, reset
  J_K_Flip_Flop j_k_ff_5 (
    .J(R_W_5), .clk(clock_5_out), .K(CLR_5), .Q(j_k_ff_5_q), .Qn(j_k_ff_5_qn));  // open: preset, reset
  J_K_Flip_Flop j_k_ff_6 (.J(R_W_6), .clk(clock_6_out), .K(CLR_6), .Q(j_k_ff_6_q));  // open: Qn, preset, reset
  J_K_Flip_Flop j_k_ff_7 (
    .J(R_W_7), .clk(clock_7_out), .K(CLR_7), .Q(j_k_ff_7_q), .Qn(j_k_ff_7_qn));  // open: preset, reset
  J_K_Flip_Flop j_k_ff_8 (
    .J(R_W_8), .clk(clock_8_out), .K(CLR_8), .Q(j_k_ff_8_q), .Qn(j_k_ff_8_qn));  // open: preset, reset
  J_K_Flip_Flop j_k_ff_9 (
    .J(j_k_ff_1_q), .clk(clock_1_out), .K(j_k_ff_1_qn), .Q(j_k_ff_9_q), .Qn(j_k_ff_9_qn));  // open: preset, reset
  J_K_Flip_Flop j_k_ff_10 (
    .J(j_k_ff_5_q), .clk(clock_5_out), .K(j_k_ff_5_qn), .Q(j_k_ff_10_q), .Qn(j_k_ff_10_qn));  // open: preset, reset
  J_K_Flip_Flop j_k_ff_11 (.J(j_k_ff_6_q), .clk(clock_6_out), .K(CLR_6), .Q(j_k_ff_11_q));  // open: Qn, preset, reset
  J_K_Flip_Flop j_k_ff_12 (.J(j_k_ff_2_q), .clk(clock_2_out), .K(CLR_2), .Q(j_k_ff_12_q));  // open: Qn, preset, reset
  J_K_Flip_Flop j_k_ff_13 (
    .J(j_k_ff_3_q), .clk(clock_3_out), .K(j_k_ff_3_qn), .Q(j_k_ff_13_q), .Qn(j_k_ff_13_qn));  // open: preset, reset
  J_K_Flip_Flop j_k_ff_14 (
    .J(j_k_ff_4_q), .clk(clock_4_out), .K(j_k_ff_4_qn), .Q(j_k_ff_14_q), .Qn(j_k_ff_14_qn));  // open: preset, reset
  J_K_Flip_Flop j_k_ff_15 (
    .J(j_k_ff_7_q), .clk(clock_7_out), .K(j_k_ff_7_qn), .Q(j_k_ff_15_q), .Qn(j_k_ff_15_qn));  // open: preset, reset
  J_K_Flip_Flop j_k_ff_16 (
    .J(j_k_ff_8_q), .clk(clock_8_out), .K(j_k_ff_8_qn), .Q(j_k_ff_16_q), .Qn(j_k_ff_16_qn));  // open: preset, reset
  J_K_Flip_Flop j_k_ff_17 (
    .J(j_k_ff_10_q), .clk(clock_5_out), .K(j_k_ff_10_qn), .Q(j_k_ff_17_q), .Qn(j_k_ff_17_qn));  // open: preset, reset
  J_K_Flip_Flop j_k_ff_18 (
    .J(j_k_ff_9_q), .clk(clock_1_out), .K(j_k_ff_9_qn), .Q(j_k_ff_18_q), .Qn(j_k_ff_18_qn));  // open: preset, reset
  J_K_Flip_Flop j_k_ff_19 (
    .J(j_k_ff_12_q), .clk(clock_2_out), .K(CLR_2), .Q(j_k_ff_19_q), .Qn(j_k_ff_19_qn));  // open: preset, reset
  J_K_Flip_Flop j_k_ff_20 (
    .J(j_k_ff_13_q), .clk(clock_3_out), .K(j_k_ff_13_qn), .Q(j_k_ff_20_q), .Qn(j_k_ff_20_qn));  // open: preset, reset
  J_K_Flip_Flop j_k_ff_21 (
    .J(j_k_ff_14_q), .clk(clock_4_out), .K(j_k_ff_14_qn), .Q(j_k_ff_21_q), .Qn(j_k_ff_21_qn));  // open: preset, reset
  J_K_Flip_Flop j_k_ff_22 (
    .J(j_k_ff_11_q), .clk(clock_6_out), .K(CLR_6), .Q(j_k_ff_22_q), .Qn(j_k_ff_22_qn));  // open: preset, reset
  J_K_Flip_Flop j_k_ff_23 (
    .J(j_k_ff_15_q), .clk(clock_7_out), .K(j_k_ff_15_qn), .Q(j_k_ff_23_q), .Qn(j_k_ff_23_qn));  // open: preset, reset
  J_K_Flip_Flop j_k_ff_24 (
    .J(j_k_ff_16_q), .clk(clock_8_out), .K(j_k_ff_16_qn), .Q(j_k_ff_24_q), .Qn(j_k_ff_24_qn));  // open: preset, reset
  J_K_Flip_Flop j_k_ff_25 (
    .J(j_k_ff_17_q), .clk(clock_5_out), .K(j_k_ff_17_qn), .Q(j_k_ff_25_q), .Qn(j_k_ff_25_qn));  // open: preset, reset
  J_K_Flip_Flop j_k_ff_26 (
    .J(j_k_ff_18_q), .clk(clock_1_out), .K(j_k_ff_18_qn), .Q(j_k_ff_26_q), .Qn(j_k_ff_26_qn));  // open: preset, reset
  J_K_Flip_Flop j_k_ff_27 (
    .J(j_k_ff_19_q), .clk(clock_2_out), .K(j_k_ff_19_qn), .Q(j_k_ff_27_q), .Qn(j_k_ff_27_qn));  // open: preset, reset
  J_K_Flip_Flop j_k_ff_28 (
    .J(j_k_ff_20_q), .clk(clock_3_out), .K(j_k_ff_20_qn), .Q(j_k_ff_28_q), .Qn(j_k_ff_28_qn));  // open: preset, reset
  J_K_Flip_Flop j_k_ff_29 (
    .J(j_k_ff_21_q), .clk(clock_4_out), .K(j_k_ff_21_qn), .Q(j_k_ff_29_q), .Qn(j_k_ff_29_qn));  // open: preset, reset
  J_K_Flip_Flop j_k_ff_30 (
    .J(j_k_ff_22_q), .clk(clock_6_out), .K(j_k_ff_22_qn), .Q(j_k_ff_30_q), .Qn(j_k_ff_30_qn));  // open: preset, reset
  J_K_Flip_Flop j_k_ff_31 (
    .J(j_k_ff_23_q), .clk(clock_7_out), .K(j_k_ff_23_qn), .Q(j_k_ff_31_q), .Qn(j_k_ff_31_qn));  // open: preset, reset
  J_K_Flip_Flop j_k_ff_32 (
    .J(j_k_ff_24_q), .clk(clock_8_out), .K(j_k_ff_24_qn), .Q(j_k_ff_32_q), .Qn(j_k_ff_32_qn));  // open: preset, reset
  and and_1 (and_1_out, j_k_ff_26_q, j_k_ff_26_qn);
  and and_2 (and_2_out, j_k_ff_25_q, j_k_ff_25_qn);
  and and_3 (and_3_out, j_k_ff_27_q, j_k_ff_27_qn);
  and and_4 (and_4_out, j_k_ff_28_q, j_k_ff_28_qn);
  and and_5 (and_5_out, j_k_ff_29_q, j_k_ff_29_qn);
  and and_6 (and_6_out, j_k_ff_30_q, j_k_ff_30_qn);
  and and_7 (and_7_out, j_k_ff_31_q, j_k_ff_31_qn);
  and and_8 (and_8_out, j_k_ff_32_q, j_k_ff_32_qn);
  and and_9 (and_9_out, and_2_out, and_6_out);
  and and_10 (and_10_out, and_1_out, and_3_out);
  and and_11 (and_11_out, and_4_out, and_5_out);
  and and_12 (and_12_out, and_7_out, and_8_out);
  and and_13 (and_13_out, and_9_out, and_12_out);
  and and_14 (and_14_out, and_10_out, and_11_out);
  Multiplexer #(.enable("false")) multiplexer_1 (
    .in0(and_14_out), .in1(and_13_out), .out(multiplexer_1_out), .sel(in_9));
  // Probe on multiplexer_1_out
endmodule
