// Logisim project Guia_1201.circ as structural Verilog: 1 circuit, main circuit main
module main (
  input  adress,
  input  r_w,
  input  \input ,
  input  clear,
  output s0,
  output s1,
  output s2,
  output s4
);

  wire and_1_out, clk_out, j_k_ff_1_q, j_k_ff_1_qn, j_k_ff_2_q, j_k_ff_2_qn, j_k_ff_3_q, j_k_ff_3_qn,
       j_k_ff_4_q, not_1_out;

  Clock clk (.out(clk_out));
  and and_1 (and_1_out, adress, r_w, clk_out);
  not not_1 (not_1_out, \input );
  J_K_Flip_Flop j_k_ff_1 (
    .J(\input ), .clk(and_1_out), .K(not_1_out), .Q(j_k_ff_1_q), .Qn(j_k_ff_1_qn), .reset(clear));  // open: preset
  and and_2 (s0, adress, j_k_ff_1_q);
  J_K_Flip_Flop j_k_ff_2 (
    .J(j_k_ff_1_q), .clk(and_1_out), .K(j_k_ff_1_qn), .Q(j_k_ff_2_q), .Qn(j_k_ff_2_qn), .reset(clear));  // open: preset
  and and_3 (s1, adress, j_k_ff_2_q);
  J_K_Flip_Flop j_k_ff_3 (
    .J(j_k_ff_2_q), .clk(and_1_out), .K(j_k_ff_2_qn), .Q(j_k_ff_3_q), .Qn(j_k_ff_3_qn), .reset(clear));  // open: preset
  and and_4 (s2, adress, j_k_ff_3_q);
  J_K_Flip_Flop j_k_ff_4 (
    .J(j_k_ff_3_q), .clk(and_1_out), .K(j_k_ff_3_qn), .Q(j_k_ff_4_q), .reset(clear));  // open: Qn, preset
  and and_5 (s4, adress, j_k_ff_4_q);

  // Notes on the sheet:
  //   Enzo M pylo
endmodule
