// Logisim project Guia_1202.circ as structural Verilog: 2 circuits, main circuit main
module main (
  input  ADRESS,
  input  R_W,
  input  CLEAR,
  input  i0,
  input  i1,
  input  i2,
  input  i3,
  input  i4,
  input  i5,
  input  i6,
  input  i7,
  output [7:0] out_12
);

  wire CLK_out;

  Clock CLK (.out(CLK_out));
  RAM_1x4 ram_1x4_1 (
    .adress(ADRESS), .R_W(R_W), .i0(i0), .clear(CLEAR), .clock(CLK_out), .o3(out_12[3]), .o2(out_12[2]),
    .o1(out_12[1]), .o0(out_12[0]), .i1(i1), .i2(i2), .i4(i3));
  RAM_1x4 ram_1x4_2 (
    .adress(ADRESS), .R_W(R_W), .i0(i4), .clear(CLEAR), .clock(CLK_out), .o3(out_12[7]), .o2(out_12[6]),
    .o1(out_12[5]), .o0(out_12[4]), .i1(i5), .i2(i6), .i4(i7));

  // Notes on the sheet:
  //   Enzo M pylo
  //   RAM_1x8
endmodule

module RAM_1x4 (
  input  adress,
  input  R_W,
  input  clock,
  input  clear,
  input  i0,
  input  i1,
  input  i2,
  input  i4,
  output o3,
  output o2,
  output o1,
  output o0
);

  wire and_1_out, j_k_ff_1_q, j_k_ff_2_q, j_k_ff_3_q, j_k_ff_4_q, not_1_out, not_2_out, not_3_out, not_4_out;

  and and_1 (and_1_out, adress, R_W, clock);
  not not_1 (not_1_out, i0);
  J_K_Flip_Flop j_k_ff_1 (.J(i0), .clk(and_1_out), .K(not_1_out), .Q(j_k_ff_1_q), .reset(clear));  // open: Qn, preset
  J_K_Flip_Flop j_k_ff_2 (.J(i1), .clk(and_1_out), .K(not_2_out), .Q(j_k_ff_2_q), .reset(clear));  // open: Qn, preset
  not not_2 (not_2_out, i1);
  not not_3 (not_3_out, i2);
  J_K_Flip_Flop j_k_ff_3 (.J(i2), .clk(and_1_out), .K(not_3_out), .Q(j_k_ff_3_q), .reset(clear));  // open: Qn, preset
  not not_4 (not_4_out, i4);
  J_K_Flip_Flop j_k_ff_4 (.J(i4), .clk(and_1_out), .K(not_4_out), .Q(j_k_ff_4_q), .reset(clear));  // open: Qn, preset
  and and_2 (o3, adress, j_k_ff_4_q);
  and and_3 (o2, adress, j_k_ff_3_q);
  and and_4 (o1, adress, j_k_ff_2_q);
  and and_5 (o0, adress, j_k_ff_1_q);
endmodule
