// Logisim project Guia_1203.circ as structural Verilog: 3 circuits, main circuit main
module main (
  input  adress,
  input  r_w,
  input  [7:0] in_3,
  input  CLEAR,
  output [7:0] out_5
);

  wire clock_out, demultiplexer_1_out0, demultiplexer_1_out1;
  wire [7:0] ram_1x8_1_o, ram_1x8_2_o;

  Demultiplexer #(.enable("false")) demultiplexer_1 (
    .out0(demultiplexer_1_out0), .out1(demultiplexer_1_out1), .in(1'b1), .sel(adress));
  Clock clock (.out(clock_out));
  RAM_1x8 ram_1x8_1 (
    .ADDRESS(demultiplexer_1_out0), .R_W(r_w), .CLEAR(CLEAR), .o(ram_1x8_1_o), .CLOCK(clock_out), .in_1(in_3));
  RAM_1x8 ram_1x8_2 (
    .ADDRESS(demultiplexer_1_out1), .R_W(r_w), .CLEAR(CLEAR), .o(ram_1x8_2_o), .CLOCK(clock_out), .in_1(in_3));
  Multiplexer #(.width(8), .enable("false")) multiplexer_1 (
    .in0(ram_1x8_1_o), .in1(ram_1x8_2_o), .out(out_5), .sel(adress));

  // Notes on the sheet:
  //   Enzo M pylo
  //   RAM_2x8
endmodule

module RAM_1x4 (
  input  [3:0] in_1,
  input  address,
  input  r_w,
  input  clock,
  input  clear,
  output [3:0] out_6
);

  wire and_1_out, j_k_ff_1_q, j_k_ff_2_q, j_k_ff_3_q, j_k_ff_4_q, not_1_out, not_2_out, not_3_out, not_4_out;

  and and_1 (and_1_out, address, r_w, clock);
  not not_1 (not_1_out, in_1[0]);
  not not_2 (not_2_out, in_1[1]);
  J_K_Flip_Flop j_k_ff_1 (
    .J(in_1[0]), .clk(and_1_out), .K(not_1_out), .Q(j_k_ff_1_q), .reset(clear));  // open: Qn, preset
  and and_2 (out_6[0], j_k_ff_1_q, address);
  J_K_Flip_Flop j_k_ff_2 (
    .J(in_1[1]), .clk(and_1_out), .K(not_2_out), .Q(j_k_ff_2_q), .reset(clear));  // open: Qn, preset
  not not_3 (not_3_out, in_1[2]);
  and and_3 (out_6[1], j_k_ff_2_q, address);
  not not_4 (not_4_out, in_1[3]);
  J_K_Flip_Flop j_k_ff_3 (
    .J(in_1[2]), .clk(and_1_out), .K(not_3_out), .Q(j_k_ff_3_q), .reset(clear));  // open: Qn, preset
  and and_4 (out_6[2], j_k_ff_3_q, address);
  J_K_Flip_Flop j_k_ff_4 (
    .J(in_1[3]), .clk(and_1_out), .K(not_4_out), .Q(j_k_ff_4_q), .reset(clear));  // open: Qn, preset
  and and_5 (out_6[3], j_k_ff_4_q, address);

  // Notes on the sheet:
  //   RAM_1x4
endmodule

module RAM_1x8 (
  input  [7:0] in_1,
  input  ADDRESS,
  input  R_W,
  input  CLOCK,
  input  CLEAR,
  output [7:0] o
);

  RAM_1x4 ram_1x4_1 (.address(ADDRESS), .r_w(R_W), .clock(CLOCK), .clear(CLEAR), .in_1(in_1[3:0]), .out_6(o[3:0]));
  RAM_1x4 ram_1x4_2 (.address(ADDRESS), .r_w(R_W), .clock(CLOCK), .clear(CLEAR), .in_1(in_1[7:4]), .out_6(o[7:4]));

  // Notes on the sheet:
  //   RAM_1x8
endmodule
