// Logisim project G12.circ as structural Verilog: 14 circuits, main circuit RAM 1x1
module RAM_1x1 (
  input  R_W,
  input  address,
  input  clk,
  input  in,
  input  clr,
  output out
);

  wire and_1_out, d_ff_1_q;

  and and_1 (and_1_out, address, R_W, clk);
  D_Flip_Flop #(.Pre_Clr_Positions("LEGACY"), .NewFFLayout("false")) d_ff_1 (
    .clk(and_1_out), .D(in), .Q(d_ff_1_q), .reset(clr));  // open: Qn, preset
  and and_2 (out, address, d_ff_1_q);
endmodule

module RAM_1x2 (
  input  Address,
  input  R_W,
  input  Clk,
  input  Clr,
  input  b_in,
  input  a_in,
  output b_out,
  output a_out
);

  RAM_1x1 a (.R_W(R_W), .clk(Clk), .clr(Clr), .address(Address), .out(a_out), .in(a_in));
  RAM_1x1 b (.R_W(R_W), .clk(Clk), .clr(Clr), .address(Address), .out(b_out), .in(b_in));
endmodule

module RAM_1x4 (
  input  A_in,
  input  B_in,
  input  Address,
  input  C_in,
  input  D_in,
  input  R_W,
  input  Clk,
  input  Clr,
  output A_out,
  output B_out,
  output C_out,
  output D_out
);

  RAM_1x2 ram_1x2_1 (
    .R_W(R_W), .Clk(Clk), .Clr(Clr), .Address(Address), .b_out(C_out), .a_out(D_out), .b_in(C_in), .a_in(D_in));
  RAM_1x2 ram_1x2_2 (
    .R_W(R_W), .Clk(Clk), .Clr(Clr), .Address(Address), .b_out(A_out), .a_out(B_out), .b_in(A_in), .a_in(B_in));
endmodule

module RAM_1x4b (
  input  R_W,
  input  Address,
  input  Clk,
  input  Clr,
  input  A_in,
  input  B_in,
  input  C_in,
  input  D_out,
  output A_out,
  output B_out,
  output C_out,
  output D_out_2
);

  RAM_1x1 A (.R_W(R_W), .clk(Clk), .clr(Clr), .address(Address), .out(A_out), .in(A_in));
  RAM_1x1 B (.R_W(R_W), .clk(Clk), .clr(Clr), .address(Address), .out(B_out), .in(B_in));
  RAM_1x1 C (.R_W(R_W), .clk(Clk), .clr(Clr), .address(Address), .out(C_out), .in(C_in));
  RAM_1x1 D (.R_W(R_W), .clk(Clk), .clr(Clr), .address(Address), .out(D_out_2), .in(D_out));
endmodule

module RAM_1x4c (
  input  R_W,
  input  Clk,
  input  Address,
  input  Clr,
  input  [3:0] in,
  output [3:0] out
);

  RAM_1x4b ram_1x4b_1 (
    .R_W(R_W), .Clk(Clk), .Clr(Clr), .Address(Address), .A_out(out[3]), .B_out(out[2]), .C_out(out[1]),
    .D_out_2(out[0]), .A_in(in[3]), .B_in(in[2]), .C_in(in[1]), .D_out(in[0]));
endmodule

module RAM_1x8 (
  input  Address,
  input  R_W,
  input  Clk,
  input  Clr,
  input  [7:0] In,
  output [7:0] Out
);

  RAM_1x4c ram_1x4c_1 (.R_W(R_W), .Clk(Clk), .Clr(Clr), .Address(Address), .out(Out[7:4]), .in(In[7:4]));
  RAM_1x4c ram_1x4c_2 (.R_W(R_W), .Clk(Clk), .Clr(Clr), .Address(Address), .out(Out[3:0]), .in(In[3:0]));
endmodule

module RAM_1x16 (
  input  Address,
  input  R_W,
  input  Clk,
  input  Clr,
  input  [15:0] In,
  output [15:0] Out
);

  RAM_1x8 ram_1x8_1 (.R_W(R_W), .Clk(Clk), .Clr(Clr), .Out(Out[15:8]), .In(In[15:8]), .Address(Address));
  RAM_1x8 ram_1x8_2 (.R_W(R_W), .Clk(Clk), .Clr(Clr), .Out(Out[7:0]), .In(In[7:0]), .Address(Address));
endmodule

module G1201 (
  input  R_W,
  input  Address,
  input  Clk,
  input  [3:0] In,
  input  Clr,
  output [3:0] Out
);

  RAM_1x4c ram_1x4c_1 (.R_W(R_W), .Clk(Clk), .Clr(Clr), .Address(Address), .out(Out), .in(In));

  // Notes on the sheet:
  //   RAM 1x4
endmodule

module G1202 (
  input  Address,
  input  R_W,
  input  Clk,
  input  Clr,
  input  [7:0] In,
  output [7:0] Out
);

  RAM_1x4c ram_1x4c_1 (.R_W(R_W), .Clk(Clk), .Clr(Clr), .Address(Address), .out(Out[7:4]), .in(In[7:4]));
  RAM_1x4c ram_1x4c_2 (.R_W(R_W), .Clk(Clk), .Clr(Clr), .Address(Address), .out(Out[3:0]), .in(In[3:0]));

  // Notes on the sheet:
  //   RAM 1x8
endmodule

module G1203 (
  input  Address,
  input  R_W,
  input  Clk,
  input  [7:0] In,
  input  Clr,
  output [7:0] Out
);

  wire demultiplexer_1_out0, demultiplexer_1_out1;
  wire [7:0] ram_1x8_1_out, ram_1x8_2_out;

  Demultiplexer #(.enable("false")) demultiplexer_1 (
    .out0(demultiplexer_1_out0), .out1(demultiplexer_1_out1), .in(1'b1), .sel(Address));
  RAM_1x8 ram_1x8_1 (.R_W(R_W), .Clk(Clk), .Clr(Clr), .Out(ram_1x8_1_out), .In(In), .Address(demultiplexer_1_out1));
  RAM_1x8 ram_1x8_2 (.R_W(R_W), .Clk(Clk), .Clr(Clr), .Out(ram_1x8_2_out), .In(In), .Address(demultiplexer_1_out0));
  Multiplexer #(.width(8), .enable("false")) multiplexer_1 (
    .in0(ram_1x8_2_out), .in1(ram_1x8_1_out), .out(Out), .sel(Address));

  // Notes on the sheet:
  //   RAM 2x8
endmodule

module G1204 (
  input  [1:0] Address,
  input  R_W,
  input  Clk,
  input  [7:0] In,
  input  Clr,
  output [7:0] Out
);

  wire demultiplexer_1_out0, demultiplexer_1_out1;
  wire [7:0] g1203_1_out, g1203_2_out;

  G1203 g1203_1 (.Address(Address[0]), .R_W(demultiplexer_1_out0), .Clk(Clk), .Clr(Clr), .Out(g1203_1_out), .In(In));
  Demultiplexer #(.enable("false")) demultiplexer_1 (
    .out0(demultiplexer_1_out0), .out1(demultiplexer_1_out1), .in(R_W), .sel(Address[1]));
  Multiplexer #(.width(8), .enable("false")) multiplexer_1 (
    .in0(g1203_1_out), .in1(g1203_2_out), .out(Out), .sel(Address[1]));
  G1203 g1203_2 (.Address(Address[0]), .R_W(demultiplexer_1_out1), .Clk(Clk), .Clr(Clr), .Out(g1203_2_out), .In(In));

  // Notes on the sheet:
  //   RAM 4x8
endmodule

module G1205 (
  input  [2:0] Address,
  input  R_W,
  input  Clk,
  input  [7:0] In,
  input  Clr,
  output [7:0] Out
);

  wire demultiplexer_1_out0, demultiplexer_1_out1;
  wire [7:0] g1204_1_out, g1204_2_out;

  G1204 g1204_1 (.R_W(demultiplexer_1_out0), .Clk(Clk), .Clr(Clr), .Address(Address[1:0]), .In(In), .Out(g1204_1_out));
  Demultiplexer #(.enable("false")) demultiplexer_1 (
    .out0(demultiplexer_1_out0), .out1(demultiplexer_1_out1), .in(R_W), .sel(Address[2]));
  G1204 g1204_2 (.R_W(demultiplexer_1_out1), .Clk(Clk), .Clr(Clr), .Address(Address[1:0]), .In(In), .Out(g1204_2_out));
  Multiplexer #(.width(8), .enable("false")) multiplexer_1 (
    .in0(g1204_1_out), .in1(g1204_2_out), .out(Out), .sel(Address[2]));

  // Notes on the sheet:
  //   RAM 8x8
endmodule

module G1206 (
  input  [1:0] Address,
  input  R_W,
  input  Clk,
  input  [15:0] Out,
  input  Clr,
  output [15:0] In
);

  G1204 g1204_1 (.R_W(R_W), .Clk(Clk), .Clr(Clr), .Address(Address), .In(Out[15:8]), .Out(In[15:8]));
  G1204 g1204_2 (.R_W(R_W), .Clk(Clk), .Clr(Clr), .Address(Address), .In(Out[7:0]), .Out(In[7:0]));

  // Notes on the sheet:
  //   RAM 4x16
endmodule

module G1207 (
  input  [2:0] Address,
  input  R_W,
  input  Clk,
  input  Clr,
  input  [15:0] In,
  output [15:0] Out
);

  wire demultiplexer_1_out0, demultiplexer_1_out1, demultiplexer_1_out2, demultiplexer_1_out3,
       demultiplexer_1_out4, demultiplexer_1_out5, demultiplexer_1_out6, demultiplexer_1_out7;
  wire [15:0] ram_1x16_1_out, ram_1x16_2_out, ram_1x16_3_out, ram_1x16_4_out, ram_1x16_5_out, ram_1x16_6_out,
       ram_1x16_7_out, ram_1x16_8_out;

  RAM_1x16 ram_1x16_1 (.R_W(demultiplexer_1_out0), .Clk(Clk), .Clr(Clr), .Out(ram_1x16_1_out), .In(In), .Address(1'b1));
  RAM_1x16 ram_1x16_2 (.R_W(demultiplexer_1_out1), .Clk(Clk), .Clr(Clr), .Out(ram_1x16_2_out), .In(In), .Address(1'b1));
  RAM_1x16 ram_1x16_3 (.R_W(demultiplexer_1_out2), .Clk(Clk), .Clr(Clr), .Out(ram_1x16_3_out), .In(In), .Address(1'b1));
  RAM_1x16 ram_1x16_4 (.R_W(demultiplexer_1_out3), .Clk(Clk), .Clr(Clr), .Out(ram_1x16_4_out), .In(In), .Address(1'b1));
  Demultiplexer #(.select(3), .enable("false")) demultiplexer_1 (
    .out0(demultiplexer_1_out0), .out1(demultiplexer_1_out1), .out2(demultiplexer_1_out2),
    .out3(demultiplexer_1_out3), .out4(demultiplexer_1_out4), .out5(demultiplexer_1_out5),
    .out6(demultiplexer_1_out6), .out7(demultiplexer_1_out7), .in(R_W), .sel(Address));
  RAM_1x16 ram_1x16_5 (.R_W(demultiplexer_1_out4), .Clk(Clk), .Clr(Clr), .Out(ram_1x16_5_out), .In(In), .Address(1'b1));
  RAM_1x16 ram_1x16_6 (.R_W(demultiplexer_1_out5), .Clk(Clk), .Clr(Clr), .Out(ram_1x16_6_out), .In(In), .Address(1'b1));
  RAM_1x16 ram_1x16_7 (.R_W(demultiplexer_1_out6), .Clk(Clk), .Clr(Clr), .Out(ram_1x16_7_out), .In(In), .Address(1'b1));
  RAM_1x16 ram_1x16_8 (.R_W(demultiplexer_1_out7), .Clk(Clk), .Clr(Clr), .Out(ram_1x16_8_out), .In(In), .Address(1'b1));
  Multiplexer #(.select(3), .width(16), .enable("false")) multiplexer_1 (
    .in0(ram_1x16_1_out), .in1(ram_1x16_2_out), .in2(ram_1x16_3_out), .in3(ram_1x16_4_out),
    .in4(ram_1x16_5_out), .in5(ram_1x16_6_out), .in6(ram_1x16_7_out), .in7(ram_1x16_8_out), .out(Out),
    .sel(Address));

  // Notes on the sheet:
  //   RAM 8x16
endmodule
