// Logisim project Guia_12.circ as structural Verilog: 10 circuits, main circuit FlipFlop_JK
module FlipFlop_JK (
  input  clk,
  input  in,
  input  clr,
  output s,
  output ns
);

  wire and_1_out, and_2_out, not_1_out, or_1_out;

  not not_1 (not_1_out, in);
  J_K_Flip_Flop #(.Pre_Clr_Positions("LEGACY"), .NewFFLayout("false")) j_k_ff_1 (
    .clk(clk), .Q(s), .Qn(ns), .preset(and_1_out), .reset(or_1_out));  // open: J, K
  and and_1 (and_1_out, in, clk);
  or or_1 (or_1_out, and_2_out, clr);
  and and_2 (and_2_out, not_1_out, clk);

  // Notes on the sheet:
  //   FlipFlop JK
endmodule

module RAM_1x1 (
  input  rw,
  input  addr,
  input  clk,
  input  in,
  input  clr,
  output out_6
);

  wire and_1_out, flipflop_jk_1_s;

  and and_1 (and_1_out, addr, rw, clk);
  and and_2 (out_6, addr, flipflop_jk_1_s);
  FlipFlop_JK flipflop_jk_1 (.in(in), .s(flipflop_jk_1_s), .clk(and_1_out), .clr(clr));  // open: ns

  // Notes on the sheet:
  //   RAM 1x1
endmodule

module RAM_1x16 (
  input  clk,
  input  rw,
  input  [15:0] in_3,
  input  clr,
  input  addr,
  output [15:0] out_6
);

  _02___RAM_1x8 u_02_ram_1x8_1 (.clk(clk), .rw(rw), .clr(clr), .addr(addr), .in(in_3[7:0]), .out(out_6[7:0]));
  _02___RAM_1x8 u_02_ram_1x8_2 (.clk(clk), .rw(rw), .clr(clr), .addr(addr), .in(in_3[15:8]), .out(out_6[15:8]));
  // Probe on in_3
  // Probe on out_6

  // Notes on the sheet:
  //   RAM 1x16
endmodule

module _01___RAM_1x4 (
  input  [3:0] in,
  input  clr,
  input  clk,
  input  rw,
  input  addr,
  output [3:0] out
);

  RAM_1x1 ram_1x1_1 (.rw(rw), .clk(clk), .clr(clr), .addr(addr), .out_6(out[0]), .in(in[0]));
  RAM_1x1 ram_1x1_2 (.rw(rw), .clk(clk), .clr(clr), .addr(addr), .out_6(out[1]), .in(in[1]));
  RAM_1x1 ram_1x1_3 (.rw(rw), .clk(clk), .clr(clr), .addr(addr), .out_6(out[2]), .in(in[2]));
  RAM_1x1 ram_1x1_4 (.rw(rw), .clk(clk), .clr(clr), .addr(addr), .out_6(out[3]), .in(in[3]));

  // Notes on the sheet:
  //   Ram 1x4
endmodule

module _02___RAM_1x8 (
  input  clk,
  input  rw,
  input  [7:0] in,
  input  clr,
  input  addr,
  output [7:0] out
);

  _01___RAM_1x4 u_01_ram_1x4_1 (.in(in[3:0]), .out(out[3:0]), .clr(clr), .clk(clk), .rw(rw), .addr(addr));
  _01___RAM_1x4 u_01_ram_1x4_2 (.in(in[7:4]), .out(out[7:4]), .clr(clr), .clk(clk), .rw(rw), .addr(addr));

  // Notes on the sheet:
  //   RAM 1x8
endmodule

module _03___RAM_2x8 (
  input  clk,
  input  [7:0] in,
  input  rw,
  input  clr,
  input  addr,
  output [7:0] out
);

  wire demultiplexer_1_out0, demultiplexer_1_out1;
  wire [7:0] n02_ram_1x8_1_out, n02_ram_1x8_2_out;

  Demultiplexer #(.enable("false")) demultiplexer_1 (
    .out0(demultiplexer_1_out0), .out1(demultiplexer_1_out1), .in(1'b1), .sel(addr));
  _02___RAM_1x8 u_02_ram_1x8_1 (
    .clk(clk), .rw(rw), .clr(clr), .addr(demultiplexer_1_out0), .in(in), .out(n02_ram_1x8_1_out));
  _02___RAM_1x8 u_02_ram_1x8_2 (
    .clk(clk), .rw(rw), .clr(clr), .addr(demultiplexer_1_out1), .in(in), .out(n02_ram_1x8_2_out));
  // Probe on in
  Multiplexer #(.width(8), .enable("false")) multiplexer_1 (
    .in0(n02_ram_1x8_1_out), .in1(n02_ram_1x8_2_out), .out(out), .sel(addr));
  // Probe on out

  // Notes on the sheet:
  //   RAM 2x8
endmodule

module _04___RAM_4x8 (
  input  clk,
  input  rw,
  input  [7:0] in,
  input  clr,
  input  [1:0] addr,
  output [7:0] out
);

  wire and_1_out, and_2_out, not_1_out;
  wire [7:0] n03_ram_2x8_1_out, n03_ram_2x8_2_out;

  not not_1 (not_1_out, addr[1]);
  and and_1 (and_1_out, rw, not_1_out);
  and and_2 (and_2_out, addr[1], rw);
  _03___RAM_2x8 u_03_ram_2x8_1 (.clk(clk), .rw(and_1_out), .clr(clr), .addr(addr[0]), .in(in), .out(n03_ram_2x8_1_out));
  _03___RAM_2x8 u_03_ram_2x8_2 (.clk(clk), .rw(and_2_out), .clr(clr), .addr(addr[0]), .in(in), .out(n03_ram_2x8_2_out));
  // Probe on in
  Multiplexer #(.width(8), .enable("false")) multiplexer_1 (
    .in0(n03_ram_2x8_1_out), .in1(n03_ram_2x8_2_out), .out(out), .sel(addr[1]));
  // Probe on out

  // Notes on the sheet:
  //   RAM 4x8
endmodule

module _05___RAM_8x8 (
  input  clk,
  input  rw,
  input  [7:0] in,
  input  clr,
  input  [2:0] addr,
  output [7:0] out
);

  wire and_1_out, and_2_out, not_1_out;
  wire [7:0] n04_ram_4x8_1_out, n04_ram_4x8_2_out;

  not not_1 (not_1_out, addr[2]);
  and and_1 (and_1_out, rw, not_1_out);
  and and_2 (and_2_out, addr[2], rw);
  _04___RAM_4x8 u_04_ram_4x8_1 (
    .clk(clk), .rw(and_1_out), .clr(clr), .addr(addr[1:0]), .in(in), .out(n04_ram_4x8_1_out));
  _04___RAM_4x8 u_04_ram_4x8_2 (
    .clk(clk), .rw(and_2_out), .clr(clr), .addr(addr[1:0]), .in(in), .out(n04_ram_4x8_2_out));
  // Probe on in
  Multiplexer #(.width(8), .enable("false")) multiplexer_1 (
    .in0(n04_ram_4x8_1_out), .in1(n04_ram_4x8_2_out), .out(out), .sel(addr[2]));
  // Probe on out

  // Notes on the sheet:
  //   RAM 8x8
endmodule

module _06___RAM_4x16 (
  input  clk,
  input  rw,
  input  [15:0] in,
  input  clr,
  input  [1:0] addr,
  output [15:0] out
);

  _04___RAM_4x8 u_04_ram_4x8_1 (.clk(clk), .rw(rw), .clr(clr), .addr(addr), .in(in[7:0]), .out(out[7:0]));
  _04___RAM_4x8 u_04_ram_4x8_2 (.clk(clk), .rw(rw), .clr(clr), .addr(addr), .in(in[15:8]), .out(out[15:8]));
  // Probe on in
  // Probe on out

  // Notes on the sheet:
  //   RAM 4x16
endmodule

module _07___RAM_8x16 (
  input  clk,
  input  [15:0] in,
  input  rw,
  input  [1:0] addr,
  input  clr,
  output [15:0] out
);

  wire demultiplexer_1_out0, demultiplexer_1_out1, demultiplexer_1_out2, demultiplexer_1_out3;
  wire [15:0] ram_1x16_1_out_6, ram_1x16_2_out_6, ram_1x16_3_out_6, ram_1x16_4_out_6;

  Demultiplexer #(.select(2), .enable("false")) demultiplexer_1 (
    .out0(demultiplexer_1_out0), .out1(demultiplexer_1_out1), .out2(demultiplexer_1_out2),
    .out3(demultiplexer_1_out3), .in(1'b1), .sel(addr));
  RAM_1x16 ram_1x16_1 (.clk(clk), .rw(rw), .clr(clr), .addr(demultiplexer_1_out0), .in_3(in), .out_6(ram_1x16_1_out_6));
  RAM_1x16 ram_1x16_2 (.clk(clk), .rw(rw), .clr(clr), .addr(demultiplexer_1_out1), .in_3(in), .out_6(ram_1x16_2_out_6));
  RAM_1x16 ram_1x16_3 (.clk(clk), .rw(rw), .clr(clr), .addr(demultiplexer_1_out2), .in_3(in), .out_6(ram_1x16_3_out_6));
  RAM_1x16 ram_1x16_4 (.clk(clk), .rw(rw), .clr(clr), .addr(demultiplexer_1_out3), .in_3(in), .out_6(ram_1x16_4_out_6));
  // Probe on in
  Multiplexer #(.select(2), .width(16), .enable("false")) multiplexer_1 (
    .in0(ram_1x16_1_out_6), .in1(ram_1x16_2_out_6), .in2(ram_1x16_3_out_6), .in3(ram_1x16_4_out_6),
    .out(out), .sel(addr));
  // Probe on out

  // Notes on the sheet:
  //   RAM 8x16
endmodule
