// Logisim project Guia11Q01.circ as structural Verilog: 1 circuit, main circuit main
module main (
  input  in_1,
  output out_2
);

  wire _00_q, _01_q, _01_qn, _10_qn, _11_q, _11_qn, clock_1_out;

  Clock clock_1 (.out(clock_1_out));
  D_Flip_Flop _00 (.clk(clock_1_out), .D(in_1), .Q(_00_q), .preset(_01_qn), .reset(_10_qn));  // open: Qn, en
  D_Flip_Flop _01 (.clk(clock_1_out), .D(_00_q), .Q(_01_q), .Qn(_01_qn));  // open: preset, en, reset
  D_Flip_Flop _11 (.clk(clock_1_out), .D(_01_q), .Q(_11_q), .Qn(_11_qn), .reset(_11_q));  // open: preset, en
  D_Flip_Flop _10 (.clk(clock_1_out), .D(_11_qn), .Q(out_2), .Qn(_10_qn));  // open: preset, en, reset
endmodule
