// Logisim project Guia11Q02.circ as structural Verilog: 1 circuit, main circuit main
module main (
  input  in_1,
  output out_2
);

  wire _000_q, _001_q, _001_qn, _010_q, _010_qn, _011_qn, clock_1_out;

  Clock clock_1 (.out(clock_1_out));
  D_Flip_Flop _000 (.clk(clock_1_out), .D(in_1), .Q(_000_q), .preset(_001_qn));  // open: Qn, en, reset
  D_Flip_Flop _001 (.clk(clock_1_out), .D(_000_q), .Q(_001_q), .Qn(_001_qn));  // open: preset, en, reset
  D_Flip_Flop _011 (.clk(clock_1_out), .D(_001_q), .Qn(_011_qn), .reset(out_2));  // open: Q, preset, en
  D_Flip_Flop _010 (.clk(clock_1_out), .D(_011_qn), .Q(_010_q), .Qn(_010_qn));  // open: preset, en, reset
  D_Flip_Flop _110 (.clk(clock_1_out), .D(_010_q), .Q(out_2), .Qn(_010_qn));  // open: preset, en, reset
endmodule
