// Logisim project Guia_0503.circ as structural Verilog: 1 circuit, main circuit main
module main (
  input  a,
  input  in_2,
  output s
);

  wire nor_1_out, nor_2_out, nor_3_out;

  nor nor_1 (nor_1_out, a, a);
  nor nor_2 (nor_2_out, nor_1_out, in_2);
  nor nor_3 (nor_3_out, nor_2_out, nor_2_out);
  nor nor_4 (s, nor_3_out, nor_3_out);

  // Notes on the sheet:
  //   b
  //   ~a
  //   (~a | b)
  //   ~(~a | b)
endmodule
