// Logisim project Guia_0504.circ as structural Verilog: 1 circuit, main circuit main
module main (
  input  a,
  input  in_2,
  output s
);

  wire nand_1_out, nand_2_out, nand_3_out;

  nand nand_1 (nand_1_out, a, a);
  nand nand_2 (nand_2_out, nand_1_out, in_2);
  nand nand_3 (nand_3_out, nand_2_out, nand_2_out);
  nand nand_4 (s, nand_3_out, nand_3_out);

  // Notes on the sheet:
  //   b
  //   ~a
  //   (~a & b)
  //   ~(~a & b)
endmodule
