// Logisim project Guia_0508.circ as structural Verilog: 1 circuit, main circuit main
module main (
  input  a,
  input  in_2,
  output s
);

  wire nand_1_out, nand_2_out, nand_3_out, nand_4_out, nand_5_out;

  nand nand_1 (nand_1_out, a, a);
  nand nand_2 (nand_2_out, in_2, in_2);
  nand nand_3 (nand_3_out, nand_1_out, nand_1_out);
  nand nand_4 (nand_4_out, nand_2_out, nand_2_out);
  nand nand_5 (nand_5_out, nand_3_out, nand_4_out);
  nand nand_6 (s, nand_5_out, nand_5_out);

  // Notes on the sheet:
  //   b
  //   (~a)
  //   (~b)
  //   (~a | ~b)
  //   ~(~a | ~b)
endmodule
