// Logisim project Questao_1201.circ as structural Verilog: 1 circuit, main circuit main
module main (
  input  in_1,
  input  in_2,
  input  in_3,
  input  in_4,
  output out_5,
  output out_6,
  output out_7,
  output out_8
);

  wire and_1_out, clock_1_out, j_k_ff_1_q, j_k_ff_2_q, j_k_ff_3_q, j_k_ff_4_q, not_1_out, not_2_out,
       not_3_out, not_4_out;

  Clock clock_1 (.out(clock_1_out));
  not not_1 (not_1_out, in_3);
  not not_2 (not_2_out, in_3);
  and and_1 (and_1_out, in_1, in_2, clock_1_out);
  not not_3 (not_3_out, in_3);
  not not_4 (not_4_out, in_3);
  J_K_Flip_Flop j_k_ff_1 (.J(in_3), .clk(and_1_out), .K(not_1_out), .Q(j_k_ff_1_q), .reset(in_4));  // open: Qn, preset
  J_K_Flip_Flop j_k_ff_2 (.clk(and_1_out), .K(not_2_out), .Q(j_k_ff_2_q), .reset(in_4));  // open: J, Qn, preset
  J_K_Flip_Flop j_k_ff_3 (.clk(and_1_out), .K(not_3_out), .Q(j_k_ff_3_q), .reset(in_4));  // open: J, Qn, preset
  J_K_Flip_Flop j_k_ff_4 (.clk(and_1_out), .K(not_4_out), .Q(j_k_ff_4_q), .reset(in_4));  // open: J, Qn, preset
  and and_2 (out_5, j_k_ff_1_q, in_1);
  and and_3 (out_6, j_k_ff_2_q, in_1);
  and and_4 (out_7, j_k_ff_3_q, in_1);
  and and_5 (out_8, j_k_ff_4_q, in_1);
endmodule
