// Logisim project Guia13_01.circ as structural Verilog: 1 circuit, main circuit main
module main (
  input  load,
  input  clr,
  output out_3,
  output out_4,
  output out_5,
  output out_6
);

  wire clock_1_out;

  Clock clock_1 (.out(clock_1_out));
  J_K_Flip_Flop #(.Pre_Clr_Positions("LEGACY"), .enable("true"), .NewFFLayout("false")) j_k_ff_1 (
    .J(load), .clk(out_4), .K(load), .Q(out_3), .reset(clr));  // open: Qn, preset, en
  J_K_Flip_Flop #(.Pre_Clr_Positions("LEGACY"), .enable("true"), .NewFFLayout("false")) j_k_ff_2 (
    .J(load), .clk(out_5), .K(load), .Q(out_4), .reset(clr));  // open: Qn, preset, en
  J_K_Flip_Flop #(.Pre_Clr_Positions("LEGACY"), .enable("true"), .NewFFLayout("false")) j_k_ff_3 (
    .J(load), .clk(out_6), .K(load), .Q(out_5), .reset(clr));  // open: Qn, preset, en
  J_K_Flip_Flop #(.Pre_Clr_Positions("LEGACY"), .enable("true"), .NewFFLayout("false")) j_k_ff_4 (
    .J(load), .clk(clock_1_out), .K(load), .Q(out_6), .reset(clr));  // open: Qn, preset, en
endmodule
