// Logisim project Guia13_03.circ as structural Verilog: 1 circuit, main circuit main
module main (
  input  load,
  output a,
  output b,
  output c,
  output d
);

  wire and_1_out, clock_1_out, j_k_ff_1_qn, j_k_ff_2_qn, j_k_ff_3_qn, j_k_ff_4_qn, not_1_out, not_2_out,
       not_3_out, or_1_out;

  Clock clock_1 (.out(clock_1_out));
  not not_1 (not_1_out, load);
  or or_1 (or_1_out, not_1_out, and_1_out);
  not not_2 (not_2_out, j_k_ff_1_qn);
  and and_1 (and_1_out, not_2_out, j_k_ff_2_qn, not_3_out, j_k_ff_4_qn);
  not not_3 (not_3_out, j_k_ff_3_qn);
  J_K_Flip_Flop #(.Pre_Clr_Positions("LEGACY"), .enable("true"), .NewFFLayout("false")) j_k_ff_1 (
    .J(load), .clk(clock_1_out), .K(load), .Q(d), .Qn(j_k_ff_1_qn), .preset(or_1_out));  // open: en, reset
  J_K_Flip_Flop #(.Pre_Clr_Positions("LEGACY"), .enable("true"), .NewFFLayout("false")) j_k_ff_2 (
    .J(load), .clk(d), .K(load), .Q(c), .Qn(j_k_ff_2_qn), .preset(or_1_out));  // open: en, reset
  J_K_Flip_Flop #(.Pre_Clr_Positions("LEGACY"), .enable("true"), .NewFFLayout("false")) j_k_ff_3 (
    .J(load), .clk(c), .K(load), .Q(b), .Qn(j_k_ff_3_qn), .preset(or_1_out));  // open: en, reset
  J_K_Flip_Flop #(.Pre_Clr_Positions("LEGACY"), .enable("true"), .NewFFLayout("false")) j_k_ff_4 (
    .J(load), .clk(b), .K(load), .Q(a), .Qn(j_k_ff_4_qn), .preset(or_1_out));  // open: en, reset
endmodule
