// Logisim project Guia13_05.circ as structural Verilog: 1 circuit, main circuit main
module main (
  input  clr,
  output out_2,
  output out_3,
  output out_4
);

  wire and_1_out, clock_1_out, not_1_out, or_1_out, t_ff_2_qn, t_ff_3_qn;

  Clock clock_1 (.out(clock_1_out));
  or or_1 (or_1_out, clr, and_1_out);
  and and_1 (and_1_out, out_2, not_1_out, out_4);
  T_Flip_Flop #(.Pre_Clr_Positions("LEGACY"), .enable("true"), .NewFFLayout("false")) t_ff_1 (
    .clk(t_ff_2_qn), .T(t_ff_2_qn), .Q(out_2), .reset(or_1_out));  // open: Qn, preset, en
  not not_1 (not_1_out, out_3);
  T_Flip_Flop #(.Pre_Clr_Positions("LEGACY"), .enable("true"), .NewFFLayout("false")) t_ff_2 (
    .clk(t_ff_3_qn), .T(t_ff_3_qn), .Q(out_3), .Qn(t_ff_2_qn), .reset(or_1_out));  // open: preset, en
  T_Flip_Flop #(.Pre_Clr_Positions("LEGACY"), .enable("true"), .NewFFLayout("false")) t_ff_3 (
    .clk(clock_1_out), .T(clock_1_out), .Q(out_4), .Qn(t_ff_3_qn), .reset(or_1_out));  // open: preset, en
endmodule
