// Logisim project Guia1301.circ as structural Verilog: 1 circuit, main circuit main
module main (
  input  in_1
);

  wire clock_1_out, j_k_ff_1_q, j_k_ff_2_q, j_k_ff_3_q, j_k_ff_4_q;

  J_K_Flip_Flop j_k_ff_1 (.J(in_1), .clk(clock_1_out), .Q(j_k_ff_1_q));  // open: K, Qn, preset, en, reset
  Clock clock_1 (.out(clock_1_out));
  J_K_Flip_Flop j_k_ff_2 (.J(in_1), .clk(j_k_ff_1_q), .Q(j_k_ff_2_q));  // open: K, Qn, preset, en, reset
  J_K_Flip_Flop j_k_ff_3 (.J(in_1), .clk(j_k_ff_2_q), .Q(j_k_ff_3_q));  // open: K, Qn, preset, en, reset
  J_K_Flip_Flop j_k_ff_4 (.J(in_1), .clk(j_k_ff_3_q), .Q(j_k_ff_4_q));  // open: K, Qn, preset, en, reset
  J_K_Flip_Flop j_k_ff_5 (.J(in_1), .clk(j_k_ff_4_q));  // open: K, Q, Qn, preset, en, reset
endmodule
