// Logisim project Guia1302.circ as structural Verilog: 1 circuit, main circuit main
module main (
  input  in_1
);

  wire j_k_ff_1_qn, j_k_ff_2_qn, j_k_ff_3_qn, j_k_ff_4_qn;

  J_K_Flip_Flop j_k_ff_1 (.J(in_1), .Qn(j_k_ff_1_qn));  // open: clk, K, Q, preset, en, reset
  J_K_Flip_Flop j_k_ff_2 (.J(in_1), .clk(j_k_ff_1_qn), .Qn(j_k_ff_2_qn));  // open: K, Q, preset, en, reset
  J_K_Flip_Flop j_k_ff_3 (.J(in_1), .clk(j_k_ff_2_qn), .Qn(j_k_ff_3_qn));  // open: K, Q, preset, en, reset
  J_K_Flip_Flop j_k_ff_4 (.J(in_1), .clk(j_k_ff_3_qn), .Qn(j_k_ff_4_qn));  // open: K, Q, preset, en, reset
  J_K_Flip_Flop j_k_ff_5 (.J(in_1), .clk(j_k_ff_4_qn));  // open: K, Q, Qn, preset, en, reset
endmodule
