// Logisim project Guia1304.circ as structural Verilog: 1 circuit, main circuit main
module main (
  input  in_1
);

  wire and_1_out, clock_1_out, j_k_ff_1_q, j_k_ff_2_q, j_k_ff_2_qn, j_k_ff_3_qn, j_k_ff_4_q;

  J_K_Flip_Flop j_k_ff_1 (.J(in_1), .clk(j_k_ff_4_q), .Q(j_k_ff_1_q), .reset(and_1_out));  // open: K, Qn, preset, en
  J_K_Flip_Flop j_k_ff_2 (
    .J(in_1), .clk(j_k_ff_1_q), .Q(j_k_ff_2_q), .Qn(j_k_ff_2_qn), .reset(and_1_out));  // open: K, preset, en
  and and_1 (and_1_out, j_k_ff_1_q, j_k_ff_2_qn, j_k_ff_3_qn, j_k_ff_4_q);
  J_K_Flip_Flop j_k_ff_3 (.J(in_1), .clk(j_k_ff_2_q), .Qn(j_k_ff_3_qn), .reset(and_1_out));  // open: K, Q, preset, en
  J_K_Flip_Flop j_k_ff_4 (.J(in_1), .clk(clock_1_out), .Q(j_k_ff_4_q), .reset(and_1_out));  // open: K, Qn, preset, en
  Clock clock_1 (.out(clock_1_out));
endmodule
