// Logisim project g1301.circ as structural Verilog: 1 circuit, main circuit main
module main (
  input  in_1,
  input  in_2,
  input  CLR
);

  wire j_k_ff_1_qn, j_k_ff_2_qn, j_k_ff_3_qn, j_k_ff_4_qn, j_k_ff_5_qn;

  // Probe on j_k_ff_1_qn
  J_K_Flip_Flop j_k_ff_1 (.J(in_2), .clk(j_k_ff_2_qn), .K(in_2), .Qn(j_k_ff_1_qn), .reset(CLR));  // open: Q, preset
  // Probe on j_k_ff_2_qn
  J_K_Flip_Flop j_k_ff_2 (.J(in_2), .clk(j_k_ff_3_qn), .K(in_2), .Qn(j_k_ff_2_qn), .reset(CLR));  // open: Q, preset
  // Probe on j_k_ff_3_qn
  J_K_Flip_Flop j_k_ff_3 (.J(in_2), .clk(j_k_ff_4_qn), .K(in_2), .Qn(j_k_ff_3_qn), .reset(CLR));  // open: Q, preset
  // Probe on j_k_ff_4_qn
  J_K_Flip_Flop j_k_ff_4 (.J(in_2), .clk(j_k_ff_5_qn), .K(in_2), .Qn(j_k_ff_4_qn), .reset(CLR));  // open: Q, preset
  // Probe on j_k_ff_5_qn
  J_K_Flip_Flop j_k_ff_5 (.J(in_2), .clk(in_1), .K(in_2), .Qn(j_k_ff_5_qn), .reset(CLR));  // open: Q, preset
endmodule
