// Logisim project g1303.circ as structural Verilog: 1 circuit, main circuit main
module main (
  input  X1,
  input  pulse,
  input  CLR
);

  wire and_1_out, j_k_ff_1_q, j_k_ff_1_qn, j_k_ff_2_q, j_k_ff_2_qn, j_k_ff_3_q, j_k_ff_3_qn, not_1_out,
       not_2_out, or_1_out;

  or or_1 (or_1_out, CLR, and_1_out);
  not not_1 (not_1_out, j_k_ff_1_q);
  and and_1 (and_1_out, not_1_out, not_2_out);
  // Probe on j_k_ff_3_q
  J_K_Flip_Flop j_k_ff_1 (
    .J(X1), .clk(pulse), .K(X1), .Q(j_k_ff_1_q), .Qn(j_k_ff_1_qn), .reset(or_1_out));  // open: preset
  not not_2 (not_2_out, j_k_ff_2_q);
  // Probe on j_k_ff_3_q
  J_K_Flip_Flop j_k_ff_2 (
    .J(X1), .clk(j_k_ff_1_qn), .K(X1), .Q(j_k_ff_2_q), .Qn(j_k_ff_2_qn), .reset(or_1_out));  // open: preset
  // Probe on j_k_ff_2_q
  J_K_Flip_Flop j_k_ff_3 (
    .J(X1), .clk(j_k_ff_2_qn), .K(X1), .Q(j_k_ff_3_q), .Qn(j_k_ff_3_qn), .reset(or_1_out));  // open: preset
  // Probe on j_k_ff_1_q
  J_K_Flip_Flop j_k_ff_4 (.J(X1), .clk(j_k_ff_3_qn), .K(X1), .Q(j_k_ff_3_q), .reset(or_1_out));  // open: Qn, preset
endmodule
