// Logisim project Guia13.circ as structural Verilog: 5 circuits, main circuit Q1
module Q1 (
  input  in_1,
  input  in_2,
  output out_3,
  output out_4,
  output out_5,
  output out_6,
  output out_7
);

  wire clock_1_out;

  Clock clock_1 (.out(clock_1_out));
  J_K_Flip_Flop j_k_ff_1 (.J(in_1), .clk(clock_1_out), .K(in_1), .Q(out_7), .reset(in_2));  // open: Qn, preset
  J_K_Flip_Flop j_k_ff_2 (.J(in_1), .clk(out_7), .K(in_1), .Q(out_6), .reset(in_2));  // open: Qn, preset
  J_K_Flip_Flop j_k_ff_3 (.J(in_1), .clk(out_6), .K(in_1), .Q(out_5), .reset(in_2));  // open: Qn, preset
  J_K_Flip_Flop j_k_ff_4 (.J(in_1), .clk(out_5), .K(in_1), .Q(out_4), .reset(in_2));  // open: Qn, preset
  J_K_Flip_Flop j_k_ff_5 (.J(in_1), .clk(out_4), .K(in_1), .Q(out_3), .reset(in_2));  // open: Qn, preset
endmodule

module Q2 (
  input  in_1,
  output out_2,
  output out_3,
  output out_4,
  output out_5,
  output out_6
);

  wire clock_1_out, j_k_ff_1_qn, j_k_ff_2_qn, j_k_ff_3_qn, j_k_ff_4_qn;

  Clock clock_1 (.out(clock_1_out));
  J_K_Flip_Flop j_k_ff_1 (
    .J(clock_1_out), .clk(clock_1_out), .K(clock_1_out), .Q(out_6), .Qn(j_k_ff_1_qn), .reset(in_1));  // open: preset
  J_K_Flip_Flop j_k_ff_2 (
    .J(j_k_ff_1_qn), .clk(j_k_ff_1_qn), .K(j_k_ff_1_qn), .Q(out_5), .Qn(j_k_ff_2_qn), .reset(in_1));  // open: preset
  J_K_Flip_Flop j_k_ff_3 (
    .J(j_k_ff_2_qn), .clk(j_k_ff_2_qn), .K(j_k_ff_2_qn), .Q(out_4), .Qn(j_k_ff_3_qn), .reset(in_1));  // open: preset
  J_K_Flip_Flop j_k_ff_4 (
    .J(j_k_ff_3_qn), .clk(j_k_ff_3_qn), .K(j_k_ff_3_qn), .Q(out_3), .Qn(j_k_ff_4_qn), .reset(in_1));  // open: preset
  J_K_Flip_Flop j_k_ff_5 (
    .J(j_k_ff_4_qn), .clk(j_k_ff_4_qn), .K(j_k_ff_4_qn), .Q(out_2), .reset(in_1));  // open: Qn, preset
endmodule

module Q3 (
  input  in_1,
  output out_2,
  output out_3,
  output out_4,
  output out_5
);

  wire and_1_out, clock_1_out, j_k_ff_1_qn, j_k_ff_2_qn, j_k_ff_3_qn, or_1_out;

  Clock clock_1 (.out(clock_1_out));
  or or_1 (or_1_out, and_1_out, in_1);
  J_K_Flip_Flop j_k_ff_1 (
    .J(clock_1_out), .clk(clock_1_out), .K(clock_1_out), .Q(out_5), .Qn(j_k_ff_1_qn), .reset(or_1_out));  // open: preset
  and and_1 (and_1_out, out_5, out_4, out_2);
  J_K_Flip_Flop j_k_ff_2 (
    .J(j_k_ff_1_qn), .clk(j_k_ff_1_qn), .K(j_k_ff_1_qn), .Q(out_4), .Qn(j_k_ff_2_qn), .reset(or_1_out));  // open: preset
  J_K_Flip_Flop j_k_ff_3 (
    .J(j_k_ff_2_qn), .clk(j_k_ff_2_qn), .K(j_k_ff_2_qn), .Q(out_3), .Qn(j_k_ff_3_qn), .reset(or_1_out));  // open: preset
  J_K_Flip_Flop j_k_ff_4 (
    .J(j_k_ff_3_qn), .clk(j_k_ff_3_qn), .K(j_k_ff_3_qn), .Q(out_2), .reset(or_1_out));  // open: Qn, preset
endmodule

module Q4 (
  input  in_1,
  input  in_2,
  output out_3,
  output out_4,
  output out_5,
  output out_6
);

  wire and_1_out, clock_1_out, not_1_out, not_2_out, or_1_out;

  Clock clock_1 (.out(clock_1_out));
  or or_1 (or_1_out, and_1_out, in_2);
  J_K_Flip_Flop j_k_ff_1 (.J(in_1), .clk(clock_1_out), .K(in_1), .Q(out_6), .reset(or_1_out));  // open: Qn, preset
  not not_1 (not_1_out, out_5);
  and and_1 (and_1_out, out_6, not_1_out, not_2_out, out_3);
  not not_2 (not_2_out, out_4);
  J_K_Flip_Flop j_k_ff_2 (.J(in_1), .clk(out_6), .K(in_1), .Q(out_5), .reset(or_1_out));  // open: Qn, preset
  J_K_Flip_Flop j_k_ff_3 (.J(in_1), .clk(out_5), .K(in_1), .Q(out_4), .reset(or_1_out));  // open: Qn, preset
  J_K_Flip_Flop j_k_ff_4 (.J(in_1), .clk(out_4), .K(in_1), .Q(out_3), .reset(or_1_out));  // open: Qn, preset
endmodule

module Q5 (
  input  in_1,
  output out_2,
  output out_3,
  output out_4
);

  wire and_1_out, and_2_out, and_3_out, and_4_out, clock_1_out, not_1_out, not_2_out, not_3_out, or_1_out,
       t_ff_4_q;

  Clock clock_1 (.out(clock_1_out));
  T_Flip_Flop t_ff_1 (.clk(clock_1_out), .T(in_1), .Q(out_4));  // open: Qn, preset, reset
  and and_1 (and_1_out, out_4, not_1_out, out_4);
  not not_1 (not_1_out, out_2);
  and and_2 (and_2_out, out_2, not_2_out, out_4);
  not not_2 (not_2_out, out_3);
  or or_1 (or_1_out, and_1_out, and_2_out);
  T_Flip_Flop t_ff_2 (.clk(clock_1_out), .T(or_1_out), .Q(out_3), .reset(t_ff_4_q));  // open: Qn, preset
  and and_3 (and_3_out, out_3, out_4, out_3);
  T_Flip_Flop t_ff_3 (.clk(clock_1_out), .T(and_3_out), .Q(out_2));  // open: Qn, preset, reset
  and and_4 (and_4_out, out_4, out_3, out_2);
  not not_3 (not_3_out, and_4_out);
  T_Flip_Flop t_ff_4 (.clk(clock_1_out), .T(and_4_out), .Q(t_ff_4_q), .reset(not_3_out));  // open: Qn, preset
endmodule
