// Logisim project Guia_1307.circ as structural Verilog: 1 circuit, main circuit main
module Contador_Anel_Torcido_5_bits (
  input  Clear,
  input  Clock
);

  wire j_k_ff_1_p2, j_k_ff_3_p1, j_k_ff_4_p1, j_k_ff_5_p1;

  // J_K_Flip_Flop j_k_ff_1: pin names not known; wires that end beside it: Clear, j_k_ff_1_p2
  // J_K_Flip_Flop j_k_ff_2: pin names not known; wires that end beside it: j_k_ff_1_p2
  // J_K_Flip_Flop j_k_ff_3: pin names not known; wires that end beside it: j_k_ff_3_p1
  // J_K_Flip_Flop j_k_ff_4: pin names not known; wires that end beside it: j_k_ff_4_p1
  // J_K_Flip_Flop j_k_ff_5: pin names not known; wires that end beside it: j_k_ff_5_p1
endmodule
