// Logisim project Guia08.circ as structural Verilog: 1 circuit, main circuit main
module main (
  input  x,
  input  y,
  input  cin,
  input  in_4,
  input  in_5,
  input  in_6,
  input  in_7,
  input  in_8,
  input  x_2,
  input  y_2,
  input  in_11,
  input  in_12,
  input  in_13,
  input  in_14,
  input  in_15,
  output SUM,
  output CARRY,
  output SUM_2,
  output CARRY_2,
  output out_20,
  output out_21,
  output out_22,
  output out_23,
  output out_24
);

  wire adder_2_cout, adder_3_cout, adder_4_cout, adder_5_cout, and_1_out, and_2_out, and_3_out, xor_1_out;

  xor xor_1 (xor_1_out, x, y);
  and and_1 (and_1_out, x, y);
  and and_2 (and_2_out, x, cin);
  and and_3 (and_3_out, y, cin);
  xor xor_2 (SUM_2, x_2, y_2);
  and and_4 (CARRY_2, x_2, y_2);
  xor xor_3 (SUM, xor_1_out, cin);
  or or_1 (CARRY, and_1_out, and_2_out, and_3_out);
  Adder #(.width(1)) adder_1 (.a(in_11), .b(in_4), .out(out_20), .cin(adder_2_cout));  // open: cout
  Adder #(.width(1)) adder_2 (.a(in_12), .b(in_5), .out(out_21), .cin(adder_3_cout), .cout(adder_2_cout));
  Adder #(.width(1)) adder_3 (.a(in_13), .b(in_6), .out(out_22), .cin(adder_4_cout), .cout(adder_3_cout));
  Adder #(.width(1)) adder_4 (.a(in_14), .b(in_7), .out(out_23), .cin(adder_5_cout), .cout(adder_4_cout));
  Adder #(.width(1)) adder_5 (.a(in_15), .b(in_8), .out(out_24), .cout(adder_5_cout));  // open: cin

  // Notes on the sheet:
  //   FULL-ADDER
  //   HALF ADDER
  //   Cout conecta no Cin do próximo adder
  //   5-BIT ADDER
endmodule
