// Logisim project Questao_1304.circ as structural Verilog: 1 circuit, main circuit main
module main (
  input  in_1,
  input  in_2
);

  wire and_1_out, j_k_ff_1_q, j_k_ff_1_qn, j_k_ff_2_q, j_k_ff_3_q, j_k_ff_3_qn, j_k_ff_4_q, not_1_out,
       not_2_out, not_3_out, or_1_out;

  not not_1 (not_1_out, in_1);
  or or_1 (or_1_out, not_1_out, and_1_out);
  not not_2 (not_2_out, j_k_ff_1_qn);
  and and_1 (and_1_out, not_2_out, not_3_out);
  not not_3 (not_3_out, j_k_ff_3_qn);
  J_K_Flip_Flop j_k_ff_1 (
    .J(in_1), .clk(in_2), .K(in_1), .Q(j_k_ff_1_q), .Qn(j_k_ff_1_qn), .reset(or_1_out));  // open: preset
  J_K_Flip_Flop j_k_ff_2 (.J(in_1), .clk(j_k_ff_1_q), .K(in_1), .Q(j_k_ff_2_q), .reset(or_1_out));  // open: Qn, preset
  J_K_Flip_Flop j_k_ff_3 (
    .J(in_1), .clk(j_k_ff_2_q), .K(in_1), .Q(j_k_ff_3_q), .Qn(j_k_ff_3_qn), .reset(or_1_out));  // open: preset
  J_K_Flip_Flop j_k_ff_4 (.J(in_1), .clk(j_k_ff_3_q), .K(in_1), .Q(j_k_ff_4_q));  // open: Qn, preset, reset
  // Probe on j_k_ff_1_q
  // Probe on j_k_ff_2_q
  // Probe on j_k_ff_3_q
  // Probe on j_k_ff_4_q
endmodule
