// Logisim project Questao_1305.circ as structural Verilog: 1 circuit, main circuit main
module main (
  input  in_1,
  input  in_2,
  input  in_3
);

  wire and_1_out, and_2_out, and_3_out, and_4_out, and_5_out, and_6_out, not_1_out, t_ff_1_q, t_ff_1_qn,
       t_ff_2_q, t_ff_2_qn, t_ff_3_q, t_ff_3_qn, t_ff_4_q, t_ff_4_qn, t_ff_5_q, t_ff_5_qn, t_ff_6_q,
       t_ff_6_qn, t_ff_7_q;

  T_Flip_Flop t_ff_1 (.clk(in_1), .T(in_2), .Q(t_ff_1_q), .Qn(t_ff_1_qn), .reset(in_3));  // open: preset
  T_Flip_Flop t_ff_2 (.clk(in_1), .T(and_1_out), .Q(t_ff_2_q), .Qn(t_ff_2_qn), .reset(in_3));  // open: preset
  T_Flip_Flop t_ff_3 (.clk(in_1), .T(and_2_out), .Q(t_ff_3_q), .Qn(t_ff_3_qn), .reset(in_3));  // open: preset
  T_Flip_Flop t_ff_4 (.clk(in_1), .T(and_3_out), .Q(t_ff_4_q), .Qn(t_ff_4_qn), .reset(in_3));  // open: preset
  T_Flip_Flop t_ff_5 (.clk(in_1), .T(and_4_out), .Q(t_ff_5_q), .Qn(t_ff_5_qn), .reset(in_3));  // open: preset
  T_Flip_Flop t_ff_6 (.clk(in_1), .T(and_5_out), .Q(t_ff_6_q), .Qn(t_ff_6_qn), .reset(in_3));  // open: preset
  T_Flip_Flop t_ff_7 (.clk(in_1), .T(and_6_out), .Q(t_ff_7_q), .reset(in_3));  // open: Qn, preset
  // Probe on t_ff_1_q
  and and_1 (and_1_out, t_ff_1_qn, not_1_out);
  // Probe on t_ff_2_q
  and and_2 (and_2_out, t_ff_2_qn, not_1_out);
  // Probe on t_ff_3_q
  and and_3 (and_3_out, t_ff_3_qn, not_1_out);
  // Probe on t_ff_4_q
  and and_4 (and_4_out, t_ff_4_qn, not_1_out);
  // Probe on t_ff_5_q
  and and_5 (and_5_out, t_ff_5_qn, not_1_out);
  // Probe on t_ff_6_q
  and and_6 (and_6_out, t_ff_6_qn, not_1_out);
  // Probe on t_ff_7_q
  not not_1 (not_1_out, in_3);
endmodule
