// Logisim project g1302.circ as structural Verilog: 1 circuit, main circuit main
module main (
  input  PULSE,
  input  X1,
  input  CLR
);

  wire j_k_ff_1_qn, j_k_ff_2_q, j_k_ff_2_qn, j_k_ff_3_q, j_k_ff_3_qn, j_k_ff_4_q, j_k_ff_4_qn, j_k_ff_5_q,
       j_k_ff_5_qn;

  // Probe on j_k_ff_1_qn
  J_K_Flip_Flop j_k_ff_1 (.J(X1), .clk(j_k_ff_2_q), .K(X1), .Qn(j_k_ff_1_qn), .reset(CLR));  // open: Q, preset
  // Probe on j_k_ff_2_qn
  J_K_Flip_Flop j_k_ff_2 (
    .J(X1), .clk(j_k_ff_3_q), .K(X1), .Q(j_k_ff_2_q), .Qn(j_k_ff_2_qn), .reset(CLR));  // open: preset
  // Probe on j_k_ff_3_qn
  J_K_Flip_Flop j_k_ff_3 (
    .J(X1), .clk(j_k_ff_4_q), .K(X1), .Q(j_k_ff_3_q), .Qn(j_k_ff_3_qn), .reset(CLR));  // open: preset
  // Probe on j_k_ff_4_qn
  J_K_Flip_Flop j_k_ff_4 (
    .J(X1), .clk(j_k_ff_5_q), .K(X1), .Q(j_k_ff_4_q), .Qn(j_k_ff_4_qn), .reset(CLR));  // open: preset
  // Probe on j_k_ff_5_qn
  J_K_Flip_Flop j_k_ff_5 (.J(X1), .clk(PULSE), .K(X1), .Q(j_k_ff_5_q), .Qn(j_k_ff_5_qn), .reset(CLR));  // open: preset
endmodule
