// Logisim project Guia_1402.circ as structural Verilog: 1 circuit, main circuit main
module main (
  input  in_1,
  input  in_2,
  input  in_3,
  input  in_4,
  input  in_5,
  input  in_6,
  input  in_7
);

  wire clock_1_out, d_ff_1_q, d_ff_2_q, d_ff_3_q, d_ff_4_q, d_ff_5_q, d_ff_6_q, multiplexer_1_out,
       multiplexer_2_out, multiplexer_3_out, multiplexer_4_out, multiplexer_5_out, multiplexer_6_out;

  Clock clock_1 (.out(clock_1_out));
  Multiplexer #(.enable("false")) multiplexer_1 (.in0(in_1), .in1(d_ff_6_q), .out(multiplexer_1_out), .sel(in_7));
  Multiplexer #(.enable("false")) multiplexer_2 (.in0(in_2), .in1(d_ff_1_q), .out(multiplexer_2_out), .sel(in_7));
  D_Flip_Flop d_ff_1 (.clk(clock_1_out), .D(multiplexer_1_out), .Q(d_ff_1_q));  // open: Qn, preset, reset
  Multiplexer #(.enable("false")) multiplexer_3 (.in0(in_3), .in1(d_ff_2_q), .out(multiplexer_3_out), .sel(in_7));
  D_Flip_Flop d_ff_2 (.clk(clock_1_out), .D(multiplexer_2_out), .Q(d_ff_2_q));  // open: Qn, preset, reset
  Multiplexer #(.enable("false")) multiplexer_4 (.in0(in_4), .in1(d_ff_3_q), .out(multiplexer_4_out), .sel(in_7));
  Multiplexer #(.enable("false")) multiplexer_5 (.in0(in_5), .in1(d_ff_4_q), .out(multiplexer_5_out), .sel(in_7));
  D_Flip_Flop d_ff_3 (.clk(clock_1_out), .D(multiplexer_3_out), .Q(d_ff_3_q));  // open: Qn, preset, reset
  Multiplexer #(.enable("false")) multiplexer_6 (.in0(in_6), .in1(d_ff_5_q), .out(multiplexer_6_out), .sel(in_7));
  D_Flip_Flop d_ff_4 (.clk(clock_1_out), .D(multiplexer_4_out), .Q(d_ff_4_q));  // open: Qn, preset, reset
  D_Flip_Flop d_ff_5 (.clk(clock_1_out), .D(multiplexer_5_out), .Q(d_ff_5_q));  // open: Qn, preset, reset
  D_Flip_Flop d_ff_6 (.clk(clock_1_out), .D(multiplexer_6_out), .Q(d_ff_6_q));  // open: Qn, preset, reset
endmodule
