// Logisim project Guia_14.circ as structural Verilog
module SR_LEFT_6_bits_FIRST_PRESET (
  input  Input,
  input  Clear
);

  wire Clock_out, d_ff_1_q, d_ff_2_q, d_ff_3_q, d_ff_4_q, d_ff_5_q;

  Clock Clock (.out(Clock_out));
  // Probe on d_ff_1_q
  D_Flip_Flop d_ff_1 (.clk(Clock_out), .D(d_ff_2_q), .Q(d_ff_1_q), .reset(Clear));  // open: Qn, preset
  // Probe on d_ff_2_q
  D_Flip_Flop d_ff_2 (.clk(Clock_out), .D(d_ff_3_q), .Q(d_ff_2_q), .reset(Clear));  // open: Qn, preset
  // Probe on d_ff_3_q
  D_Flip_Flop d_ff_3 (.clk(Clock_out), .D(d_ff_4_q), .Q(d_ff_3_q), .reset(Clear));  // open: Qn, preset
  // Probe on d_ff_4_q
  D_Flip_Flop d_ff_4 (.clk(Clock_out), .D(d_ff_5_q), .Q(d_ff_4_q), .reset(Clear));  // open: Qn, preset
  // Probe on d_ff_5_q
  D_Flip_Flop d_ff_5 (.clk(Clock_out), .D(Clock_out), .Q(d_ff_5_q), .preset(Clear));  // open: Qn, reset
  // Probe on Clock_out
  D_Flip_Flop d_ff_6 (.clk(Clock_out), .D(Input), .Q(Clock_out), .preset(Clear), .reset(Clear));  // open: Qn

  // Notes on the sheet:
  //   Registrador de Deslocamento para a Esquerda de 6 bits com Load no Primeiro
endmodule

module SR_LEFT_6_bits_ALL_PRESET (
  input  Input,
  input  Clear
);

  wire Clock_out, d_ff_1_q, d_ff_2_q, d_ff_3_q, d_ff_4_q, d_ff_5_q, d_ff_6_q;

  Clock Clock (.out(Clock_out));
  // Probe on d_ff_1_q
  D_Flip_Flop d_ff_1 (.clk(Clock_out), .D(d_ff_2_q), .Q(d_ff_1_q), .preset(Clear));  // open: Qn, reset
  // Probe on d_ff_2_q
  D_Flip_Flop d_ff_2 (.clk(Clock_out), .D(d_ff_3_q), .Q(d_ff_2_q), .preset(Clear));  // open: Qn, reset
  // Probe on d_ff_3_q
  D_Flip_Flop d_ff_3 (.clk(Clock_out), .D(d_ff_4_q), .Q(d_ff_3_q), .preset(Clear));  // open: Qn, reset
  // Probe on d_ff_4_q
  D_Flip_Flop d_ff_4 (.clk(Clock_out), .D(d_ff_5_q), .Q(d_ff_4_q), .preset(Clear));  // open: Qn, reset
  // Probe on d_ff_5_q
  D_Flip_Flop d_ff_5 (.clk(Clock_out), .D(d_ff_6_q), .Q(d_ff_5_q), .preset(Clear));  // open: Qn, reset
  // Probe on d_ff_6_q
  D_Flip_Flop d_ff_6 (.clk(Clock_out), .D(Input), .Q(d_ff_6_q), .preset(Clear));  // open: Qn, reset

  // Notes on the sheet:
  //   Registrador de Deslocamento para a Esquerda de 6 bits com Load em Todos
endmodule

module SR_RIGHT_RING_6_bits_FIRST_PRESET (
  input  Input,
  input  Clear
);

  wire Clock_out, d_ff_1_q, d_ff_2_q, d_ff_3_q, d_ff_4_q, d_ff_5_q, d_ff_6_q;

  Clock Clock (.out(Clock_out));
  // OR_Gate or_1 has open pins: in0=Input, out=open
  // Probe on d_ff_1_q
  D_Flip_Flop d_ff_1 (.clk(Clock_out), .D(d_ff_6_q), .Q(d_ff_1_q), .preset(Clear));  // open: Qn, reset
  // Probe on d_ff_2_q
  D_Flip_Flop d_ff_2 (.clk(Clock_out), .D(d_ff_1_q), .Q(d_ff_2_q), .reset(Clear));  // open: Qn, preset
  D_Flip_Flop d_ff_3 (.clk(Clock_out), .D(d_ff_2_q), .Q(d_ff_3_q), .reset(Clear));  // open: Qn, preset
  // Probe on d_ff_3_q
  // Probe on d_ff_4_q
  D_Flip_Flop d_ff_4 (.clk(Clock_out), .D(d_ff_3_q), .Q(d_ff_4_q), .reset(Clear));  // open: Qn, preset
  // Probe on d_ff_5_q
  D_Flip_Flop d_ff_5 (.clk(Clock_out), .D(d_ff_4_q), .Q(d_ff_5_q), .reset(Clear));  // open: Qn, preset
  // Probe on d_ff_6_q
  D_Flip_Flop d_ff_6 (.clk(Clock_out), .D(d_ff_5_q), .Q(d_ff_6_q), .reset(Clear));  // open: Qn, preset

  // Notes on the sheet:
  //   Registrador de Deslocamento Circular ("Ring") para a Direita de 6 bits com Load no Primeiro
endmodule

module SR_LEFT_TWISTED_6_bits_FIRST_PRESET (
  input  Input,
  input  Clear
);

  wire Clock_out, d_ff_1_q, d_ff_1_qn, d_ff_2_q, d_ff_3_q, d_ff_4_q, d_ff_5_q, d_ff_6_q, or_1_out;

  Clock Clock (.out(Clock_out));
  or or_1 (or_1_out, d_ff_1_qn, Input);
  // Probe on d_ff_1_q
  D_Flip_Flop d_ff_1 (.clk(Clock_out), .D(d_ff_2_q), .Q(d_ff_1_q), .Qn(d_ff_1_qn), .reset(Clear));  // open: preset
  // Probe on d_ff_2_q
  D_Flip_Flop d_ff_2 (.clk(Clock_out), .D(d_ff_3_q), .Q(d_ff_2_q), .reset(Clear));  // open: Qn, preset
  // Probe on d_ff_3_q
  D_Flip_Flop d_ff_3 (.clk(Clock_out), .D(d_ff_4_q), .Q(d_ff_3_q), .reset(Clear));  // open: Qn, preset
  // Probe on d_ff_4_q
  D_Flip_Flop d_ff_4 (.clk(Clock_out), .D(d_ff_5_q), .Q(d_ff_4_q), .reset(Clear));  // open: Qn, preset
  // Probe on d_ff_5_q
  D_Flip_Flop d_ff_5 (.clk(Clock_out), .D(d_ff_6_q), .Q(d_ff_5_q), .reset(Clear));  // open: Qn, preset
  // Probe on d_ff_6_q
  D_Flip_Flop d_ff_6 (.clk(Clock_out), .D(or_1_out), .Q(d_ff_6_q), .preset(Clear), .reset(Clear));  // open: Qn

  // Notes on the sheet:
  //   Registrador de Deslocamento Circular ("Twisted Ring") para a Esquerda de 6 bits com Load no Primeiro
endmodule

module PS_6_bits (
  input  in_1,
  input  in_2,
  input  in_3,
  input  in_4,
  input  in_5,
  input  in_6,
  input  Load,
  input  Clear
);

  wire and_1_out, and_2_out, and_3_out, and_4_out, and_5_out, and_6_out, Clock_out, d_ff_1_q, d_ff_2_q,
       d_ff_3_q, d_ff_4_q, d_ff_5_q, d_ff_6_q;

  Clock Clock (.out(Clock_out));
  // Probe on d_ff_1_q
  and and_1 (and_1_out, Load, in_1);
  D_Flip_Flop d_ff_1 (.clk(Clock_out), .D(1'b0), .Q(d_ff_1_q), .preset(and_1_out), .reset(Clear));  // open: Qn
  and and_2 (and_2_out, Load, in_2);
  D_Flip_Flop d_ff_2 (.clk(Clock_out), .D(d_ff_1_q), .Q(d_ff_2_q), .preset(and_2_out), .reset(Clear));  // open: Qn
  // Probe on d_ff_2_q
  and and_3 (and_3_out, Load, in_3);
  // Probe on d_ff_3_q
  and and_4 (and_4_out, Load, in_4);
  D_Flip_Flop d_ff_3 (.clk(Clock_out), .D(d_ff_2_q), .Q(d_ff_3_q), .preset(and_3_out), .reset(Clear));  // open: Qn
  // Probe on d_ff_4_q
  D_Flip_Flop d_ff_4 (.clk(Clock_out), .D(d_ff_3_q), .Q(d_ff_4_q), .preset(and_4_out), .reset(Clear));  // open: Qn
  // Probe on d_ff_5_q
  and and_5 (and_5_out, Load, in_5);
  D_Flip_Flop d_ff_5 (.clk(Clock_out), .D(d_ff_4_q), .Q(d_ff_5_q), .preset(and_5_out), .reset(Clear));  // open: Qn
  and and_6 (and_6_out, Load, in_6);
  D_Flip_Flop d_ff_6 (.clk(Clock_out), .D(d_ff_5_q), .Q(d_ff_6_q), .preset(and_6_out), .reset(Clear));  // open: Qn
  // Probe on d_ff_6_q

  // Notes on the sheet:
  //   Conversor Paralelo-Série de 6 bits
endmodule
