// Logisim project Guia1402.circ as structural Verilog: 1 circuit, main circuit main
module main (
  input  in_1,
  input  in_2
);

  wire clock_1_out, d_ff_1_q, d_ff_1_qn, d_ff_2_q, d_ff_2_qn, d_ff_3_q, d_ff_3_qn, d_ff_4_q, d_ff_4_qn,
       multiplexer_1_out, multiplexer_2_out, multiplexer_3_out, multiplexer_4_out;

  Clock clock_1 (.out(clock_1_out));
  Multiplexer multiplexer_1 (.in0(d_ff_4_q), .in1(d_ff_4_qn), .out(multiplexer_1_out), .sel(in_1), .en(in_2));
  D_Flip_Flop d_ff_1 (
    .clk(clock_1_out), .D(multiplexer_1_out), .Q(d_ff_1_q), .Qn(d_ff_1_qn));  // open: preset, en, reset
  Multiplexer multiplexer_2 (.in0(d_ff_1_q), .in1(d_ff_1_qn), .out(multiplexer_2_out), .sel(in_1), .en(in_2));
  D_Flip_Flop d_ff_2 (
    .clk(clock_1_out), .D(multiplexer_2_out), .Q(d_ff_2_q), .Qn(d_ff_2_qn));  // open: preset, en, reset
  D_Flip_Flop d_ff_3 (
    .clk(clock_1_out), .D(multiplexer_3_out), .Q(d_ff_3_q), .Qn(d_ff_3_qn));  // open: preset, en, reset
  Multiplexer multiplexer_3 (.in0(d_ff_2_q), .in1(d_ff_2_qn), .out(multiplexer_3_out), .sel(in_1), .en(in_2));
  Multiplexer multiplexer_4 (.in0(d_ff_3_q), .in1(d_ff_3_qn), .out(multiplexer_4_out), .sel(in_1), .en(in_2));
  D_Flip_Flop d_ff_4 (
    .clk(clock_1_out), .D(multiplexer_4_out), .Q(d_ff_4_q), .Qn(d_ff_4_qn));  // open: preset, en, reset
endmodule
