// Logisim project Guia_14.circ as structural Verilog: 1 circuit, main circuit main
module main (
  input  in_1,
  input  Clr,
  input  data,
  output A,
  output B,
  output C,
  output D,
  output E,
  output F
);

  wire clock_1_out;

  Clock clock_1 (.out(clock_1_out));
  D_Flip_Flop d_ff_1 (.clk(clock_1_out), .D(B), .Q(A), .preset(in_1), .reset(Clr));  // open: Qn
  D_Flip_Flop d_ff_2 (.clk(clock_1_out), .D(C), .Q(B));  // open: Qn, preset, reset
  D_Flip_Flop d_ff_3 (.clk(clock_1_out), .D(D), .Q(C));  // open: Qn, preset, reset
  D_Flip_Flop d_ff_4 (.clk(clock_1_out), .D(E), .Q(D));  // open: Qn, preset, reset
  D_Flip_Flop d_ff_5 (.clk(clock_1_out), .D(F), .Q(E));  // open: Qn, preset, reset
  D_Flip_Flop d_ff_6 (.clk(clock_1_out), .D(data), .Q(F));  // open: Qn, preset, reset

  // Notes on the sheet:
  //   806937 - Felipe Pereira da Silva
endmodule
