// Logisim project g1401.circ as structural Verilog: 1 circuit, main circuit main
module main (
  input  CLK,
  input  data,
  input  CLR
);

  wire d_ff_1_q, d_ff_2_q, d_ff_3_q, d_ff_4_q, d_ff_5_q, d_ff_6_q, undriven;

  // Probe on d_ff_1_q
  D_Flip_Flop d_ff_1 (.clk(CLK), .D(d_ff_2_q), .Q(d_ff_1_q), .reset(CLR));  // open: Qn, preset
  // Probe on d_ff_2_q
  D_Flip_Flop d_ff_2 (.clk(CLK), .D(d_ff_3_q), .Q(d_ff_2_q), .reset(CLR));  // open: Qn, preset
  // Probe on d_ff_3_q
  D_Flip_Flop d_ff_3 (.clk(CLK), .D(d_ff_4_q), .Q(d_ff_3_q), .preset(undriven), .reset(CLR));  // open: Qn
  // Probe on d_ff_4_q
  D_Flip_Flop d_ff_4 (.clk(CLK), .D(d_ff_5_q), .Q(d_ff_4_q), .reset(CLR));  // open: Qn, preset
  // Probe on d_ff_5_q
  D_Flip_Flop d_ff_5 (.clk(CLK), .D(d_ff_6_q), .Q(d_ff_5_q), .reset(CLR));  // open: Qn, preset
  // Probe on d_ff_6_q
  D_Flip_Flop d_ff_6 (.clk(CLK), .D(data), .Q(d_ff_6_q), .reset(CLR));  // open: Qn, preset
endmodule
