// Logisim project g141.circ as structural Verilog: 1 circuit, main circuit main
module main (
  input  CLK,
  input  CLR,
  input  Data,
  input  LOAD,
  input  in_5,
  input  in_6,
  input  in_7,
  input  in_8,
  input  in_9,
  input  in_10
);

  wire and_1_out, and_2_out, and_3_out, and_4_out, and_5_out, and_6_out, d_ff_1_q, d_ff_2_q, d_ff_3_q,
       d_ff_4_q, d_ff_5_q, d_ff_6_q;

  // Probe on d_ff_1_q
  and and_1 (and_1_out, LOAD, in_5);
  D_Flip_Flop #(.Pre_Clr_Positions("LEGACY"), .enable("true")) d_ff_1 (
    .clk(CLK), .D(d_ff_2_q), .Q(d_ff_1_q), .preset(and_1_out), .reset(CLR));  // open: Qn, en
  // Probe on d_ff_2_q
  D_Flip_Flop #(.Pre_Clr_Positions("LEGACY"), .enable("true")) d_ff_2 (
    .clk(CLK), .D(d_ff_3_q), .Q(d_ff_2_q), .preset(and_2_out), .reset(CLR));  // open: Qn, en
  and and_2 (and_2_out, LOAD, in_6);
  // Probe on d_ff_3_q
  D_Flip_Flop #(.Pre_Clr_Positions("LEGACY"), .enable("true")) d_ff_3 (
    .clk(CLK), .D(d_ff_4_q), .Q(d_ff_3_q), .preset(and_3_out), .reset(CLR));  // open: Qn, en
  and and_3 (and_3_out, LOAD, in_7);
  // Probe on d_ff_4_q
  and and_4 (and_4_out, LOAD, in_8);
  D_Flip_Flop #(.Pre_Clr_Positions("LEGACY"), .enable("true")) d_ff_4 (
    .clk(CLK), .D(d_ff_5_q), .Q(d_ff_4_q), .preset(and_4_out), .reset(CLR));  // open: Qn, en
  // Probe on d_ff_5_q
  and and_5 (and_5_out, LOAD, in_9);
  D_Flip_Flop #(.Pre_Clr_Positions("LEGACY"), .enable("true")) d_ff_5 (
    .clk(CLK), .D(d_ff_6_q), .Q(d_ff_5_q), .preset(and_5_out), .reset(CLR));  // open: Qn, en
  // Probe on d_ff_6_q
  and and_6 (and_6_out, LOAD, in_10);
  D_Flip_Flop #(.Pre_Clr_Positions("LEGACY"), .enable("true")) d_ff_6 (
    .clk(CLK), .D(Data), .Q(d_ff_6_q), .preset(and_6_out), .reset(CLR));  // open: Qn, en
endmodule
