// Logisim project Guia_14.circ as structural Verilog: 7 circuits, main circuit Q1
module Q1 (
  input  in_1,
  input  Clr,
  input  data,
  output A,
  output B,
  output C,
  output D,
  output E,
  output F
);

  wire clock_1_out;

  Clock clock_1 (.out(clock_1_out));
  D_Flip_Flop d_ff_1 (.clk(clock_1_out), .D(B), .Q(A), .preset(in_1), .reset(Clr));  // open: Qn
  D_Flip_Flop d_ff_2 (.clk(clock_1_out), .D(C), .Q(B));  // open: Qn, preset, reset
  D_Flip_Flop d_ff_3 (.clk(clock_1_out), .D(D), .Q(C));  // open: Qn, preset, reset
  D_Flip_Flop d_ff_4 (.clk(clock_1_out), .D(E), .Q(D));  // open: Qn, preset, reset
  D_Flip_Flop d_ff_5 (.clk(clock_1_out), .D(F), .Q(E));  // open: Qn, preset, reset
  D_Flip_Flop d_ff_6 (.clk(clock_1_out), .D(data), .Q(F));  // open: Qn, preset, reset
endmodule

module Q2 (
  input  in_1,
  input  in_2,
  input  in_3,
  input  in_4,
  input  in_5,
  input  in_6,
  input  in_7,
  input  data,
  input  Clr,
  input  in_10,
  input  in_11,
  input  in_12,
  input  in_13,
  input  in_14,
  input  in_15,
  output A,
  output B,
  output C,
  output D,
  output E,
  output F
);

  wire and_1_out, and_2_out, and_3_out, and_4_out, and_5_out, and_6_out, and_7_out, and_8_out, and_9_out,
       and_10_out, and_11_out, and_12_out, clock_1_out;

  Clock clock_1 (.out(clock_1_out));
  and and_1 (and_1_out, in_7, in_1);
  D_Flip_Flop d_ff_1 (.clk(clock_1_out), .D(B), .Q(A), .preset(and_1_out), .reset(and_2_out));  // open: Qn
  and and_2 (and_2_out, Clr, in_10);
  and and_3 (and_3_out, in_7, in_2);
  and and_4 (and_4_out, Clr, in_11);
  D_Flip_Flop d_ff_2 (.clk(clock_1_out), .D(C), .Q(B), .preset(and_3_out), .reset(and_4_out));  // open: Qn
  and and_5 (and_5_out, in_7, in_3);
  D_Flip_Flop d_ff_3 (.clk(clock_1_out), .D(D), .Q(C), .preset(and_5_out), .reset(and_6_out));  // open: Qn
  and and_6 (and_6_out, Clr, in_12);
  and and_7 (and_7_out, in_7, in_4);
  D_Flip_Flop d_ff_4 (.clk(clock_1_out), .D(E), .Q(D), .preset(and_7_out), .reset(and_8_out));  // open: Qn
  and and_8 (and_8_out, Clr, in_13);
  and and_9 (and_9_out, in_7, in_5);
  and and_10 (and_10_out, Clr, in_14);
  D_Flip_Flop d_ff_5 (.clk(clock_1_out), .D(F), .Q(E), .preset(and_9_out), .reset(and_10_out));  // open: Qn
  and and_11 (and_11_out, in_7, in_6);
  D_Flip_Flop d_ff_6 (.clk(clock_1_out), .D(data), .Q(F), .preset(and_11_out), .reset(and_12_out));  // open: Qn
  and and_12 (and_12_out, Clr, in_15);
endmodule

module Q3 (
  input  in_1,
  output out_2,
  output out_3,
  output out_4,
  output out_5,
  output out_6,
  output out_7
);

  wire clock_1_out;

  Clock clock_1 (.out(clock_1_out));
  D_Flip_Flop d_ff_1 (.clk(clock_1_out), .D(in_1), .Q(out_2));  // open: Qn, preset, reset
  D_Flip_Flop d_ff_2 (.clk(clock_1_out), .D(out_2), .Q(out_3));  // open: Qn, preset, reset
  D_Flip_Flop d_ff_3 (.clk(clock_1_out), .D(out_3), .Q(out_4));  // open: Qn, preset, reset
  D_Flip_Flop d_ff_4 (.clk(clock_1_out), .D(out_4), .Q(out_5));  // open: Qn, preset, reset
  D_Flip_Flop d_ff_5 (.clk(clock_1_out), .D(out_5), .Q(out_6));  // open: Qn, preset, reset
  D_Flip_Flop d_ff_6 (.clk(clock_1_out), .D(out_6));  // open: Q, Qn, preset, reset

  assign out_7 = in_1;
endmodule

module Q4 (
  input  in_1,
  input  in_2,
  output out_3,
  output out_4,
  output out_5,
  output out_6,
  output out_7,
  output out_8
);

  wire clock_1_out;

  Clock clock_1 (.out(clock_1_out));
  or or_1 (out_8, in_1, out_8);
  D_Flip_Flop d_ff_1 (.clk(clock_1_out), .D(out_3), .reset(in_2));  // open: Q, Qn, preset
  D_Flip_Flop d_ff_2 (.clk(clock_1_out), .D(out_4), .Q(out_3), .reset(in_2));  // open: Qn, preset
  D_Flip_Flop d_ff_3 (.clk(clock_1_out), .D(out_5), .Q(out_4), .reset(in_2));  // open: Qn, preset
  D_Flip_Flop d_ff_4 (.clk(clock_1_out), .D(out_6), .Q(out_5), .reset(in_2));  // open: Qn, preset
  D_Flip_Flop d_ff_5 (.clk(clock_1_out), .D(out_7), .Q(out_6), .reset(in_2));  // open: Qn, preset
  D_Flip_Flop d_ff_6 (.clk(clock_1_out), .D(out_8), .Q(out_7), .reset(in_2));  // open: Qn, preset
endmodule

module Q5 (
  input  in_1,
  input  in_2,
  input  in_3,
  input  in_4,
  input  in_5,
  input  in_6,
  input  in_7,
  input  in_8,
  output out_9,
  output out_10,
  output out_11,
  output out_12,
  output out_13
);

  wire and_1_out, and_2_out, and_3_out, and_4_out, and_5_out, and_6_out, clock_1_out;

  Clock clock_1 (.out(clock_1_out));
  D_Flip_Flop d_ff_1 (.clk(clock_1_out), .D(in_1), .Q(out_9), .reset(and_1_out));  // open: Qn, preset
  and and_1 (and_1_out, in_2, in_3);
  and and_2 (and_2_out, in_2, in_4);
  D_Flip_Flop d_ff_2 (.clk(clock_1_out), .D(out_9), .Q(out_10), .reset(and_2_out));  // open: Qn, preset
  D_Flip_Flop d_ff_3 (.clk(clock_1_out), .D(out_10), .Q(out_11), .reset(and_3_out));  // open: Qn, preset
  and and_3 (and_3_out, in_2, in_5);
  and and_4 (and_4_out, in_2, in_6);
  D_Flip_Flop d_ff_4 (.clk(clock_1_out), .D(out_11), .Q(out_12), .reset(and_4_out));  // open: Qn, preset
  D_Flip_Flop d_ff_5 (.clk(clock_1_out), .D(out_12), .Q(out_13), .reset(and_5_out));  // open: Qn, preset
  and and_5 (and_5_out, in_2, in_7);
  D_Flip_Flop d_ff_6 (.clk(clock_1_out), .D(out_13), .reset(and_6_out));  // open: Q, Qn, preset
  and and_6 (and_6_out, in_2, in_8);
endmodule

module Q6 (
  input  in_1,
  input  in_2,
  output out_3,
  output out_4,
  output out_5,
  output out_6,
  output out_7
);

  wire clock_1_out;

  Clock clock_1 (.out(clock_1_out));
  D_Flip_Flop d_ff_1 (.clk(clock_1_out), .D(in_2), .Q(out_3), .preset(in_1));  // open: Qn, reset
  D_Flip_Flop d_ff_2 (.clk(clock_1_out), .D(out_3), .Q(out_4), .preset(in_1));  // open: Qn, reset
  D_Flip_Flop d_ff_3 (.clk(clock_1_out), .D(out_4), .Q(out_5), .preset(in_1));  // open: Qn, reset
  D_Flip_Flop d_ff_4 (.clk(clock_1_out), .D(out_5), .Q(out_6), .preset(in_1));  // open: Qn, reset
  D_Flip_Flop d_ff_5 (.clk(clock_1_out), .D(out_6), .Q(out_7), .preset(in_1));  // open: Qn, reset
  D_Flip_Flop d_ff_6 (.clk(clock_1_out), .D(out_7), .preset(in_1));  // open: Q, Qn, reset
endmodule

module Q7 (
  input  in_1,
  input  in_2,
  output out_3,
  output out_4,
  output out_5,
  output out_6,
  output out_7,
  output out_8
);

  wire clock_1_out, or_1_out;

  Clock clock_1 (.out(clock_1_out));
  or or_1 (or_1_out, in_1, out_8);
  D_Flip_Flop d_ff_1 (.clk(clock_1_out), .D(or_1_out), .Q(out_3), .reset(in_2));  // open: Qn, preset
  D_Flip_Flop d_ff_2 (.clk(clock_1_out), .D(out_3), .Q(out_4), .reset(in_2));  // open: Qn, preset
  D_Flip_Flop d_ff_3 (.clk(clock_1_out), .D(out_4), .Q(out_5), .reset(in_2));  // open: Qn, preset
  D_Flip_Flop d_ff_4 (.clk(clock_1_out), .D(out_5), .Q(out_6), .reset(in_2));  // open: Qn, preset
  D_Flip_Flop d_ff_5 (.clk(clock_1_out), .D(out_6), .Q(out_7), .reset(in_2));  // open: Qn, preset
  D_Flip_Flop d_ff_6 (.clk(clock_1_out), .D(out_7), .Q(out_8), .reset(in_2));  // open: Qn, preset
endmodule
