// Logisim project G14.circ as structural Verilog: 7 circuits, main circuit G1401
module G1401 (
  input  In,
  input  Load,
  output out_3,
  output out_4,
  output out_5,
  output out_6,
  output out_7,
  output out_8
);

  wire Clk_out;

  Clock Clk (.out(Clk_out));
  D_Flip_Flop #(.Pre_Clr_Positions("LEGACY"), .NewFFLayout("false")) d_ff_1 (
    .clk(Clk_out), .D(out_4), .Q(out_3), .reset(Load));  // open: Qn, preset
  D_Flip_Flop #(.Pre_Clr_Positions("LEGACY"), .NewFFLayout("false")) d_ff_2 (
    .clk(Clk_out), .D(out_5), .Q(out_4), .reset(Load));  // open: Qn, preset
  D_Flip_Flop #(.Pre_Clr_Positions("LEGACY"), .NewFFLayout("false")) d_ff_3 (
    .clk(Clk_out), .D(out_6), .Q(out_5), .reset(Load));  // open: Qn, preset
  D_Flip_Flop #(.Pre_Clr_Positions("LEGACY"), .NewFFLayout("false")) d_ff_4 (
    .clk(Clk_out), .D(out_7), .Q(out_6), .reset(Load));  // open: Qn, preset
  D_Flip_Flop #(.Pre_Clr_Positions("LEGACY"), .NewFFLayout("false")) d_ff_5 (
    .clk(Clk_out), .D(out_8), .Q(out_7), .reset(Load));  // open: Qn, preset
  D_Flip_Flop #(.Pre_Clr_Positions("LEGACY"), .NewFFLayout("false")) d_ff_6 (
    .clk(Clk_out), .D(In), .Q(out_8), .preset(Load));  // open: Qn, reset
endmodule

module G1402 (
  input  In,
  input  Load,
  output out_3,
  output out_4,
  output out_5,
  output out_6,
  output out_7,
  output out_8
);

  wire Clk_out;

  Clock Clk (.out(Clk_out));
  D_Flip_Flop #(.Pre_Clr_Positions("LEGACY"), .NewFFLayout("false")) d_ff_1 (
    .clk(Clk_out), .D(out_4), .Q(out_3), .preset(Load));  // open: Qn, reset
  D_Flip_Flop #(.Pre_Clr_Positions("LEGACY"), .NewFFLayout("false")) d_ff_2 (
    .clk(Clk_out), .D(out_5), .Q(out_4), .preset(Load));  // open: Qn, reset
  D_Flip_Flop #(.Pre_Clr_Positions("LEGACY"), .NewFFLayout("false")) d_ff_3 (
    .clk(Clk_out), .D(out_6), .Q(out_5), .preset(Load));  // open: Qn, reset
  D_Flip_Flop #(.Pre_Clr_Positions("LEGACY"), .NewFFLayout("false")) d_ff_4 (
    .clk(Clk_out), .D(out_7), .Q(out_6), .preset(Load));  // open: Qn, reset
  D_Flip_Flop #(.Pre_Clr_Positions("LEGACY"), .NewFFLayout("false")) d_ff_5 (
    .clk(Clk_out), .D(out_8), .Q(out_7), .preset(Load));  // open: Qn, reset
  D_Flip_Flop #(.Pre_Clr_Positions("LEGACY"), .NewFFLayout("false")) d_ff_6 (
    .clk(Clk_out), .D(In), .Q(out_8), .preset(Load));  // open: Qn, reset
endmodule

module G1403 (
  input  In,
  input  Load
);

  wire Clk_out, d_ff_1_q, d_ff_2_q, d_ff_3_q, d_ff_4_q, d_ff_5_q, d_ff_6_q, or_1_out;

  Clock Clk (.out(Clk_out));
  or or_1 (or_1_out, d_ff_6_q, In);
  D_Flip_Flop #(.Pre_Clr_Positions("LEGACY"), .NewFFLayout("false")) d_ff_1 (
    .clk(Clk_out), .D(or_1_out), .Q(d_ff_1_q), .preset(Load));  // open: Qn, reset
  D_Flip_Flop #(.Pre_Clr_Positions("LEGACY"), .NewFFLayout("false")) d_ff_2 (
    .clk(Clk_out), .D(d_ff_1_q), .Q(d_ff_2_q), .reset(Load));  // open: Qn, preset
  D_Flip_Flop #(.Pre_Clr_Positions("LEGACY"), .NewFFLayout("false")) d_ff_3 (
    .clk(Clk_out), .D(d_ff_2_q), .Q(d_ff_3_q), .reset(Load));  // open: Qn, preset
  D_Flip_Flop #(.Pre_Clr_Positions("LEGACY"), .NewFFLayout("false")) d_ff_4 (
    .clk(Clk_out), .D(d_ff_3_q), .Q(d_ff_4_q), .reset(Load));  // open: Qn, preset
  D_Flip_Flop #(.Pre_Clr_Positions("LEGACY"), .NewFFLayout("false")) d_ff_5 (
    .clk(Clk_out), .D(d_ff_4_q), .Q(d_ff_5_q), .reset(Load));  // open: Qn, preset
  D_Flip_Flop #(.Pre_Clr_Positions("LEGACY"), .NewFFLayout("false")) d_ff_6 (
    .clk(Clk_out), .D(d_ff_5_q), .Q(d_ff_6_q), .reset(Load));  // open: Qn, preset
endmodule

module G1404 (
  input  In,
  input  Load,
  output out_3,
  output out_4,
  output out_5,
  output out_6,
  output out_7,
  output out_8
);

  wire Clk_out, d_ff_1_qn, or_1_out;

  Clock Clk (.out(Clk_out));
  D_Flip_Flop #(.Pre_Clr_Positions("LEGACY"), .NewFFLayout("false")) d_ff_1 (
    .clk(Clk_out), .D(out_4), .Q(out_3), .Qn(d_ff_1_qn), .reset(Load));  // open: preset
  D_Flip_Flop #(.Pre_Clr_Positions("LEGACY"), .NewFFLayout("false")) d_ff_2 (
    .clk(Clk_out), .D(out_5), .Q(out_4), .reset(Load));  // open: Qn, preset
  D_Flip_Flop #(.Pre_Clr_Positions("LEGACY"), .NewFFLayout("false")) d_ff_3 (
    .clk(Clk_out), .D(out_6), .Q(out_5), .reset(Load));  // open: Qn, preset
  D_Flip_Flop #(.Pre_Clr_Positions("LEGACY"), .NewFFLayout("false")) d_ff_4 (
    .clk(Clk_out), .D(out_7), .Q(out_6), .reset(Load));  // open: Qn, preset
  D_Flip_Flop #(.Pre_Clr_Positions("LEGACY"), .NewFFLayout("false")) d_ff_5 (
    .clk(Clk_out), .D(out_8), .Q(out_7), .reset(Load));  // open: Qn, preset
  or or_1 (or_1_out, In, d_ff_1_qn);
  D_Flip_Flop #(.Pre_Clr_Positions("LEGACY"), .NewFFLayout("false")) d_ff_6 (
    .clk(Clk_out), .D(or_1_out), .Q(out_8), .preset(Load));  // open: Qn, reset
endmodule

module G1405 (
  input  Load,
  input  [5:0] Load_In,
  output Out
);

  wire and_1_out, and_2_out, and_3_out, and_4_out, and_5_out, and_6_out, Clk_out, d_ff_1_q, d_ff_2_q,
       d_ff_3_q, d_ff_4_q, d_ff_5_q;

  Clock Clk (.out(Clk_out));
  D_Flip_Flop #(.Pre_Clr_Positions("LEGACY"), .NewFFLayout("false")) d_ff_1 (
    .clk(Clk_out), .D(1'b0), .Q(d_ff_1_q), .preset(and_1_out));  // open: Qn, reset
  and and_1 (and_1_out, Load, Load_In[5]);
  and and_2 (and_2_out, Load, Load_In[4]);
  D_Flip_Flop #(.Pre_Clr_Positions("LEGACY"), .NewFFLayout("false")) d_ff_2 (
    .clk(Clk_out), .D(d_ff_1_q), .Q(d_ff_2_q), .preset(and_2_out));  // open: Qn, reset
  and and_3 (and_3_out, Load, Load_In[3]);
  D_Flip_Flop #(.Pre_Clr_Positions("LEGACY"), .NewFFLayout("false")) d_ff_3 (
    .clk(Clk_out), .D(d_ff_2_q), .Q(d_ff_3_q), .preset(and_3_out));  // open: Qn, reset
  and and_4 (and_4_out, Load, Load_In[2]);
  D_Flip_Flop #(.Pre_Clr_Positions("LEGACY"), .NewFFLayout("false")) d_ff_4 (
    .clk(Clk_out), .D(d_ff_3_q), .Q(d_ff_4_q), .preset(and_4_out));  // open: Qn, reset
  D_Flip_Flop #(.Pre_Clr_Positions("LEGACY"), .NewFFLayout("false")) d_ff_5 (
    .clk(Clk_out), .D(d_ff_4_q), .Q(d_ff_5_q), .preset(and_5_out));  // open: Qn, reset
  and and_5 (and_5_out, Load, Load_In[1]);
  D_Flip_Flop #(.Pre_Clr_Positions("LEGACY"), .NewFFLayout("false")) d_ff_6 (
    .clk(Clk_out), .D(d_ff_5_q), .Q(Out), .preset(and_6_out));  // open: Qn, reset
  and and_6 (and_6_out, Load, Load_In[0]);
endmodule

module G1406 (
  input  In,
  input  Load,
  input  Clr
);

  wire Clk_out, d_ff_1_q, d_ff_2_q, d_ff_3_q, d_ff_4_q, d_ff_5_q, xor_1_out;

  Clock Clk (.out(Clk_out));
  D_Flip_Flop #(.Pre_Clr_Positions("LEGACY"), .NewFFLayout("false")) d_ff_1 (
    .clk(Clk_out), .D(d_ff_2_q), .Q(d_ff_1_q), .preset(Load), .reset(Clr));  // open: Qn
  D_Flip_Flop #(.Pre_Clr_Positions("LEGACY"), .NewFFLayout("false")) d_ff_2 (
    .clk(Clk_out), .D(d_ff_3_q), .Q(d_ff_2_q), .preset(Load), .reset(Clr));  // open: Qn
  D_Flip_Flop #(.Pre_Clr_Positions("LEGACY"), .NewFFLayout("false")) d_ff_3 (
    .clk(Clk_out), .D(d_ff_4_q), .Q(d_ff_3_q), .preset(Load), .reset(Clr));  // open: Qn
  D_Flip_Flop #(.Pre_Clr_Positions("LEGACY"), .NewFFLayout("false")) d_ff_4 (
    .clk(Clk_out), .D(d_ff_5_q), .Q(d_ff_4_q), .preset(Load), .reset(Clr));  // open: Qn
  xor xor_1 (xor_1_out, d_ff_1_q, In);
  D_Flip_Flop #(.Pre_Clr_Positions("LEGACY"), .NewFFLayout("false")) d_ff_5 (
    .clk(Clk_out), .D(xor_1_out), .Q(d_ff_5_q), .preset(Load), .reset(Clr));  // open: Qn
endmodule

module G1407 (
  input  IN,
  input  Load,
  input  Clr
);

  wire Clk_out, d_ff_1_q, d_ff_2_q, d_ff_3_q, d_ff_4_q, d_ff_5_qn, or_1_out;

  Clock Clk (.out(Clk_out));
  or or_1 (or_1_out, IN, d_ff_5_qn);
  D_Flip_Flop #(.Pre_Clr_Positions("LEGACY"), .NewFFLayout("false")) d_ff_1 (
    .clk(Clk_out), .D(or_1_out), .Q(d_ff_1_q), .preset(Load), .reset(Clr));  // open: Qn
  D_Flip_Flop #(.Pre_Clr_Positions("LEGACY"), .NewFFLayout("false")) d_ff_2 (
    .clk(Clk_out), .D(d_ff_1_q), .Q(d_ff_2_q), .preset(Load), .reset(Clr));  // open: Qn
  D_Flip_Flop #(.Pre_Clr_Positions("LEGACY"), .NewFFLayout("false")) d_ff_3 (
    .clk(Clk_out), .D(d_ff_2_q), .Q(d_ff_3_q), .preset(Load), .reset(Clr));  // open: Qn
  D_Flip_Flop #(.Pre_Clr_Positions("LEGACY"), .NewFFLayout("false")) d_ff_4 (
    .clk(Clk_out), .D(d_ff_3_q), .Q(d_ff_4_q), .preset(Load), .reset(Clr));  // open: Qn
  D_Flip_Flop #(.Pre_Clr_Positions("LEGACY"), .NewFFLayout("false")) d_ff_5 (
    .clk(Clk_out), .D(d_ff_4_q), .Qn(d_ff_5_qn), .preset(Load), .reset(Clr));  // open: Q
endmodule
