// Logisim project G13.circ as structural Verilog: 8 circuits, main circuit G1304
module G1301 (
  input  in_1,
  input  in_2
);

  wire clock_1_out, j_k_ff_1_qn, j_k_ff_2_qn, j_k_ff_3_qn, j_k_ff_4_qn;
  wire [4:0] j_k_ff_1_q, not_1_out;

  Clock clock_1 (.out(clock_1_out));
  J_K_Flip_Flop #(.Pre_Clr_Positions("LEGACY"), .NewFFLayout("false")) j_k_ff_1 (
    .J(in_1), .clk(clock_1_out), .K(in_1), .Q(j_k_ff_1_q[0]), .Qn(j_k_ff_1_qn), .reset(in_2));  // open: preset
  J_K_Flip_Flop #(.Pre_Clr_Positions("LEGACY"), .NewFFLayout("false")) j_k_ff_2 (
    .J(in_1), .clk(j_k_ff_1_qn), .K(in_1), .Q(j_k_ff_1_q[1]), .Qn(j_k_ff_2_qn), .reset(in_2));  // open: preset
  // Probe on not_1_out
  // Probe on not_1_out
  assign not_1_out = ~j_k_ff_1_q;  // NOT_Gate not_1, 5 bits wide
  J_K_Flip_Flop #(.Pre_Clr_Positions("LEGACY"), .NewFFLayout("false")) j_k_ff_3 (
    .J(in_1), .clk(j_k_ff_2_qn), .K(in_1), .Q(j_k_ff_1_q[2]), .Qn(j_k_ff_3_qn), .reset(in_2));  // open: preset
  J_K_Flip_Flop #(.Pre_Clr_Positions("LEGACY"), .NewFFLayout("false")) j_k_ff_4 (
    .J(in_1), .clk(j_k_ff_3_qn), .K(in_1), .Q(j_k_ff_1_q[3]), .Qn(j_k_ff_4_qn), .reset(in_2));  // open: preset
  J_K_Flip_Flop #(.Pre_Clr_Positions("LEGACY"), .NewFFLayout("false")) j_k_ff_5 (
    .J(in_1), .clk(j_k_ff_4_qn), .K(in_1), .Q(j_k_ff_1_q[4]), .reset(in_2));  // open: Qn, preset
endmodule

module G1302 (
  input  in_1,
  input  in_2
);

  wire clock_1_out, j_k_ff_1_qn, j_k_ff_2_qn, j_k_ff_3_qn, j_k_ff_4_qn;
  wire [4:0] j_k_ff_1_q;

  Clock clock_1 (.out(clock_1_out));
  J_K_Flip_Flop #(.Pre_Clr_Positions("LEGACY"), .NewFFLayout("false")) j_k_ff_1 (
    .J(in_1), .clk(clock_1_out), .K(in_1), .Q(j_k_ff_1_q[0]), .Qn(j_k_ff_1_qn), .reset(in_2));  // open: preset
  J_K_Flip_Flop #(.Pre_Clr_Positions("LEGACY"), .NewFFLayout("false")) j_k_ff_2 (
    .J(in_1), .clk(j_k_ff_1_qn), .K(in_1), .Q(j_k_ff_1_q[1]), .Qn(j_k_ff_2_qn), .reset(in_2));  // open: preset
  // Probe on j_k_ff_1_q
  // Probe on j_k_ff_1_q
  J_K_Flip_Flop #(.Pre_Clr_Positions("LEGACY"), .NewFFLayout("false")) j_k_ff_3 (
    .J(in_1), .clk(j_k_ff_2_qn), .K(in_1), .Q(j_k_ff_1_q[2]), .Qn(j_k_ff_3_qn), .reset(in_2));  // open: preset
  J_K_Flip_Flop #(.Pre_Clr_Positions("LEGACY"), .NewFFLayout("false")) j_k_ff_4 (
    .J(in_1), .clk(j_k_ff_3_qn), .K(in_1), .Q(j_k_ff_1_q[3]), .Qn(j_k_ff_4_qn), .reset(in_2));  // open: preset
  J_K_Flip_Flop #(.Pre_Clr_Positions("LEGACY"), .NewFFLayout("false")) j_k_ff_5 (
    .J(in_1), .clk(j_k_ff_4_qn), .K(in_1), .Q(j_k_ff_1_q[4]), .reset(in_2));  // open: Qn, preset
endmodule

module G1303 (
  input  X,
  input  Clr
);

  wire and_1_out, Clk_out, j_k_ff_1_q, j_k_ff_2_q, j_k_ff_3_q, or_1_out;
  wire [3:0] j_k_ff_1_qn;

  Clock Clk (.out(Clk_out));
  or or_1 (or_1_out, Clr, and_1_out);
  and and_1 (and_1_out, j_k_ff_1_q, j_k_ff_1_qn[1], j_k_ff_3_q, j_k_ff_1_qn[3]);
  J_K_Flip_Flop #(.Pre_Clr_Positions("LEGACY"), .NewFFLayout("false")) j_k_ff_1 (
    .J(X), .clk(Clk_out), .K(X), .Q(j_k_ff_1_q), .Qn(j_k_ff_1_qn[0]), .preset(or_1_out));  // open: reset
  // Probe on j_k_ff_1_qn
  // Probe on j_k_ff_1_qn
  J_K_Flip_Flop #(.Pre_Clr_Positions("LEGACY"), .NewFFLayout("false")) j_k_ff_2 (
    .J(X), .clk(j_k_ff_1_q), .K(X), .Q(j_k_ff_2_q), .Qn(j_k_ff_1_qn[1]), .preset(or_1_out));  // open: reset
  J_K_Flip_Flop #(.Pre_Clr_Positions("LEGACY"), .NewFFLayout("false")) j_k_ff_3 (
    .J(X), .clk(j_k_ff_2_q), .K(X), .Q(j_k_ff_3_q), .Qn(j_k_ff_1_qn[2]), .preset(or_1_out));  // open: reset
  J_K_Flip_Flop #(.Pre_Clr_Positions("LEGACY"), .NewFFLayout("false")) j_k_ff_4 (
    .J(X), .clk(j_k_ff_3_q), .K(X), .Qn(j_k_ff_1_qn[3]), .preset(or_1_out));  // open: Q, reset
endmodule

module G1304 (
  input  in_1,
  input  in_2
);

  wire and_1_out, clock_1_out, j_k_ff_1_q, j_k_ff_2_qn, j_k_ff_3_qn, j_k_ff_4_qn, j_k_ff_5_qn, or_1_out;
  wire [3:0] j_k_ff_2_q;

  Clock clock_1 (.out(clock_1_out));
  and and_1 (and_1_out, j_k_ff_2_qn, j_k_ff_3_qn, j_k_ff_4_qn, j_k_ff_5_qn);
  J_K_Flip_Flop #(.Pre_Clr_Positions("LEGACY"), .NewFFLayout("false")) j_k_ff_1 (
    .J(and_1_out), .clk(clock_1_out), .K(and_1_out), .Q(j_k_ff_1_q), .reset(or_1_out));  // open: Qn, preset
  J_K_Flip_Flop #(.Pre_Clr_Positions("LEGACY"), .NewFFLayout("false")) j_k_ff_2 (
    .J(in_1), .clk(clock_1_out), .K(in_1), .Q(j_k_ff_2_q[0]), .Qn(j_k_ff_2_qn), .preset(or_1_out));  // open: reset
  or or_1 (or_1_out, in_2, j_k_ff_1_q);
  J_K_Flip_Flop #(.Pre_Clr_Positions("LEGACY"), .NewFFLayout("false")) j_k_ff_3 (
    .J(in_1), .clk(j_k_ff_2_q[0]), .K(in_1), .Q(j_k_ff_2_q[1]), .Qn(j_k_ff_3_qn), .reset(or_1_out));  // open: preset
  // Probe on j_k_ff_2_q
  J_K_Flip_Flop #(.Pre_Clr_Positions("LEGACY"), .NewFFLayout("false")) j_k_ff_4 (
    .J(in_1), .clk(j_k_ff_2_q[1]), .K(in_1), .Q(j_k_ff_2_q[2]), .Qn(j_k_ff_4_qn), .reset(or_1_out));  // open: preset
  J_K_Flip_Flop #(.Pre_Clr_Positions("LEGACY"), .NewFFLayout("false")) j_k_ff_5 (
    .J(in_1), .clk(j_k_ff_2_q[2]), .K(in_1), .Q(j_k_ff_2_q[3]), .Qn(j_k_ff_5_qn), .preset(or_1_out));  // open: reset
endmodule

module G1305 (
  input  in_1,
  input  in_2
);

  wire and_1_out, and_2_out, clock_1_out, t_ff_1_qn, t_ff_2_qn;
  wire [2:0] t_ff_1_q;

  Clock clock_1 (.out(clock_1_out));
  T_Flip_Flop #(.Pre_Clr_Positions("LEGACY"), .NewFFLayout("false")) t_ff_1 (
    .clk(clock_1_out), .T(in_1), .Q(t_ff_1_q[0]), .Qn(t_ff_1_qn), .reset(in_2));  // open: preset
  and and_1 (and_1_out, t_ff_1_qn, in_1);
  // Probe on t_ff_1_q
  // Probe on t_ff_1_q
  T_Flip_Flop #(.Pre_Clr_Positions("LEGACY"), .NewFFLayout("false")) t_ff_2 (
    .clk(clock_1_out), .T(and_1_out), .Q(t_ff_1_q[1]), .Qn(t_ff_2_qn), .reset(in_2));  // open: preset
  and and_2 (and_2_out, t_ff_2_qn, and_1_out);
  T_Flip_Flop #(.Pre_Clr_Positions("LEGACY"), .NewFFLayout("false")) t_ff_3 (
    .clk(clock_1_out), .T(and_2_out), .Q(t_ff_1_q[2]), .reset(in_2));  // open: Qn, preset
endmodule

module G1306 (
  input  in_1,
  input  in_2
);

  wire clock_1_out, or_1_out;
  wire [4:0] j_k_ff_5_q;

  Clock clock_1 (.out(clock_1_out));
  or or_1 (or_1_out, j_k_ff_5_q[0], in_1);
  J_K_Flip_Flop #(.Pre_Clr_Positions("LEGACY"), .NewFFLayout("false")) j_k_ff_1 (
    .J(or_1_out), .clk(clock_1_out), .K(j_k_ff_5_q[4]), .Q(j_k_ff_5_q[4]), .reset(in_2));  // open: Qn, preset
  // Probe on j_k_ff_5_q
  J_K_Flip_Flop #(.Pre_Clr_Positions("LEGACY"), .NewFFLayout("false")) j_k_ff_2 (
    .J(j_k_ff_5_q[4]), .clk(clock_1_out), .K(j_k_ff_5_q[3]), .Q(j_k_ff_5_q[3]), .reset(in_2));  // open: Qn, preset
  J_K_Flip_Flop #(.Pre_Clr_Positions("LEGACY"), .NewFFLayout("false")) j_k_ff_3 (
    .J(j_k_ff_5_q[3]), .clk(clock_1_out), .K(j_k_ff_5_q[2]), .Q(j_k_ff_5_q[2]), .reset(in_2));  // open: Qn, preset
  J_K_Flip_Flop #(.Pre_Clr_Positions("LEGACY"), .NewFFLayout("false")) j_k_ff_4 (
    .J(j_k_ff_5_q[2]), .clk(clock_1_out), .K(j_k_ff_5_q[1]), .Q(j_k_ff_5_q[1]), .reset(in_2));  // open: Qn, preset
  J_K_Flip_Flop #(.Pre_Clr_Positions("LEGACY"), .NewFFLayout("false")) j_k_ff_5 (
    .J(j_k_ff_5_q[1]), .clk(clock_1_out), .K(j_k_ff_5_q[0]), .Q(j_k_ff_5_q[0]), .reset(in_2));  // open: Qn, preset
endmodule

module G1307 (
  input  in_1,
  input  in_2
);

  wire clock_1_out, dflip_4_out_6, or_1_out;
  wire [3:0] not_1_out;

  Clock clock_1 (.out(clock_1_out));
  or or_1 (or_1_out, dflip_4_out_6, in_1);
  DFlip dflip_1 (.out_5(not_1_out[3]), .in_1(clock_1_out), .in_2(or_1_out), .in_4(in_2));  // open: out_6, in_3
  DFlip dflip_2 (.out_5(not_1_out[2]), .in_1(clock_1_out), .in_2(not_1_out[3]), .in_4(in_2));  // open: out_6, in_3
  // Probe on not_1_out
  DFlip dflip_3 (.out_5(not_1_out[1]), .in_1(clock_1_out), .in_2(not_1_out[2]), .in_4(in_2));  // open: out_6, in_3
  not not_1 (not_1_out[0], dflip_4_out_6);
  DFlip dflip_4 (.out_6(dflip_4_out_6), .in_1(clock_1_out), .in_2(not_1_out[1]), .in_4(in_2));  // open: out_5, in_3
endmodule

module DFlip (
  input  in_1,
  input  in_2,
  input  in_3,
  input  in_4,
  output out_5,
  output out_6
);

  wire nand_1_out;

  nand nand_1 (nand_1_out, in_2, out_5);
  J_K_Flip_Flop #(.Pre_Clr_Positions("LEGACY"), .NewFFLayout("false")) j_k_ff_1 (
    .J(in_2), .clk(in_1), .K(nand_1_out), .Q(out_5), .Qn(out_6), .preset(in_3), .reset(in_4));
endmodule
