// Logisim project Guia_13.circ as structural Verilog: 9 circuits, main circuit 01.
module _01 (
  input  x,
  input  clr,
  output [4:0] out_3
);

  wire clock_1_out;

  Clock clock_1 (.out(clock_1_out));
  J_K_Flip_Flop #(.Pre_Clr_Positions("LEGACY"), .enable("true"), .NewFFLayout("false")) j_k_ff_1 (
    .J(x), .clk(clock_1_out), .K(x), .Q(out_3[0]), .reset(clr));  // open: Qn, preset, en
  J_K_Flip_Flop #(.Pre_Clr_Positions("LEGACY"), .enable("true"), .NewFFLayout("false")) j_k_ff_2 (
    .J(x), .clk(out_3[0]), .K(x), .Q(out_3[1]), .reset(clr));  // open: Qn, preset, en
  // Probe on out_3
  J_K_Flip_Flop #(.Pre_Clr_Positions("LEGACY"), .enable("true"), .NewFFLayout("false")) j_k_ff_3 (
    .J(x), .clk(out_3[1]), .K(x), .Q(out_3[2]), .reset(clr));  // open: Qn, preset, en
  J_K_Flip_Flop #(.Pre_Clr_Positions("LEGACY"), .enable("true"), .NewFFLayout("false")) j_k_ff_4 (
    .J(x), .clk(out_3[2]), .K(x), .Q(out_3[3]), .reset(clr));  // open: Qn, preset, en
  J_K_Flip_Flop #(.Pre_Clr_Positions("LEGACY"), .enable("true"), .NewFFLayout("false")) j_k_ff_5 (
    .J(x), .clk(out_3[3]), .K(x), .Q(out_3[4]), .reset(clr));  // open: Qn, preset, en
endmodule

module _02 (
  input  x,
  input  clr,
  output [4:0] out_3
);

  wire clock_1_out, j_k_ff_1_qn, j_k_ff_2_qn, j_k_ff_3_qn, j_k_ff_4_qn;

  Clock clock_1 (.out(clock_1_out));
  J_K_Flip_Flop #(.Pre_Clr_Positions("LEGACY"), .enable("true"), .NewFFLayout("false")) j_k_ff_1 (
    .J(x), .clk(clock_1_out), .K(x), .Q(out_3[0]), .Qn(j_k_ff_1_qn), .reset(clr));  // open: preset, en
  J_K_Flip_Flop #(.Pre_Clr_Positions("LEGACY"), .enable("true"), .NewFFLayout("false")) j_k_ff_2 (
    .J(x), .clk(j_k_ff_1_qn), .K(x), .Q(out_3[1]), .Qn(j_k_ff_2_qn), .reset(clr));  // open: preset, en
  // Probe on out_3
  J_K_Flip_Flop #(.Pre_Clr_Positions("LEGACY"), .enable("true"), .NewFFLayout("false")) j_k_ff_3 (
    .J(x), .clk(j_k_ff_2_qn), .K(x), .Q(out_3[2]), .Qn(j_k_ff_3_qn), .reset(clr));  // open: preset, en
  J_K_Flip_Flop #(.Pre_Clr_Positions("LEGACY"), .enable("true"), .NewFFLayout("false")) j_k_ff_4 (
    .J(x), .clk(j_k_ff_3_qn), .K(x), .Q(out_3[3]), .Qn(j_k_ff_4_qn), .reset(clr));  // open: preset, en
  J_K_Flip_Flop #(.Pre_Clr_Positions("LEGACY"), .enable("true"), .NewFFLayout("false")) j_k_ff_5 (
    .J(x), .clk(j_k_ff_4_qn), .K(x), .Q(out_3[4]), .reset(clr));  // open: Qn, preset, en
endmodule

module _03 (
  input  x,
  input  clr,
  output [3:0] out_3
);

  wire and_1_out, clock_1_out, j_k_ff_1_qn, j_k_ff_2_qn, j_k_ff_3_qn, not_1_out, not_2_out, or_1_out;

  Clock clock_1 (.out(clock_1_out));
  or or_1 (or_1_out, clr, and_1_out);
  and and_1 (and_1_out, not_1_out, out_3[1], not_2_out, out_3[3]);
  J_K_Flip_Flop #(.Pre_Clr_Positions("LEGACY"), .enable("true"), .NewFFLayout("false")) j_k_ff_1 (
    .J(x), .clk(clock_1_out), .K(x), .Q(out_3[0]), .Qn(j_k_ff_1_qn), .reset(or_1_out));  // open: preset, en
  not not_1 (not_1_out, out_3[0]);
  not not_2 (not_2_out, out_3[2]);
  J_K_Flip_Flop #(.Pre_Clr_Positions("LEGACY"), .enable("true"), .NewFFLayout("false")) j_k_ff_2 (
    .J(x), .clk(j_k_ff_1_qn), .K(x), .Q(out_3[1]), .Qn(j_k_ff_2_qn), .reset(or_1_out));  // open: preset, en
  // Probe on out_3
  J_K_Flip_Flop #(.Pre_Clr_Positions("LEGACY"), .enable("true"), .NewFFLayout("false")) j_k_ff_3 (
    .J(x), .clk(j_k_ff_2_qn), .K(x), .Q(out_3[2]), .Qn(j_k_ff_3_qn), .reset(or_1_out));  // open: preset, en
  J_K_Flip_Flop #(.Pre_Clr_Positions("LEGACY"), .enable("true"), .NewFFLayout("false")) j_k_ff_4 (
    .J(x), .clk(j_k_ff_3_qn), .K(x), .Q(out_3[3]), .reset(or_1_out));  // open: Qn, preset, en
endmodule

module _04 (
  input  x,
  input  clr,
  output [3:0] out_3
);

  wire and_1_out, clock_1_out, j_k_ff_1_q, j_k_ff_2_qn, j_k_ff_3_qn, j_k_ff_4_qn, not_1_out, not_2_out,
       not_3_out, not_4_out, or_1_out;

  Clock clock_1 (.out(clock_1_out));
  or or_1 (or_1_out, clr, j_k_ff_1_q);
  and and_1 (and_1_out, not_1_out, not_2_out, not_3_out, not_4_out);
  J_K_Flip_Flop #(.Pre_Clr_Positions("LEGACY"), .enable("true"), .NewFFLayout("false")) j_k_ff_1 (
    .J(and_1_out), .clk(clock_1_out), .K(and_1_out), .Q(j_k_ff_1_q), .reset(or_1_out));  // open: Qn, preset, en
  J_K_Flip_Flop #(.Pre_Clr_Positions("LEGACY"), .enable("true"), .NewFFLayout("false")) j_k_ff_2 (
    .J(x), .clk(clock_1_out), .K(x), .Q(out_3[0]), .Qn(j_k_ff_2_qn), .preset(or_1_out));  // open: en, reset
  not not_1 (not_1_out, out_3[0]);
  not not_2 (not_2_out, out_3[1]);
  not not_3 (not_3_out, out_3[2]);
  not not_4 (not_4_out, out_3[3]);
  J_K_Flip_Flop #(.Pre_Clr_Positions("LEGACY"), .enable("true"), .NewFFLayout("false")) j_k_ff_3 (
    .J(x), .clk(out_3[0]), .K(x), .Q(out_3[1]), .Qn(j_k_ff_3_qn), .reset(or_1_out));  // open: preset, en
  // Probe on out_3
  J_K_Flip_Flop #(.Pre_Clr_Positions("LEGACY"), .enable("true"), .NewFFLayout("false")) j_k_ff_4 (
    .J(x), .clk(out_3[1]), .K(x), .Q(out_3[2]), .Qn(j_k_ff_4_qn), .reset(or_1_out));  // open: preset, en
  J_K_Flip_Flop #(.Pre_Clr_Positions("LEGACY"), .enable("true"), .NewFFLayout("false")) j_k_ff_5 (
    .J(x), .clk(out_3[2]), .K(x), .Q(out_3[3]), .preset(or_1_out));  // open: Qn, en, reset
endmodule

module _05 (
  input  x,
  output [2:0] out_2
);

  wire and_1_out, and_2_out, clock_1_out;

  Clock clock_1 (.out(clock_1_out));
  T_Flip_Flop #(.Pre_Clr_Positions("LEGACY"), .enable("true"), .NewFFLayout("false")) t_ff_1 (
    .clk(clock_1_out), .T(x), .Q(out_2[0]));  // open: Qn, preset, reset, en
  and and_1 (and_1_out, out_2[0], x);
  // Probe on out_2
  T_Flip_Flop #(.Pre_Clr_Positions("LEGACY"), .enable("true"), .NewFFLayout("false")) t_ff_2 (
    .clk(clock_1_out), .T(and_1_out), .Q(out_2[1]));  // open: Qn, preset, reset, en
  and and_2 (and_2_out, out_2[1], and_1_out);
  T_Flip_Flop #(.Pre_Clr_Positions("LEGACY"), .enable("true"), .NewFFLayout("false")) t_ff_3 (
    .clk(clock_1_out), .T(and_2_out), .Q(out_2[2]));  // open: Qn, preset, reset, en
endmodule

module teste (
  input  x,
  input  clr,
  output [4:0] out_3
);

  wire and_1_out, and_2_out, and_3_out, and_4_out, clock_1_out;

  Clock clock_1 (.out(clock_1_out));
  T_Flip_Flop #(.Pre_Clr_Positions("LEGACY"), .enable("true"), .NewFFLayout("false")) t_ff_1 (
    .clk(clock_1_out), .T(x), .Q(out_3[0]), .reset(clr));  // open: Qn, preset, en
  and and_1 (and_1_out, out_3[0], x);
  // Probe on out_3
  T_Flip_Flop #(.Pre_Clr_Positions("LEGACY"), .enable("true"), .NewFFLayout("false")) t_ff_2 (
    .clk(clock_1_out), .T(and_1_out), .Q(out_3[1]), .reset(clr));  // open: Qn, preset, en
  and and_2 (and_2_out, out_3[1], and_1_out);
  T_Flip_Flop #(.Pre_Clr_Positions("LEGACY"), .enable("true"), .NewFFLayout("false")) t_ff_3 (
    .clk(clock_1_out), .T(and_2_out), .Q(out_3[2]), .reset(clr));  // open: Qn, preset, en
  T_Flip_Flop #(.Pre_Clr_Positions("LEGACY"), .enable("true"), .NewFFLayout("false")) t_ff_4 (
    .clk(clock_1_out), .T(and_3_out), .Q(out_3[3]), .reset(clr));  // open: Qn, preset, en
  and and_3 (and_3_out, out_3[2], and_2_out);
  and and_4 (and_4_out, out_3[3], and_3_out);
  T_Flip_Flop #(.Pre_Clr_Positions("LEGACY"), .enable("true"), .NewFFLayout("false")) t_ff_5 (
    .clk(clock_1_out), .T(and_4_out), .Q(out_3[4]), .reset(clr));  // open: Qn, preset, en
endmodule

module _06 (
  input  \input ,
  input  clr,
  output out_3,
  output out_4,
  output out_5,
  output out_6,
  output out_7
);

  wire clock_1_out, or_1_out;

  Clock clock_1 (.out(clock_1_out));
  or or_1 (or_1_out, \input , out_7);
  J_K_Flip_Flop #(.Pre_Clr_Positions("LEGACY"), .NewFFLayout("false")) j_k_ff_1 (
    .J(or_1_out), .clk(clock_1_out), .K(out_3), .Q(out_3), .reset(clr));  // open: Qn, preset
  J_K_Flip_Flop #(.Pre_Clr_Positions("LEGACY"), .NewFFLayout("false")) j_k_ff_2 (
    .J(out_3), .clk(clock_1_out), .K(out_4), .Q(out_4), .reset(clr));  // open: Qn, preset
  J_K_Flip_Flop #(.Pre_Clr_Positions("LEGACY"), .NewFFLayout("false")) j_k_ff_3 (
    .J(out_4), .clk(clock_1_out), .K(out_5), .Q(out_5), .reset(clr));  // open: Qn, preset
  J_K_Flip_Flop #(.Pre_Clr_Positions("LEGACY"), .NewFFLayout("false")) j_k_ff_4 (
    .J(out_5), .clk(clock_1_out), .K(out_6), .Q(out_6), .reset(clr));  // open: Qn, preset
  J_K_Flip_Flop #(.Pre_Clr_Positions("LEGACY"), .NewFFLayout("false")) j_k_ff_5 (
    .J(out_6), .clk(clock_1_out), .K(out_7), .Q(out_7), .reset(clr));  // open: Qn, preset
endmodule

module d____com_jk (
  input  in_1,
  input  clk,
  input  in_3,
  input  in_4,
  output out_5,
  output out_6
);

  wire nand_1_out;

  nand nand_1 (nand_1_out, in_1, out_5);
  J_K_Flip_Flop #(.Pre_Clr_Positions("LEGACY"), .NewFFLayout("false")) j_k_ff_1 (
    .J(in_1), .clk(clk), .K(nand_1_out), .Q(out_5), .Qn(out_6), .preset(in_3), .reset(in_4));
endmodule

module _07 (
  input  \input ,
  input  clr,
  output out_3,
  output out_4,
  output out_5,
  output out_6,
  output out_7
);

  wire clock_1_out, d_com_jk_5_out_6, or_1_out;

  Clock clock_1 (.out(clock_1_out));
  or or_1 (or_1_out, \input , d_com_jk_5_out_6);
  d____com_jk d_com_jk_1 (.in_1(or_1_out), .clk(clock_1_out), .out_5(out_3), .in_4(clr));  // open: out_6, in_3
  d____com_jk d_com_jk_2 (.in_1(out_3), .clk(clock_1_out), .out_5(out_4), .in_4(clr));  // open: out_6, in_3
  d____com_jk d_com_jk_3 (.in_1(out_4), .clk(clock_1_out), .out_5(out_5), .in_4(clr));  // open: out_6, in_3
  d____com_jk d_com_jk_4 (.in_1(out_5), .clk(clock_1_out), .out_5(out_6), .in_4(clr));  // open: out_6, in_3
  d____com_jk d_com_jk_5 (
    .in_1(out_6), .clk(clock_1_out), .out_5(out_7), .out_6(d_com_jk_5_out_6), .in_4(clr));  // open: in_3
endmodule
