// Logisim project Questao_1401.circ as structural Verilog: 1 circuit, main circuit main
module main (
  input  in_1,
  input  in_2,
  input  in_3,
  input  in_4,
  input  in_5,
  input  in_6,
  input  in_7,
  input  in_8,
  input  in_9,
  input  in_10
);

  wire and_1_out, and_2_out, and_3_out, and_4_out, and_5_out, and_6_out, d_ff_1_q, d_ff_2_q, d_ff_3_q,
       d_ff_4_q, d_ff_5_q, d_ff_6_q;

  and and_1 (and_1_out, in_4, in_5);
  and and_2 (and_2_out, in_4, in_6);
  and and_3 (and_3_out, in_4, in_7);
  and and_4 (and_4_out, in_4, in_8);
  and and_5 (and_5_out, in_4, in_9);
  and and_6 (and_6_out, in_4, in_10);
  D_Flip_Flop #(.Pre_Clr_Positions("LEGACY"), .enable("true")) d_ff_1 (
    .clk(in_1), .D(d_ff_2_q), .Q(d_ff_1_q), .preset(and_1_out), .reset(in_2));  // open: Qn, en
  D_Flip_Flop #(.Pre_Clr_Positions("LEGACY"), .enable("true")) d_ff_2 (
    .clk(in_1), .D(d_ff_3_q), .Q(d_ff_2_q), .preset(and_2_out), .reset(in_2));  // open: Qn, en
  D_Flip_Flop #(.Pre_Clr_Positions("LEGACY"), .enable("true")) d_ff_3 (
    .clk(in_1), .D(d_ff_4_q), .Q(d_ff_3_q), .preset(and_3_out), .reset(in_2));  // open: Qn, en
  D_Flip_Flop #(.Pre_Clr_Positions("LEGACY"), .enable("true")) d_ff_4 (
    .clk(in_1), .D(d_ff_5_q), .Q(d_ff_4_q), .preset(and_4_out), .reset(in_2));  // open: Qn, en
  D_Flip_Flop #(.Pre_Clr_Positions("LEGACY"), .enable("true")) d_ff_5 (
    .clk(in_1), .D(d_ff_6_q), .Q(d_ff_5_q), .preset(and_5_out), .reset(in_2));  // open: Qn, en
  D_Flip_Flop #(.Pre_Clr_Positions("LEGACY"), .enable("true")) d_ff_6 (
    .clk(in_1), .D(in_3), .Q(d_ff_6_q), .preset(and_6_out), .reset(in_2));  // open: Qn, en
  // Probe on d_ff_1_q
  // Probe on d_ff_2_q
  // Probe on d_ff_3_q
  // Probe on d_ff_4_q
  // Probe on d_ff_5_q
  // Probe on d_ff_6_q
endmodule
