// Logisim project Questao_1402.circ as structural Verilog: 1 circuit, main circuit main
module main (
  input  in_1,
  input  in_2,
  input  in_3,
  input  in_4,
  input  in_5
);

  wire and_1_out, d_ff_1_q, d_ff_2_q, d_ff_3_q, d_ff_4_q, d_ff_5_q, d_ff_6_q;

  buf and_1 (and_1_out, in_4);  // AND_Gate
  // Probe on d_ff_1_q
  D_Flip_Flop #(.Pre_Clr_Positions("LEGACY"), .enable("true")) d_ff_1 (
    .clk(in_1), .D(d_ff_2_q), .Q(d_ff_1_q), .preset(and_1_out), .reset(in_2));  // open: Qn, en
  // Probe on d_ff_2_q
  D_Flip_Flop #(.Pre_Clr_Positions("LEGACY"), .enable("true")) d_ff_2 (
    .clk(in_1), .D(d_ff_3_q), .Q(d_ff_2_q), .reset(in_2));  // open: Qn, preset, en
  // Probe on d_ff_3_q
  D_Flip_Flop #(.Pre_Clr_Positions("LEGACY"), .enable("true")) d_ff_3 (
    .clk(in_1), .D(d_ff_4_q), .Q(d_ff_3_q), .reset(in_2));  // open: Qn, preset, en
  // Probe on d_ff_4_q
  D_Flip_Flop #(.Pre_Clr_Positions("LEGACY"), .enable("true")) d_ff_4 (
    .clk(in_1), .D(d_ff_5_q), .Q(d_ff_4_q), .reset(in_2));  // open: Qn, preset, en
  // Probe on d_ff_5_q
  D_Flip_Flop #(.Pre_Clr_Positions("LEGACY"), .enable("true")) d_ff_5 (
    .clk(in_1), .D(d_ff_6_q), .Q(d_ff_5_q), .reset(in_2));  // open: Qn, preset, en
  // Probe on d_ff_6_q
  D_Flip_Flop #(.Pre_Clr_Positions("LEGACY"), .enable("true")) d_ff_6 (
    .clk(in_1), .D(in_3), .Q(d_ff_6_q), .preset(in_4), .reset(in_2));  // open: Qn, en
endmodule
