// Logisim project Questao_1405.circ as structural Verilog: 1 circuit, main circuit main
module main (
  input  in_1,
  input  in_2
);

  wire clock_1_out, d_ff_1_q, d_ff_2_q, d_ff_3_q, d_ff_4_q, d_ff_5_q, d_ff_6_q, or_1_out;

  Clock clock_1 (.out(clock_1_out));
  or or_1 (or_1_out, d_ff_2_q, in_1, d_ff_6_q);
  D_Flip_Flop #(.Pre_Clr_Positions("LEGACY"), .enable("true")) d_ff_1 (
    .clk(clock_1_out), .D(or_1_out), .Q(d_ff_1_q), .reset(in_2));  // open: Qn, preset, en
  D_Flip_Flop #(.Pre_Clr_Positions("LEGACY"), .enable("true")) d_ff_2 (
    .clk(clock_1_out), .D(d_ff_3_q), .Q(d_ff_2_q), .reset(in_2));  // open: Qn, preset, en
  D_Flip_Flop #(.Pre_Clr_Positions("LEGACY"), .enable("true")) d_ff_3 (
    .clk(clock_1_out), .D(d_ff_4_q), .Q(d_ff_3_q), .reset(in_2));  // open: Qn, preset, en
  D_Flip_Flop #(.Pre_Clr_Positions("LEGACY"), .enable("true")) d_ff_4 (
    .clk(clock_1_out), .D(d_ff_5_q), .Q(d_ff_4_q), .reset(in_2));  // open: Qn, preset, en
  D_Flip_Flop #(.Pre_Clr_Positions("LEGACY"), .enable("true")) d_ff_5 (
    .clk(clock_1_out), .D(d_ff_6_q), .Q(d_ff_5_q), .reset(in_2));  // open: Qn, preset, en
  D_Flip_Flop #(.Pre_Clr_Positions("LEGACY"), .enable("true")) d_ff_6 (
    .clk(clock_1_out), .D(d_ff_6_q), .Q(d_ff_6_q), .reset(in_2));  // open: Qn, preset, en
  // Probe on d_ff_4_q
  // Probe on d_ff_5_q
  // Probe on d_ff_6_q
  // Probe on d_ff_6_q
  // Probe on d_ff_2_q
  // Probe on d_ff_1_q
  // Probe on d_ff_3_q
endmodule
