// Logisim project g1402.circ as structural Verilog: 1 circuit, main circuit main
module main (
  input  CLK,
  input  CLR,
  input  Data,
  input  LOAD,
  input  in_5
);

  wire and_1_out, d_ff_1_q, d_ff_2_q, d_ff_3_q, d_ff_4_q, d_ff_5_q, d_ff_6_q, undriven;

  // Probe on d_ff_1_q
  and and_1 (and_1_out, LOAD, in_5);
  D_Flip_Flop #(.Pre_Clr_Positions("LEGACY"), .enable("true")) d_ff_1 (
    .clk(CLK), .D(d_ff_2_q), .Q(d_ff_1_q), .preset(and_1_out), .reset(CLR));  // open: Qn, en
  // Probe on d_ff_2_q
  D_Flip_Flop #(.Pre_Clr_Positions("LEGACY"), .enable("true")) d_ff_2 (
    .clk(CLK), .D(d_ff_3_q), .Q(d_ff_2_q), .preset(undriven), .reset(CLR));  // open: Qn, en
  // Probe on d_ff_3_q
  D_Flip_Flop #(.Pre_Clr_Positions("LEGACY"), .enable("true")) d_ff_3 (
    .clk(CLK), .D(d_ff_4_q), .Q(d_ff_3_q), .reset(CLR));  // open: Qn, preset, en
  // Probe on d_ff_4_q
  D_Flip_Flop #(.Pre_Clr_Positions("LEGACY"), .enable("true")) d_ff_4 (
    .clk(CLK), .D(d_ff_5_q), .Q(d_ff_4_q), .reset(CLR));  // open: Qn, preset, en
  // Probe on d_ff_5_q
  D_Flip_Flop #(.Pre_Clr_Positions("LEGACY"), .enable("true")) d_ff_5 (
    .clk(CLK), .D(d_ff_6_q), .Q(d_ff_5_q), .reset(CLR));  // open: Qn, preset, en
  // Probe on d_ff_6_q
  D_Flip_Flop #(.Pre_Clr_Positions("LEGACY"), .enable("true")) d_ff_6 (
    .clk(CLK), .D(Data), .Q(d_ff_6_q), .preset(LOAD), .reset(CLR));  // open: Qn, en
endmodule
