// Logisim project Guia13.circ as structural Verilog: 5 circuits, main circuit questao01
module questao01 (
  input  pulse,
  input  in_2
);

  wire clock_out, j_k_ff_1_qn, j_k_ff_2_qn, j_k_ff_3_qn, j_k_ff_4_qn, j_k_ff_5_qn;

  Clock clock (.out(clock_out));
  // Probe on j_k_ff_1_qn
  J_K_Flip_Flop j_k_ff_1 (
    .J(in_2), .clk(j_k_ff_2_qn), .K(in_2), .Qn(j_k_ff_1_qn), .reset(clock_out));  // open: Q, preset
  // Probe on j_k_ff_2_qn
  J_K_Flip_Flop j_k_ff_2 (
    .J(in_2), .clk(j_k_ff_3_qn), .K(in_2), .Qn(j_k_ff_2_qn), .reset(clock_out));  // open: Q, preset
  // Probe on j_k_ff_3_qn
  J_K_Flip_Flop j_k_ff_3 (
    .J(in_2), .clk(j_k_ff_4_qn), .K(in_2), .Qn(j_k_ff_3_qn), .reset(clock_out));  // open: Q, preset
  // Probe on j_k_ff_4_qn
  J_K_Flip_Flop j_k_ff_4 (
    .J(in_2), .clk(j_k_ff_5_qn), .K(in_2), .Qn(j_k_ff_4_qn), .reset(clock_out));  // open: Q, preset
  J_K_Flip_Flop j_k_ff_5 (.J(in_2), .clk(pulse), .K(in_2), .Qn(j_k_ff_5_qn), .reset(clock_out));  // open: Q, preset
  // Probe on j_k_ff_5_qn
endmodule

module questao02 (
  input  pulse,
  input  in_2
);

  wire clock_1_out, j_k_ff_1_qn, j_k_ff_2_q, j_k_ff_2_qn, j_k_ff_3_q, j_k_ff_3_qn, j_k_ff_4_q, j_k_ff_4_qn,
       j_k_ff_5_q, j_k_ff_5_qn;

  Clock clock_1 (.out(clock_1_out));
  // Probe on j_k_ff_1_qn
  J_K_Flip_Flop j_k_ff_1 (
    .J(in_2), .clk(j_k_ff_2_q), .K(in_2), .Qn(j_k_ff_1_qn), .reset(clock_1_out));  // open: Q, preset
  // Probe on j_k_ff_2_qn
  J_K_Flip_Flop j_k_ff_2 (
    .J(in_2), .clk(j_k_ff_3_q), .K(in_2), .Q(j_k_ff_2_q), .Qn(j_k_ff_2_qn), .reset(clock_1_out));  // open: preset
  // Probe on j_k_ff_3_qn
  J_K_Flip_Flop j_k_ff_3 (
    .J(in_2), .clk(j_k_ff_4_q), .K(in_2), .Q(j_k_ff_3_q), .Qn(j_k_ff_3_qn), .reset(clock_1_out));  // open: preset
  // Probe on j_k_ff_4_qn
  J_K_Flip_Flop j_k_ff_4 (
    .J(in_2), .clk(j_k_ff_5_q), .K(in_2), .Q(j_k_ff_4_q), .Qn(j_k_ff_4_qn), .reset(clock_1_out));  // open: preset
  J_K_Flip_Flop j_k_ff_5 (
    .J(in_2), .clk(pulse), .K(in_2), .Q(j_k_ff_5_q), .Qn(j_k_ff_5_qn), .reset(clock_1_out));  // open: preset
  // Probe on j_k_ff_5_qn
endmodule

module questao03 (
  input  in_1,
  input  pulse
);

  wire and_1_out, clock_1_out, j_k_ff_1_q, j_k_ff_1_qn, j_k_ff_2_q, j_k_ff_2_qn, j_k_ff_3_q, j_k_ff_3_qn,
       j_k_ff_4_q, nand_1_out, not_1_out, not_2_out;

  Clock clock_1 (.out(clock_1_out));
  J_K_Flip_Flop j_k_ff_1 (
    .J(in_1), .clk(pulse), .K(in_1), .Q(j_k_ff_1_q), .Qn(j_k_ff_1_qn), .reset(and_1_out));  // open: preset
  and and_1 (and_1_out, clock_1_out, nand_1_out);
  not not_1 (not_1_out, j_k_ff_1_q);
  nand nand_1 (nand_1_out, not_1_out, j_k_ff_2_q, not_2_out, j_k_ff_4_q);
  not not_2 (not_2_out, j_k_ff_3_q);
  // Probe on j_k_ff_4_q
  // Probe on j_k_ff_3_q
  J_K_Flip_Flop j_k_ff_2 (
    .J(in_1), .clk(j_k_ff_1_qn), .K(in_1), .Q(j_k_ff_2_q), .Qn(j_k_ff_2_qn), .reset(and_1_out));  // open: preset
  // Probe on j_k_ff_2_q
  J_K_Flip_Flop j_k_ff_3 (
    .J(in_1), .clk(j_k_ff_2_qn), .K(in_1), .Q(j_k_ff_3_q), .Qn(j_k_ff_3_qn), .reset(and_1_out));  // open: preset
  // Probe on j_k_ff_1_q
  J_K_Flip_Flop j_k_ff_4 (
    .J(in_1), .clk(j_k_ff_3_qn), .K(in_1), .Q(j_k_ff_4_q), .reset(and_1_out));  // open: Qn, preset
endmodule

module questao04 (
  input  in_1,
  input  pulse
);

  wire and_1_out, j_k_ff_1_q, j_k_ff_1_qn, j_k_ff_2_q, j_k_ff_2_qn, j_k_ff_3_q, j_k_ff_3_qn, j_k_ff_4_q,
       j_k_ff_4_qn, not_1_out, not_2_out, not_3_out, or_1_out;

  not not_1 (not_1_out, in_1);
  and and_1 (and_1_out, not_2_out, j_k_ff_2_qn, not_3_out, j_k_ff_4_qn);
  // Probe on j_k_ff_4_q
  J_K_Flip_Flop j_k_ff_1 (
    .J(in_1), .clk(pulse), .K(in_1), .Q(j_k_ff_1_q), .Qn(j_k_ff_1_qn), .reset(or_1_out));  // open: preset
  or or_1 (or_1_out, not_1_out, and_1_out);
  not not_2 (not_2_out, j_k_ff_1_qn);
  not not_3 (not_3_out, j_k_ff_3_qn);
  // Probe on j_k_ff_3_q
  J_K_Flip_Flop j_k_ff_2 (
    .J(in_1), .clk(j_k_ff_1_q), .K(in_1), .Q(j_k_ff_2_q), .Qn(j_k_ff_2_qn), .reset(or_1_out));  // open: preset
  // Probe on j_k_ff_2_q
  J_K_Flip_Flop j_k_ff_3 (
    .J(in_1), .clk(j_k_ff_2_q), .K(in_1), .Q(j_k_ff_3_q), .Qn(j_k_ff_3_qn), .reset(or_1_out));  // open: preset
  // Probe on j_k_ff_1_q
  J_K_Flip_Flop j_k_ff_4 (
    .J(in_1), .clk(j_k_ff_3_q), .K(in_1), .Q(j_k_ff_4_q), .Qn(j_k_ff_4_qn), .reset(or_1_out));  // open: preset
endmodule

module questao05 (
  input  pulse
);

  wire and_1_out, clock_1_out, not_1_out, or_1_out, t_ff_1_q, t_ff_2_q, t_ff_2_qn, t_ff_3_q, t_ff_3_qn;

  Clock clock_1 (.out(clock_1_out));
  or or_1 (or_1_out, clock_1_out, and_1_out);
  and and_1 (and_1_out, t_ff_1_q, not_1_out, t_ff_3_q);
  // Probe on t_ff_1_q
  T_Flip_Flop t_ff_1 (.clk(t_ff_2_qn), .T(t_ff_2_qn), .Q(t_ff_1_q), .reset(or_1_out));  // open: Qn, preset
  not not_1 (not_1_out, t_ff_2_q);
  // Probe on t_ff_2_q
  T_Flip_Flop t_ff_2 (.clk(t_ff_3_qn), .T(t_ff_3_qn), .Q(t_ff_2_q), .Qn(t_ff_2_qn), .reset(or_1_out));  // open: preset
  // Probe on t_ff_3_q
  T_Flip_Flop t_ff_3 (.clk(pulse), .T(pulse), .Q(t_ff_3_q), .Qn(t_ff_3_qn), .reset(or_1_out));  // open: preset
endmodule
