// Logisim project Guia_14.circ as structural Verilog: 8 circuits, main circuit 01.
module _01 (
  input  \input ,
  input  load,
  output [5:0] out_3
);

  wire clock_1_out;

  Clock clock_1 (.out(clock_1_out));
  D_Flip_Flop #(.Pre_Clr_Positions("LEGACY"), .NewFFLayout("false")) d_ff_1 (
    .clk(clock_1_out), .D(out_3[4]), .Q(out_3[5]), .reset(load));  // open: Qn, preset
  D_Flip_Flop #(.Pre_Clr_Positions("LEGACY"), .NewFFLayout("false")) d_ff_2 (
    .clk(clock_1_out), .D(out_3[3]), .Q(out_3[4]), .reset(load));  // open: Qn, preset
  D_Flip_Flop #(.Pre_Clr_Positions("LEGACY"), .NewFFLayout("false")) d_ff_3 (
    .clk(clock_1_out), .D(out_3[2]), .Q(out_3[3]), .reset(load));  // open: Qn, preset
  D_Flip_Flop #(.Pre_Clr_Positions("LEGACY"), .NewFFLayout("false")) d_ff_4 (
    .clk(clock_1_out), .D(out_3[1]), .Q(out_3[2]), .reset(load));  // open: Qn, preset
  D_Flip_Flop #(.Pre_Clr_Positions("LEGACY"), .NewFFLayout("false")) d_ff_5 (
    .clk(clock_1_out), .D(out_3[0]), .Q(out_3[1]), .reset(load));  // open: Qn, preset
  D_Flip_Flop #(.Pre_Clr_Positions("LEGACY"), .NewFFLayout("false")) d_ff_6 (
    .clk(clock_1_out), .D(\input ), .Q(out_3[0]), .preset(load));  // open: Qn, reset
endmodule

module _02 (
  input  \input ,
  input  load,
  output [5:0] out_3
);

  wire clock_1_out;

  Clock clock_1 (.out(clock_1_out));
  D_Flip_Flop #(.Pre_Clr_Positions("LEGACY"), .NewFFLayout("false")) d_ff_1 (
    .clk(clock_1_out), .D(out_3[4]), .Q(out_3[5]), .preset(load));  // open: Qn, reset
  D_Flip_Flop #(.Pre_Clr_Positions("LEGACY"), .NewFFLayout("false")) d_ff_2 (
    .clk(clock_1_out), .D(out_3[3]), .Q(out_3[4]), .preset(load));  // open: Qn, reset
  D_Flip_Flop #(.Pre_Clr_Positions("LEGACY"), .NewFFLayout("false")) d_ff_3 (
    .clk(clock_1_out), .D(out_3[2]), .Q(out_3[3]), .preset(load));  // open: Qn, reset
  D_Flip_Flop #(.Pre_Clr_Positions("LEGACY"), .NewFFLayout("false")) d_ff_4 (
    .clk(clock_1_out), .D(out_3[1]), .Q(out_3[2]), .preset(load));  // open: Qn, reset
  D_Flip_Flop #(.Pre_Clr_Positions("LEGACY"), .NewFFLayout("false")) d_ff_5 (
    .clk(clock_1_out), .D(out_3[0]), .Q(out_3[1]), .preset(load));  // open: Qn, reset
  D_Flip_Flop #(.Pre_Clr_Positions("LEGACY"), .NewFFLayout("false")) d_ff_6 (
    .clk(clock_1_out), .D(\input ), .Q(out_3[0]), .preset(load));  // open: Qn, reset
endmodule

module _03 (
  input  in,
  input  load,
  output [5:0] out_3
);

  wire clock_1_out, or_1_out;

  Clock clock_1 (.out(clock_1_out));
  D_Flip_Flop #(.Pre_Clr_Positions("LEGACY"), .NewFFLayout("false")) d_ff_1 (
    .clk(clock_1_out), .D(or_1_out), .Q(out_3[5]), .preset(load));  // open: Qn, reset
  or or_1 (or_1_out, in, out_3[0]);
  D_Flip_Flop #(.Pre_Clr_Positions("LEGACY"), .NewFFLayout("false")) d_ff_2 (
    .clk(clock_1_out), .D(out_3[5]), .Q(out_3[4]), .reset(load));  // open: Qn, preset
  D_Flip_Flop #(.Pre_Clr_Positions("LEGACY"), .NewFFLayout("false")) d_ff_3 (
    .clk(clock_1_out), .D(out_3[4]), .Q(out_3[3]), .reset(load));  // open: Qn, preset
  D_Flip_Flop #(.Pre_Clr_Positions("LEGACY"), .NewFFLayout("false")) d_ff_4 (
    .clk(clock_1_out), .D(out_3[3]), .Q(out_3[2]), .reset(load));  // open: Qn, preset
  D_Flip_Flop #(.Pre_Clr_Positions("LEGACY"), .NewFFLayout("false")) d_ff_5 (
    .clk(clock_1_out), .D(out_3[2]), .Q(out_3[1]), .reset(load));  // open: Qn, preset
  D_Flip_Flop #(.Pre_Clr_Positions("LEGACY"), .NewFFLayout("false")) d_ff_6 (
    .clk(clock_1_out), .D(out_3[1]), .Q(out_3[0]), .reset(load));  // open: Qn, preset
endmodule

module _04 (
  input  \input ,
  input  load,
  output [5:0] out_3
);

  wire clock_1_out, d_ff_1_qn, or_1_out;

  Clock clock_1 (.out(clock_1_out));
  D_Flip_Flop #(.Pre_Clr_Positions("LEGACY"), .NewFFLayout("false")) d_ff_1 (
    .clk(clock_1_out), .D(out_3[4]), .Q(out_3[5]), .Qn(d_ff_1_qn), .reset(load));  // open: preset
  D_Flip_Flop #(.Pre_Clr_Positions("LEGACY"), .NewFFLayout("false")) d_ff_2 (
    .clk(clock_1_out), .D(out_3[3]), .Q(out_3[4]), .reset(load));  // open: Qn, preset
  D_Flip_Flop #(.Pre_Clr_Positions("LEGACY"), .NewFFLayout("false")) d_ff_3 (
    .clk(clock_1_out), .D(out_3[2]), .Q(out_3[3]), .reset(load));  // open: Qn, preset
  D_Flip_Flop #(.Pre_Clr_Positions("LEGACY"), .NewFFLayout("false")) d_ff_4 (
    .clk(clock_1_out), .D(out_3[1]), .Q(out_3[2]), .reset(load));  // open: Qn, preset
  D_Flip_Flop #(.Pre_Clr_Positions("LEGACY"), .NewFFLayout("false")) d_ff_5 (
    .clk(clock_1_out), .D(out_3[0]), .Q(out_3[1]), .reset(load));  // open: Qn, preset
  or or_1 (or_1_out, d_ff_1_qn, \input );
  D_Flip_Flop #(.Pre_Clr_Positions("LEGACY"), .NewFFLayout("false")) d_ff_6 (
    .clk(clock_1_out), .D(or_1_out), .Q(out_3[0]), .preset(load));  // open: Qn, reset
endmodule

module conversor (
  input  clk,
  input  clr,
  input  load,
  input  in_4,
  input  in_5,
  input  in_6,
  input  in_7,
  input  in_8,
  input  in_9,
  output out_10
);

  wire and_1_out, and_2_out, and_3_out, and_4_out, and_5_out, and_6_out, and_7_out, and_8_out, and_9_out,
       and_10_out, and_11_out, and_12_out, d_ff_1_q, d_ff_2_q, d_ff_3_q, d_ff_4_q, d_ff_5_q, not_1_out,
       not_2_out, not_3_out, not_4_out, not_5_out, not_6_out, or_1_out, or_2_out, or_3_out, or_4_out,
       or_5_out, or_6_out;

  D_Flip_Flop #(.Pre_Clr_Positions("LEGACY"), .NewFFLayout("false")) d_ff_1 (
    .clk(clk), .D(1'b0), .Q(d_ff_1_q), .preset(and_3_out), .reset(or_1_out));  // open: Qn
  or or_1 (or_1_out, clr, and_1_out);
  and and_1 (and_1_out, load, not_1_out);
  not not_1 (not_1_out, and_3_out);
  and and_2 (and_2_out, load, in_5);
  and and_3 (and_3_out, load, in_4);
  D_Flip_Flop #(.Pre_Clr_Positions("LEGACY"), .NewFFLayout("false")) d_ff_2 (
    .clk(clk), .D(d_ff_1_q), .Q(d_ff_2_q), .preset(and_2_out), .reset(or_2_out));  // open: Qn
  or or_2 (or_2_out, clr, and_4_out);
  or or_3 (or_3_out, clr, and_6_out);
  and and_4 (and_4_out, load, not_2_out);
  not not_2 (not_2_out, and_2_out);
  and and_5 (and_5_out, load, in_6);
  D_Flip_Flop #(.Pre_Clr_Positions("LEGACY"), .NewFFLayout("false")) d_ff_3 (
    .clk(clk), .D(d_ff_4_q), .Q(d_ff_3_q), .preset(and_8_out), .reset(or_4_out));  // open: Qn
  D_Flip_Flop #(.Pre_Clr_Positions("LEGACY"), .NewFFLayout("false")) d_ff_4 (
    .clk(clk), .D(d_ff_2_q), .Q(d_ff_4_q), .preset(and_5_out), .reset(or_3_out));  // open: Qn
  or or_4 (or_4_out, clr, and_7_out);
  and and_6 (and_6_out, load, not_3_out);
  and and_7 (and_7_out, load, not_5_out);
  not not_3 (not_3_out, and_5_out);
  and and_8 (and_8_out, load, in_7);
  D_Flip_Flop #(.Pre_Clr_Positions("LEGACY"), .NewFFLayout("false")) d_ff_5 (
    .clk(clk), .D(d_ff_3_q), .Q(d_ff_5_q), .preset(and_10_out), .reset(or_5_out));  // open: Qn
  or or_5 (or_5_out, clr, and_9_out);
  and and_9 (and_9_out, load, not_4_out);
  not not_4 (not_4_out, and_10_out);
  not not_5 (not_5_out, and_8_out);
  and and_10 (and_10_out, load, in_8);
  D_Flip_Flop #(.Pre_Clr_Positions("LEGACY"), .NewFFLayout("false")) d_ff_6 (
    .clk(clk), .D(d_ff_5_q), .Q(out_10), .preset(and_12_out), .reset(or_6_out));  // open: Qn
  or or_6 (or_6_out, clr, and_11_out);
  and and_11 (and_11_out, load, not_6_out);
  not not_6 (not_6_out, and_12_out);
  and and_12 (and_12_out, load, in_9);
endmodule

module _05 (
  input  load,
  input  [5:0] in,
  input  clr,
  output out_4
);

  wire clock_1_out;

  Clock clock_1 (.out(clock_1_out));
  conversor conversor_1 (
    .in_4(in[0]), .in_5(in[1]), .in_6(in[2]), .in_7(in[3]), .in_8(in[4]), .in_9(in[5]), .load(load),
    .clr(clr), .out_10(out_4), .clk(clock_1_out));
endmodule

module _06 (
  input  \input ,
  input  load,
  output [4:0] out_3
);

  wire clock_1_out, xor_1_out;

  Clock clock_1 (.out(clock_1_out));
  D_Flip_Flop #(.Pre_Clr_Positions("LEGACY"), .NewFFLayout("false")) d_ff_1 (
    .clk(clock_1_out), .D(out_3[3]), .Q(out_3[4]), .preset(load));  // open: Qn, reset
  D_Flip_Flop #(.Pre_Clr_Positions("LEGACY"), .NewFFLayout("false")) d_ff_2 (
    .clk(clock_1_out), .D(out_3[2]), .Q(out_3[3]), .preset(load));  // open: Qn, reset
  D_Flip_Flop #(.Pre_Clr_Positions("LEGACY"), .NewFFLayout("false")) d_ff_3 (
    .clk(clock_1_out), .D(out_3[1]), .Q(out_3[2]), .preset(load));  // open: Qn, reset
  D_Flip_Flop #(.Pre_Clr_Positions("LEGACY"), .NewFFLayout("false")) d_ff_4 (
    .clk(clock_1_out), .D(out_3[0]), .Q(out_3[1]), .preset(load));  // open: Qn, reset
  xor xor_1 (xor_1_out, out_3[4], \input );
  D_Flip_Flop #(.Pre_Clr_Positions("LEGACY"), .NewFFLayout("false")) d_ff_5 (
    .clk(clock_1_out), .D(xor_1_out), .Q(out_3[0]), .preset(load));  // open: Qn, reset
endmodule

module _07 (
  input  \input ,
  input  load,
  output [4:0] out_3
);

  wire clock_1_out, d_ff_5_qn, or_1_out;

  Clock clock_1 (.out(clock_1_out));
  or or_1 (or_1_out, \input , d_ff_5_qn);
  D_Flip_Flop #(.Pre_Clr_Positions("LEGACY"), .NewFFLayout("false")) d_ff_1 (
    .clk(clock_1_out), .D(or_1_out), .Q(out_3[4]), .preset(load));  // open: Qn, reset
  D_Flip_Flop #(.Pre_Clr_Positions("LEGACY"), .NewFFLayout("false")) d_ff_2 (
    .clk(clock_1_out), .D(out_3[4]), .Q(out_3[3]), .preset(load));  // open: Qn, reset
  D_Flip_Flop #(.Pre_Clr_Positions("LEGACY"), .NewFFLayout("false")) d_ff_3 (
    .clk(clock_1_out), .D(out_3[3]), .Q(out_3[2]), .preset(load));  // open: Qn, reset
  D_Flip_Flop #(.Pre_Clr_Positions("LEGACY"), .NewFFLayout("false")) d_ff_4 (
    .clk(clock_1_out), .D(out_3[2]), .Q(out_3[1]), .preset(load));  // open: Qn, reset
  D_Flip_Flop #(.Pre_Clr_Positions("LEGACY"), .NewFFLayout("false")) d_ff_5 (
    .clk(clock_1_out), .D(out_3[1]), .Q(out_3[0]), .Qn(d_ff_5_qn), .preset(load));  // open: reset
endmodule
