// Logisim project PA_04.circ as structural Verilog: 1 circuit, main circuit main
module main (
  input  A,
  input  A_2,
  input  B,
  input  B_2,
  input  C,
  input  C_2,
  input  A_3,
  input  A_4,
  input  B_3,
  input  B_4,
  input  C_3,
  input  C_4,
  output out_13,
  output out_14,
  output out_15,
  output out_16
);

  wire and_1_out, and_2_out, and_3_out, and_4_out, and_5_out, and_6_out, and_7_out, and_8_out, not_1_out,
       not_2_out, not_3_out, not_4_out, not_5_out, not_6_out, not_7_out;

  not not_1 (not_1_out, A_4);
  not not_2 (not_2_out, B_4);
  not not_3 (not_3_out, C_2);
  and and_1 (and_1_out, not_1_out, not_2_out, C_4);
  and and_2 (and_2_out, A_4, B_4, C_4);
  and and_3 (and_3_out, B_2, C_2);
  and and_4 (and_4_out, A_2, not_3_out);
  or or_1 (out_16, and_1_out, and_2_out);
  or or_2 (out_14, and_3_out, and_4_out);
  not not_4 (not_4_out, A_3);
  not not_5 (not_5_out, B_3);
  not not_6 (not_6_out, A);
  not not_7 (not_7_out, B);
  and and_5 (and_5_out, not_4_out, not_5_out, C_3);
  and and_6 (and_6_out, A_3, B_3, C_3);
  and and_7 (and_7_out, not_6_out, B, C);
  and and_8 (and_8_out, A, not_7_out, C);
  or or_3 (out_15, and_5_out, and_6_out);
  or or_4 (out_13, and_7_out, and_8_out);

  // Notes on the sheet:
  //   A - Da
  //   C - SbRb
  //   Preparação_02       806937 - FELIPE PEREIRA DA SILVA
  //   B - Ta
  //   D - Tb
endmodule
