// Logisim project Guia_0503.circ as structural Verilog: 1 circuit, main circuit main
module main (
  output s
);

  wire b_p1, nor_1_out, nor_2_out, undriven;

  // Switch a: pin names not known
  nor nor_1 (nor_1_out, undriven, undriven);
  // Switch b: pin names not known; wires that end beside it: b_p1
  nor nor_2 (nor_2_out, b_p1, nor_1_out);
  nor nor_3 (s, nor_2_out, nor_2_out);
endmodule
