// Logisim project Mealy_1101.circ as structural Verilog: 1 circuit, main circuit main
// e1
module main (
  input  e1,
  input  e0,
  input  x,
  output e1_2,
  output e0_2,
  output y
);

  wire and_1_out, and_2_out, button_1_out, clock_1_out, not_1_out, not_2_out, not_3_out, or_1_out;

  not not_1 (not_1_out, x);
  not not_2 (not_2_out, e0);
  not not_3 (not_3_out, x);
  and and_1 (and_1_out, e0, not_1_out);
  and and_2 (and_2_out, e1, not_2_out, x);
  and and_3 (y, e1, e0, not_3_out);
  Button button_1 (.out(button_1_out));
  or or_1 (or_1_out, and_1_out, and_2_out);
  Clock clock_1 (.out(clock_1_out));
  D_Flip_Flop #(.enable("true")) E1___1 (
    .clk(clock_1_out), .D(or_1_out), .Q(e1_2), .reset(button_1_out));  // open: Qn, preset, en
  D_Flip_Flop #(.enable("true")) E1___0 (
    .clk(clock_1_out), .D(x), .Q(e0_2), .reset(button_1_out));  // open: Qn, preset, en
endmodule
