// Logisim project Moore_1100 (2).circ as structural Verilog: 1 circuit, main circuit main
module main (
  input  e2,
  input  e2_2,
  input  e1,
  input  e1_2,
  input  e0,
  input  x,
  input  e0_2,
  output y
);

  wire and_1_out, and_2_out, and_3_out, and_4_out, button_1_out, clock_1_out, not_1_out, not_2_out,
       not_3_out, not_4_out, or_1_out;

  not not_1 (not_1_out, x);
  not not_2 (not_2_out, e1);
  not not_3 (not_3_out, x);
  not not_4 (not_4_out, e0);
  and and_1 (and_1_out, e1, e0, not_1_out);
  and and_2 (and_2_out, not_2_out, e0, not_3_out);
  and and_3 (and_3_out, e1, not_4_out, x);
  and and_4 (and_4_out, e2_2, x);
  or or_1 (or_1_out, and_2_out, and_3_out, and_4_out);
  Button button_1 (.out(button_1_out));
  Clock clock_1 (.out(clock_1_out));
  D_Flip_Flop d_ff_1 (.clk(clock_1_out), .D(and_1_out), .Q(e2), .reset(button_1_out));  // open: Qn, preset
  D_Flip_Flop d_ff_2 (.clk(clock_1_out), .D(or_1_out), .Q(e1_2), .reset(button_1_out));  // open: Qn, preset
  D_Flip_Flop d_ff_3 (.clk(clock_1_out), .D(x), .Q(e0_2), .reset(button_1_out));  // open: Qn, preset

  assign y = e2_2;
endmodule
