// Logisim project Questao_02.circ as structural Verilog: 1 circuit, main circuit main
module main (
  input  in_1
);

  wire and_1_out, and_2_out, clock_1_out, j_k_ff_1_q, j_k_ff_1_qn, not_1_out, not_2_out;

  Clock clock_1 (.out(clock_1_out));
  and and_1 (and_1_out, in_1, not_1_out);
  not not_1 (not_1_out, j_k_ff_1_q);
  not not_2 (not_2_out, in_1);
  and and_2 (and_2_out, not_2_out, j_k_ff_1_q);
  J_K_Flip_Flop j_k_ff_1 (
    .J(and_1_out), .clk(clock_1_out), .K(and_2_out), .Q(j_k_ff_1_q), .Qn(j_k_ff_1_qn));  // open: preset, reset
  // Probe on j_k_ff_1_qn
endmodule
