// Logisim project Questao_03.circ as structural Verilog: 1 circuit, main circuit main
module main (
  input  in_1
);

  wire clock_1_out, j_k_ff_1_q, j_k_ff_1_qn, j_k_ff_2_q, j_k_ff_2_qn;

  Clock clock_1 (.out(clock_1_out));
  J_K_Flip_Flop j_k_ff_1 (
    .J(in_1), .clk(clock_1_out), .K(in_1), .Q(j_k_ff_1_q), .Qn(j_k_ff_1_qn));  // open: preset, reset
  J_K_Flip_Flop j_k_ff_2 (
    .J(in_1), .clk(clock_1_out), .K(in_1), .Q(j_k_ff_2_q), .Qn(j_k_ff_2_qn));  // open: preset, reset
  // Probe on j_k_ff_1_q
  // Probe on j_k_ff_1_qn
  // Probe on j_k_ff_2_q
  // Probe on j_k_ff_2_qn
endmodule
