// Logisim project Questao_04.circ as structural Verilog: 1 circuit, main circuit main
module main (
  input  in_1,
  input  in_2
);

  wire clock_1_out, t_ff_1_qn, t_ff_2_q, t_ff_2_qn, t_ff_3_q, t_ff_3_qn, t_ff_4_qn, t_ff_5_q, t_ff_5_qn;

  Clock clock_1 (.out(clock_1_out));
  T_Flip_Flop t_ff_1 (.clk(clock_1_out), .T(in_1), .Qn(t_ff_1_qn), .reset(in_2));  // open: Q, preset
  // Probe on t_ff_1_qn
  T_Flip_Flop t_ff_2 (.clk(t_ff_2_q), .T(in_1), .Q(t_ff_2_q), .Qn(t_ff_2_qn), .reset(in_2));  // open: preset
  // Probe on t_ff_2_qn
  T_Flip_Flop t_ff_3 (.clk(t_ff_3_q), .T(in_1), .Q(t_ff_3_q), .Qn(t_ff_3_qn), .reset(in_2));  // open: preset
  // Probe on t_ff_3_qn
  T_Flip_Flop t_ff_4 (.clk(t_ff_5_q), .T(in_1), .Qn(t_ff_4_qn), .reset(in_2));  // open: Q, preset
  // Probe on t_ff_4_qn
  T_Flip_Flop t_ff_5 (.clk(clock_1_out), .T(in_1), .Q(t_ff_5_q), .Qn(t_ff_5_qn), .reset(in_2));  // open: preset
  // Probe on t_ff_5_qn
endmodule
