// Logisim project Exercicio02_a.circ as structural Verilog: 1 circuit, main circuit main
module main (
  input  x,
  input  nx,
  input  y,
  output out_4
);

  wire not_1_out, not_2_out, or_1_out;

  not not_1 (not_1_out, nx);
  or or_1 (or_1_out, not_1_out, y);
  not not_2 (not_2_out, or_1_out);
  and and_1 (out_4, x, not_2_out);
endmodule
