// Logisim project Exercicio02_b.circ as structural Verilog: 1 circuit, main circuit main
module main (
  input  nx,
  input  y,
  output out_3
);

  wire AND_out, not_1_out, OR_out;

  not not_1 (not_1_out, nx);
  or OR (OR_out, not_1_out, y);
  and AND (AND_out, not_1_out, y);
  or OR_2 (out_3, OR_out, AND_out);

  // Notes on the sheet:
  //   ('x + y) + ('x . y)
endmodule
