// Logisim project Exercicio02_d.circ as structural Verilog: 1 circuit, main circuit main
module main (
  input  x,
  input  y,
  output out_3
);

  wire and_1_out, not_1_out, not_2_out, not_3_out, not_4_out, or_1_out;

  not not_1 (not_1_out, x);
  and and_1 (and_1_out, not_1_out, y);
  not not_2 (not_2_out, x);
  or or_1 (or_1_out, not_2_out, y);
  not not_3 (not_3_out, and_1_out);
  or or_2 (out_3, not_3_out, not_4_out);
  not not_4 (not_4_out, or_1_out);
endmodule
