// Logisim project Exercicio02_e.circ as structural Verilog: 1 circuit, main circuit main
module main (
  input  x,
  input  y,
  output out_3
);

  wire not_1_out, not_2_out, not_3_out, or_1_out, or_2_out;

  not not_1 (not_1_out, x);
  or or_1 (or_1_out, not_1_out, y);
  or or_2 (or_2_out, x, not_2_out);
  not not_2 (not_2_out, y);
  and and_1 (out_3, or_1_out, not_3_out);
  not not_3 (not_3_out, or_2_out);
endmodule
