// Logisim project Exercicio_3a.circ as structural Verilog: 1 circuit, main circuit main
module main (
  input  x,
  input  y,
  input  z,
  output m0,
  output m1,
  output m2,
  output m3,
  output m4,
  output m5,
  output m6,
  output m7
);

  wire and_1_out, and_2_out, and_3_out, and_4_out, and_5_out, and_6_out, and_7_out, and_8_out, not_1_out,
       not_2_out, not_3_out;

  not not_1 (not_1_out, x);
  not not_2 (not_2_out, y);
  not not_3 (not_3_out, z);
  and and_1 (and_1_out, x, y);
  and and_2 (and_2_out, not_1_out, not_2_out);
  and and_3 (and_3_out, x, not_2_out);
  and and_4 (and_4_out, x, y);
  and and_5 (and_5_out, not_1_out, y);
  and and_6 (and_6_out, x, not_2_out);
  and and_7 (and_7_out, x, y);
  and and_8 (and_8_out, x, y);
  and and_9 (m0, and_1_out, z);
  and and_10 (m1, and_2_out, z);
  and and_11 (m2, and_3_out, not_3_out);
  and and_12 (m3, and_4_out, not_3_out);
  buf and_13 (m4, and_5_out);  // AND_Gate
  buf and_14 (m5, and_6_out);  // AND_Gate
  and and_15 (m6, and_7_out, not_3_out);
  and and_16 (m7, and_8_out, z);
endmodule
