// Logisim project Exercicio03_c.circ as structural Verilog: 1 circuit, main circuit main
module main (
  input  x,
  input  y,
  input  w,
  input  z,
  output m0,
  output m1,
  output m2,
  output m3,
  output m4,
  output m5,
  output m6,
  output m7,
  output m8,
  output m9,
  output m10,
  output m11,
  output m12,
  output m13,
  output m14,
  output m15
);

  wire not_1_out, not_2_out, not_3_out, not_4_out, w_prime_z_out, w_z_out, w_z_prime_out, x_prime_y_out,
       x_prime_y_prime_out, x_y_out, x_y_prime_out;

  not not_1 (not_1_out, x);
  not not_2 (not_2_out, y);
  not not_3 (not_3_out, w);
  not not_4 (not_4_out, z);
  and x_y (x_y_out, x, y);
  and x_prime_y_prime (x_prime_y_prime_out, not_1_out, not_2_out);
  and x_y_prime (x_y_prime_out, x, not_2_out);
  and x_prime_y (x_prime_y_out, not_1_out, y);
  and w_z (w_z_out, w, z);
  and w_prime_z (w_prime_z_out, not_3_out, z);
  and w_z_prime (w_z_prime_out, w, not_4_out);
  and and_1 (m0, x_y_out, w_z_out);
  and and_2 (m1, x_prime_y_prime_out, w_prime_z_out);
  and and_3 (m2, x_prime_y_prime_out, w_z_prime_out);
  and and_4 (m3, x_prime_y_prime_out, w_z_out);
  and and_5 (m4, x_y_prime_out, w_z_out);
  and and_6 (m5, x_y_prime_out, w_z_prime_out);
  and and_7 (m6, x_prime_y_out, w_z_prime_out);
  and and_8 (m7, x_prime_y_out, w_z_out);
  and and_9 (m8, x_prime_y_out, w_z_out);
  and and_10 (m9, x_y_out, w_z_prime_out);
  and and_11 (m10, x_y_out, w_prime_z_out);
  and and_12 (m11, x_y_prime_out, w_z_out);
  and and_13 (m12, x_prime_y_out, w_z_out);
  and and_14 (m13, x_prime_y_prime_out, w_prime_z_out);
  and and_15 (m14, x_y_prime_out, w_prime_z_out);
  and and_16 (m15, x_y_out, w_z_out);
endmodule
