// Logisim project Exercicio03_e.circ as structural Verilog: 1 circuit, main circuit main
module main (
  input  x,
  input  y,
  input  w,
  input  z,
  output out_5
);

  wire m0_out, m1_out, m2_out, m3_out, m4_out, m5_out, m6_out, m7_out, m8_out, m9_out, m10_out, m11_out,
       not_1_out, not_2_out, not_3_out, not_4_out;

  not not_1 (not_1_out, x);
  not not_2 (not_2_out, y);
  not not_3 (not_3_out, w);
  not not_4 (not_4_out, z);
  and m0 (m0_out, not_1_out, not_2_out, not_3_out, not_4_out);
  and m1 (m1_out, x, y, w, not_4_out);
  and m2 (m2_out, not_1_out, not_2_out, w, not_4_out);
  and m3 (m3_out, x, y, w, not_4_out);
  and m4 (m4_out, x, y, w, not_4_out);
  and m5 (m5_out, not_1_out, y, not_3_out, z);
  and m6 (m6_out, x, y, w, z);
  and m7 (m7_out, not_1_out, y, w, z);
  and m8 (m8_out, x, not_2_out, not_3_out, not_4_out);
  and m9 (m9_out, not_1_out, y, not_3_out, z);
  and m10 (m10_out, x, y, not_3_out, not_4_out);
  and m11 (m11_out, x, not_2_out, w, z);
  or or_1 (out_5, m0_out, m1_out, m2_out, m3_out, m4_out, m5_out, m6_out, m7_out, m8_out, m9_out, m10_out, m11_out);
endmodule
