// Logisim project Exercicio04_a.circ as structural Verilog: 1 circuit, main circuit main
module main (
  input  x,
  input  y,
  input  z,
  output out_4
);

  wire M1_out, M2_out, M6_out, M7_out, not_1_out, not_2_out, not_3_out;

  not not_1 (not_1_out, x);
  not not_2 (not_2_out, y);
  not not_3 (not_3_out, z);
  or M1 (M1_out, x, y, not_3_out);
  or M2 (M2_out, x, not_2_out, z);
  or M6 (M6_out, not_1_out, not_2_out, z);
  or M7 (M7_out, not_1_out, not_2_out, not_3_out);
  and and_1 (out_4, M1_out, M2_out, M6_out, M7_out);
endmodule
