// Logisim project Exercicio04_b.circ as structural Verilog: 1 circuit, main circuit main
module main (
  input  x,
  input  y,
  input  z,
  output out_4
);

  wire M0_out, M3_out, M4_out, M7_out, not_1_out, not_2_out, not_3_out;

  not not_1 (not_1_out, x);
  not not_2 (not_2_out, y);
  not not_3 (not_3_out, z);
  or M0 (M0_out, x, y, z);
  or M3 (M3_out, x, not_2_out, not_3_out);
  or M4 (M4_out, not_1_out, y, z);
  or M7 (M7_out, not_1_out, not_2_out, not_3_out);
  and and_1 (out_4, M0_out, M3_out, M4_out, M7_out);
endmodule
