// Logisim project xercicio04_c.circ as structural Verilog: 1 circuit, main circuit main
module main (
  input  x,
  input  y,
  input  w,
  input  z,
  output out_5
);

  wire M0_out, M1_out, M2_out, M4_out, M6_out, M8_out, M11_out, M12_out, not_1_out, not_2_out, not_3_out,
       not_4_out;

  not not_1 (not_1_out, y);
  not not_2 (not_2_out, x);
  not not_3 (not_3_out, w);
  not not_4 (not_4_out, z);
  or M0 (M0_out, x, y, w, z);
  or M1 (M1_out, x, y, w, not_4_out);
  or M2 (M2_out, x, y, not_3_out, z);
  or M4 (M4_out, x, not_1_out, w, z);
  or M6 (M6_out, x, not_1_out, not_3_out, z);
  or M8 (M8_out, not_2_out, y, w, z);
  or M11 (M11_out, not_2_out, y, not_3_out, not_4_out);
  or M12 (M12_out, not_2_out, not_1_out, w, z);
  and and_1 (out_5, M0_out, M1_out, M2_out, M4_out, M6_out, M8_out, M11_out, M12_out);
endmodule
