// Logisim project Exercicio04_d.circ as structural Verilog: 1 circuit, main circuit main
module main (
  input  x,
  input  y,
  input  w,
  input  z,
  output out_5
);

  wire M1_out, M2_out, M4_out, M7_out, M8_out, M9_out, M15_out, not_1_out, not_2_out, not_3_out, not_4_out;

  not not_1 (not_1_out, y);
  not not_2 (not_2_out, x);
  not not_3 (not_3_out, w);
  not not_4 (not_4_out, z);
  or M1 (M1_out, x, y, w, not_4_out);
  or M2 (M2_out, x, y, not_3_out, z);
  or M4 (M4_out, x, not_1_out, w, z);
  or M7 (M7_out, x, not_1_out, not_3_out, not_4_out);
  or M8 (M8_out, not_2_out, y, w, z);
  or M9 (M9_out, not_2_out, y, w, not_4_out);
  or M15 (M15_out, not_2_out, not_1_out, not_3_out, not_4_out);
  and and_1 (out_5, M1_out, M2_out, M4_out, M7_out, M8_out, M9_out, M15_out);
endmodule
