// Logisim project Exercicio05_e.circ as structural Verilog: 1 circuit, main circuit main
module main (
  input  x,
  input  y,
  input  w,
  input  z,
  output out_5
);

  wire and_1_out, and_2_out, and_4_out, and_5_out, and_6_out, and_7_out, and_8_out, and_9_out, and_10_out,
       and_11_out, not_1_out, not_2_out, not_3_out, or_1_out, or_3_out, or_4_out, or_5_out;

  not not_1 (not_1_out, x);
  not not_2 (not_2_out, y);
  not not_3 (not_3_out, w);
  not not_4 (not_3_out, w);
  and and_1 (and_1_out, not_1_out, not_2_out, not_3_out, not_3_out);
  and and_2 (and_2_out, not_1_out, not_2_out, not_3_out, w);
  or or_1 (or_1_out, x, y, not_3_out, w);
  and and_3 (or_1_out, not_1_out, not_2_out, w, w);
  or or_2 (or_1_out, x, not_2_out, w, w);
  and and_4 (and_4_out, not_1_out, y, not_3_out, w);
  and and_5 (and_5_out, not_1_out, y, w, not_3_out);
  or or_3 (or_3_out, x, not_2_out, not_3_out, not_3_out);
  and and_6 (and_6_out, x, not_2_out, not_3_out, not_3_out);
  and and_7 (and_7_out, x, not_2_out, not_3_out, w);
  and and_8 (and_8_out, x, not_2_out, w, not_3_out);
  or or_4 (or_4_out, not_1_out, y, not_3_out, not_3_out);
  and and_9 (and_9_out, x, y, not_3_out, not_3_out);
  or or_5 (or_5_out, not_1_out, not_2_out, w, not_3_out);
  and and_10 (and_10_out, x, y, w, not_3_out);
  and and_11 (and_11_out, x, y, w, w);
  and and_12 (out_5, and_1_out, and_2_out, or_1_out, or_1_out, or_1_out, and_4_out, and_5_out, or_3_out, and_6_out, and_7_out, and_8_out, or_4_out, and_9_out, or_5_out, and_10_out, and_11_out);

  assign z = w;
endmodule
