// Logisim project Exericio01.circ as structural Verilog: 1 circuit, main circuit main
module main (
  input  a,
  input  b,
  output out_3
);

  wire nor_1_out, nor_2_out;

  not nor_1 (nor_1_out, a);  // NOR_Gate
  nor nor_2 (nor_2_out, nor_1_out, b);
  nor nor_3 (out_3, nor_2_out, b);
endmodule
