// Logisim project Exercicio02.circ as structural Verilog: 1 circuit, main circuit main
module main (
  input  a,
  input  nb,
  output out_3
);

  wire nand_1_out;

  not nand_1 (nand_1_out, nb);  // NAND_Gate
  nand nand_2 (out_3, a, nand_1_out);
endmodule
