// Logisim project Exercicio03.circ as structural Verilog: 1 circuit, main circuit main
module main (
  input  a,
  input  b,
  output out_3
);

  wire not_1_out;

  not not_1 (not_1_out, a);
  nor nor_1 (out_3, not_1_out, b);
endmodule
