// Logisim project Exercicio04.circ as structural Verilog: 1 circuit, main circuit main
module main (
  input  na,
  input  b,
  output out_3
);

  wire not_1_out;

  not not_1 (not_1_out, na);
  nand nand_1 (out_3, not_1_out, b);
endmodule
