// Logisim project Exercicio05.circ as structural Verilog: 1 circuit, main circuit main
module main (
  input  a,
  input  b,
  output out_3
);

  wire na_out, nb_out, nor_1_out, nor_2_out;

  not na (na_out, a);  // NOR_Gate
  not nb (nb_out, b);  // NOR_Gate
  nor nor_1 (nor_1_out, na_out, b);
  nor nor_2 (nor_2_out, a, nb_out);
  nor nor_3 (out_3, nor_1_out, nor_2_out);
endmodule
