// Logisim project Exercicio07.circ as structural Verilog: 1 circuit, main circuit main
module main (
  input  a,
  input  b,
  output out_3
);

  wire nor_1_out, nor_2_out, nor_3_out;

  not nor_1 (nor_1_out, a);  // NOR_Gate
  not nor_2 (nor_2_out, b);  // NOR_Gate
  nor nor_3 (nor_3_out, nor_1_out, nor_2_out);
  not nor_4 (out_3, nor_3_out);  // NOR_Gate
endmodule
