// Logisim project Exericicio08.circ as structural Verilog: 1 circuit, main circuit main
module main (
  input  in_1,
  input  in_2,
  output out_3
);

  wire nand_1_out, nand_2_out, nand_3_out;

  not nand_1 (nand_1_out, in_1);  // NAND_Gate
  not nand_2 (nand_2_out, in_2);  // NAND_Gate
  nand nand_3 (nand_3_out, nand_1_out, nand_2_out);
  not nand_4 (out_3, nand_3_out);  // NAND_Gate
endmodule
