// Logisim project Exercicio_1a.circ as structural Verilog: 1 circuit, main circuit main
module main (
  input  x,
  input  y,
  input  z,
  output out_4
);

  wire and_1_out, and_2_out, and_3_out, x_prime_out, y_prime_out, z_prime_out;

  not x_prime (x_prime_out, x);
  not y_prime (y_prime_out, x);
  not z_prime (z_prime_out, z);
  and and_1 (and_1_out, x_prime_out, y_prime_out, z);
  and and_2 (and_2_out, x, x, z_prime_out);
  and and_3 (and_3_out, x, x, z);
  or or_1 (out_4, and_1_out, and_2_out, and_3_out);

  assign y = x;
endmodule
