// Logisim project Exercicio_2e.circ as structural Verilog: 1 circuit, main circuit main
module main (
  input  x,
  input  y,
  input  z,
  output out_4
);

  wire and_1_out, and_2_out, and_3_out, and_4_out, not_1_out, not_2_out, not_3_out;

  not not_1 (not_1_out, x);
  not not_2 (not_2_out, y);
  not not_3 (not_3_out, z);
  and and_1 (and_1_out, not_1_out, not_2_out);
  and and_2 (and_2_out, y, not_3_out);
  and and_3 (and_3_out, y, z);
  and and_4 (and_4_out, x, y);
  or or_1 (out_4, and_1_out, and_2_out, and_3_out, and_4_out);
endmodule
