// Logisim project Exercicio2.circ as structural Verilog: 1 circuit, main circuit main
module main (
  input  in_1,
  input  in_2,
  input  in_3,
  input  in_4,
  output out_5,
  output out_6
);

  or or_1 (out_5, in_1, in_2, in_3, in_4);
  nor nor_1 (out_6, in_1, in_2, in_3, in_4);
endmodule
