// Logisim project Exercicio3.circ as structural Verilog: 1 circuit, main circuit main
module main (
  input  in_1,
  input  in_2,
  input  in_3,
  input  in_4,
  output out_5,
  output out_6
);

  wire and_1_out, nand_1_out, nor_1_out, or_1_out;

  and and_1 (and_1_out, in_1, in_2, in_3, in_4);
  nand nand_1 (nand_1_out, in_1, in_2, in_3, in_4);
  or or_1 (or_1_out, in_1, in_2, in_3, in_4);
  nor nor_1 (nor_1_out, in_1, in_2, in_3, in_4);
  or or_2 (out_5, and_1_out, nand_1_out);
  and and_2 (out_6, or_1_out, nor_1_out);
endmodule
