// Logisim project Exercicio5.circ as structural Verilog: 1 circuit, main circuit main
module main (
  input  in_1,
  input  in_2,
  input  in_3,
  input  in_4,
  output out_5
);

  wire and_1_out, nand_1_out, nor_1_out, not_1_out, not_2_out, not_3_out, not_4_out, or_1_out, or_2_out,
       xnor_1_out, xor_1_out;

  not not_1 (not_1_out, in_2);
  not not_2 (not_2_out, in_1);
  not not_3 (not_3_out, in_3);
  not not_4 (not_4_out, in_4);
  and and_1 (and_1_out, in_1, in_2, in_3, in_4);
  nand nand_1 (nand_1_out, in_1, in_2, in_3, in_4);
  or or_1 (or_1_out, in_1, in_2, in_3, in_4);
  or or_2 (or_2_out, in_1, in_2, in_3, in_4);
  nor nor_1 (nor_1_out, in_1, in_2, in_3, in_4);
  ExactlyOne xor_1 (.out(xor_1_out), .in0(in_1), .in1(in_2), .in2(in_3), .in3(in_4));
  NotExactlyOne xnor_1 (.out(xnor_1_out), .in0(in_1), .in1(in_2), .in2(in_3), .in3(in_4));
  or or_3 (out_5, and_1_out, nand_1_out, or_1_out, or_2_out, nor_1_out, xor_1_out, xnor_1_out);
endmodule
