// Logisim project Questao_e.circ as structural Verilog: 1 circuit, main circuit main
module main (
  input  a,
  input  b,
  input  c,
  input  d,
  output out_5
);

  wire nand_1_out, nand_2_out, nand_3_out, nand_4_out, nand_5_out, nand_6_out, nand_7_out, nand_8_out,
       nand_9_out, nand_10_out, nand_11_out, nand_12_out, not_1_out, not_2_out, not_3_out, not_4_out;

  not not_1 (not_1_out, a);
  not not_2 (not_2_out, b);
  not not_3 (not_3_out, c);
  not not_4 (not_4_out, d);
  nand nand_1 (nand_1_out, not_1_out, b, not_3_out, not_4_out);
  nand nand_2 (nand_2_out, a, not_2_out, not_3_out, not_4_out);
  nand nand_3 (nand_3_out, a, not_2_out, not_3_out, d);
  nand nand_4 (nand_4_out, a, b, not_3_out, not_4_out);
  nand nand_5 (nand_5_out, a, b, not_3_out, d);
  nand nand_6 (nand_6_out, a, b, c, not_4_out);
  not nand_7 (nand_7_out, nand_1_out);  // NAND_Gate
  not nand_8 (nand_8_out, nand_2_out);  // NAND_Gate
  not nand_9 (nand_9_out, nand_3_out);  // NAND_Gate
  not nand_10 (nand_10_out, nand_4_out);  // NAND_Gate
  not nand_11 (nand_11_out, nand_5_out);  // NAND_Gate
  not nand_12 (nand_12_out, nand_6_out);  // NAND_Gate
  or or_1 (out_5, nand_7_out, nand_8_out, nand_9_out, nand_10_out, nand_11_out, nand_12_out);

  // Notes on the sheet:
  //   4,8,9,C,D,E
endmodule
