// Logisim project Questao_f.circ as structural Verilog: 1 circuit, main circuit main
module main (
  input  a,
  input  b,
  input  c,
  input  d,
  output out_5
);

  wire nor_1_out, nor_2_out, nor_3_out, nor_4_out, nor_5_out, nor_6_out, nor_7_out, nor_8_out, nor_9_out,
       nor_10_out, nor_11_out, nor_12_out, nor_13_out, nor_14_out, nor_15_out, nor_16_out, nor_17_out,
       nor_18_out, nor_19_out, nor_20_out, not_1_out, not_2_out, not_3_out, not_4_out;

  not not_1 (not_1_out, a);
  not not_2 (not_2_out, c);
  not not_3 (not_3_out, b);
  not not_4 (not_4_out, d);
  nor nor_1 (nor_1_out, a, b, c, d);
  nor nor_2 (nor_2_out, a, b, c, not_4_out);
  nor nor_3 (nor_3_out, a, b, not_2_out, d);
  nor nor_4 (nor_4_out, a, b, not_2_out, not_4_out);
  nor nor_5 (nor_5_out, a, not_3_out, c, not_4_out);
  nor nor_6 (nor_6_out, a, not_3_out, not_2_out, d);
  nor nor_7 (nor_7_out, a, not_3_out, not_2_out, not_4_out);
  nor nor_8 (nor_8_out, not_1_out, b, not_2_out, d);
  nor nor_9 (nor_9_out, not_1_out, b, not_2_out, not_4_out);
  nor nor_10 (nor_10_out, not_1_out, not_3_out, not_2_out, not_4_out);
  not nor_11 (nor_11_out, nor_1_out);  // NOR_Gate
  not nor_12 (nor_12_out, nor_2_out);  // NOR_Gate
  not nor_13 (nor_13_out, nor_3_out);  // NOR_Gate
  not nor_14 (nor_14_out, nor_4_out);  // NOR_Gate
  not nor_15 (nor_15_out, nor_5_out);  // NOR_Gate
  not nor_16 (nor_16_out, nor_6_out);  // NOR_Gate
  not nor_17 (nor_17_out, nor_7_out);  // NOR_Gate
  not nor_18 (nor_18_out, nor_8_out);  // NOR_Gate
  not nor_19 (nor_19_out, nor_9_out);  // NOR_Gate
  not nor_20 (nor_20_out, nor_10_out);  // NOR_Gate
  and and_1 (out_5, nor_11_out, nor_12_out, nor_13_out, nor_14_out, nor_15_out, nor_16_out, nor_17_out, nor_18_out, nor_19_out, nor_20_out);

  // Notes on the sheet:
  //   0,1,2,3,5,6,7,A,B,F
endmodule
