// Logisim project Questao_a.circ as structural Verilog: 1 circuit, main circuit main
module main (
  input  in_1,
  input  in_2,
  output out_3
);

  wire not_1_out;

  not not_1 (not_1_out, in_1);
  Multiplexer #(.enable("false")) multiplexer_1 (.in0(in_1), .in1(not_1_out), .out(out_3), .sel(in_2));
endmodule
