// Logisim project Questao_b.circ as structural Verilog: 1 circuit, main circuit main
module main (
  input  c,
  input  a,
  input  in_3,
  output out_4
);

  wire multiplexer_1_out, not_1_out, not_2_out;

  not not_1 (not_1_out, a);
  not not_2 (not_2_out, c);
  Multiplexer #(.enable("false")) multiplexer_1 (.in0(a), .in1(not_1_out), .out(multiplexer_1_out), .sel(in_3));
  Multiplexer #(.enable("false")) multiplexer_2 (.in0(c), .in1(not_2_out), .out(out_4), .sel(multiplexer_1_out));
endmodule
