// Logisim project Questao_b.circ as structural Verilog: 1 circuit, main circuit main
module main (
  input  x,
  input  y,
  output out_3
);

  wire nand_1_out, nand_2_out, not_1_out, not_2_out;

  not not_1 (not_1_out, x);
  not not_2 (not_2_out, y);
  nand nand_1 (nand_1_out, not_1_out, y);
  nand nand_2 (nand_2_out, not_1_out, not_2_out);
  and and_1 (out_3, nand_1_out, nand_2_out);
endmodule
