// Logisim project Questao_03.circ as structural Verilog: 1 circuit, main circuit main
module main (
  input  in_1,
  input  in_2,
  input  in_3
);

  wire j_k_ff_1_qn, j_k_ff_2_q, j_k_ff_2_qn, j_k_ff_3_q, j_k_ff_3_qn;

  J_K_Flip_Flop j_k_ff_1 (.J(in_2), .clk(j_k_ff_2_q), .K(in_2), .Qn(j_k_ff_1_qn), .reset(in_3));  // open: Q, preset
  J_K_Flip_Flop j_k_ff_2 (
    .J(in_2), .clk(j_k_ff_3_q), .K(in_2), .Q(j_k_ff_2_q), .Qn(j_k_ff_2_qn), .reset(in_3));  // open: preset
  J_K_Flip_Flop j_k_ff_3 (
    .J(in_2), .clk(in_1), .K(in_2), .Q(j_k_ff_3_q), .Qn(j_k_ff_3_qn), .reset(in_3));  // open: preset
  // Probe on j_k_ff_1_qn
  // Probe on j_k_ff_2_qn
  // Probe on j_k_ff_3_qn
endmodule
