// Logisim project Questao_04.circ as structural Verilog: 1 circuit, main circuit main
module main (
  input  in_1,
  input  in_2,
  input  in_3
);

  wire d_ff_1_qn, d_ff_2_q, d_ff_2_qn, d_ff_3_q, d_ff_3_qn;

  D_Flip_Flop d_ff_1 (.clk(d_ff_2_q), .D(in_2), .Qn(d_ff_1_qn), .reset(in_3));  // open: Q, preset
  D_Flip_Flop d_ff_2 (.clk(d_ff_3_q), .D(in_2), .Q(d_ff_2_q), .Qn(d_ff_2_qn), .reset(in_3));  // open: preset
  D_Flip_Flop d_ff_3 (.clk(in_1), .D(in_2), .Q(d_ff_3_q), .Qn(d_ff_3_qn), .reset(in_3));  // open: preset
  // Probe on d_ff_1_qn
  // Probe on d_ff_2_qn
  // Probe on d_ff_3_qn
endmodule
