// Logisim project Questao_05.circ as structural Verilog: 1 circuit, main circuit main
module main (
  input  in_1
);

  wire and_1_out, clock_1_out, t_ff_1_q, t_ff_1_qn, t_ff_2_q, t_ff_2_qn, t_ff_3_q, t_ff_3_qn, t_ff_4_q;

  Clock clock_1 (.out(clock_1_out));
  buf and_1 (and_1_out, in_1);  // AND_Gate
  T_Flip_Flop t_ff_1 (.clk(clock_1_out), .T(1'b1), .Q(t_ff_1_q), .Qn(t_ff_1_qn), .reset(and_1_out));  // open: preset
  T_Flip_Flop t_ff_2 (.clk(t_ff_1_qn), .T(1'b1), .Q(t_ff_2_q), .Qn(t_ff_2_qn), .reset(and_1_out));  // open: preset
  T_Flip_Flop t_ff_3 (.clk(t_ff_2_qn), .T(1'b1), .Q(t_ff_3_q), .Qn(t_ff_3_qn), .reset(and_1_out));  // open: preset
  T_Flip_Flop t_ff_4 (.clk(t_ff_3_qn), .T(1'b1), .Q(t_ff_4_q), .reset(and_1_out));  // open: Qn, preset
  LED led_1 (.in(t_ff_1_q));
  LED led_2 (.in(t_ff_2_q));
  LED led_3 (.in(t_ff_3_q));
  LED led_4 (.in(t_ff_4_q));
endmodule
