// Logisim project Decodificador.circ as structural Verilog: 2 circuits, main circuit main
module main (
  input  in_1,
  input  in_2,
  input  in_3,
  input  in_4
);

  wire exercicio_1_a, exercicio_1_b, exercicio_1_c, exercicio_1_d, exercicio_1_e, exercicio_1_f,
       exercicio_1_g;

  Exercicio exercicio_1 (
    .e3(in_1), .e2(in_2), .e1(in_3), .e0(in_4), .a(exercicio_1_a), .b(exercicio_1_b), .c(exercicio_1_c),
    .d(exercicio_1_d), .e(exercicio_1_e), .f(exercicio_1_f), .g(exercicio_1_g));
  _7_Segment_Display u_7_segment_display_1 (
    .g(exercicio_1_g), .f(exercicio_1_f), .a(exercicio_1_a), .b(exercicio_1_b), .e(exercicio_1_e),
    .d(exercicio_1_d), .c(exercicio_1_c));  // open: dp
endmodule

module Exercicio (
  input  e3,
  input  e2,
  input  e1,
  input  e0,
  output a,
  output b,
  output c,
  output d,
  output e,
  output f,
  output g
);

  wire and_1_out, and_2_out, and_3_out, and_4_out, and_5_out, and_6_out, and_7_out, and_8_out, and_9_out,
       not_2_out, not_4_out, not_5_out, not_6_out, not_7_out, not_8_out, not_9_out, not_10_out, not_11_out,
       not_12_out, not_13_out, not_14_out, not_15_out, not_16_out, not_17_out, not_18_out, not_19_out;

  not not_1 (a, e0);
  not not_2 (not_2_out, e2);
  not not_3 (d, e0);
  not not_4 (not_4_out, e2);
  and and_1 (and_1_out, not_4_out, not_5_out, not_6_out);
  not not_5 (not_5_out, e1);
  not not_6 (not_6_out, e0);
  and and_2 (and_2_out, e2, e1, not_7_out);
  not not_7 (not_7_out, e0);
  and and_3 (and_3_out, e3, not_8_out);
  not not_8 (not_8_out, e0);
  not not_9 (not_9_out, e1);
  not not_10 (not_10_out, e0);
  not not_11 (not_11_out, e3);
  not not_12 (not_12_out, e2);
  not not_13 (not_13_out, e0);
  not not_14 (not_14_out, e0);
  not not_15 (not_15_out, e3);
  not not_16 (not_16_out, e2);
  not not_17 (not_17_out, e3);
  not not_18 (not_18_out, e1);
  not not_19 (not_19_out, e0);
  or or_1 (b, not_2_out, e0, e1, e3);
  or or_2 (e, and_1_out, and_2_out, and_3_out);
  and and_4 (and_4_out, not_9_out, not_10_out);
  and and_5 (and_5_out, not_11_out, not_12_out, e1, e0);
  and and_6 (and_6_out, e2, not_13_out);
  and and_7 (and_7_out, e3, not_14_out);
  and and_8 (and_8_out, not_15_out, not_16_out, e1);
  or or_3 (g, and_8_out, and_9_out);
  and and_9 (and_9_out, not_17_out, e2, not_18_out, not_19_out);
  or or_4 (f, and_4_out, and_5_out, and_6_out, and_7_out);

  assign c = 1'b1;
endmodule
