// Logisim project Somador de 2 numeros(3bits).circ as structural Verilog: 1 circuit, main circuit main
module main (
  input  a0,
  input  a1,
  input  a2,
  input  b0,
  input  b1,
  input  b2,
  output P1,
  output P2,
  output P3,
  output P4,
  output P5
);

  wire a0b0_out, a0b1_out, a0b2_out, a1b0_out, a1b1_out, a1b2_out, a2b0_out, a2b1_out, a2b2_out,
       adder_1_cout, adder_2_cout, adder_3_cout, adder_5_out;

  and a0b0 (a0b0_out, b0, a0);
  and a0b1 (a0b1_out, b1, a0);
  and a1b0 (a1b0_out, b0, a1);
  and a0b2 (a0b2_out, b2, a0);
  Adder #(.width(1)) adder_1 (.a(a1b0_out), .b(a0b1_out), .out(P1), .cout(adder_1_cout));  // open: cin
  and a1b1 (a1b1_out, b1, a1);
  and a1b2 (a1b2_out, b2, a1);
  and a2b0 (a2b0_out, b0, a2);
  Adder #(.width(1)) adder_2 (.a(a2b1_out), .b(a1b2_out), .out(P3), .cin(adder_3_cout), .cout(adder_2_cout));
  and a2b2 (a2b2_out, b2, a2);
  and a2b1 (a2b1_out, b1, a2);
  Adder #(.width(1)) adder_3 (.a(adder_5_out), .b(a0b2_out), .out(P2), .cout(adder_3_cout));  // open: cin
  Adder #(.width(1)) adder_4 (.a(a2b2_out), .b(a0b0_out), .out(P4), .cin(adder_2_cout), .cout(P5));
  Adder #(.width(1)) adder_5 (.a(a1b1_out), .b(a2b0_out), .out(adder_5_out), .cin(adder_1_cout));  // open: cout
endmodule
